// Logisim project test.circ as structural Verilog: 1 circuit, main circuit main
module main (
  input  [1:0] in_1
);

  wire [3:0] _01;
  wire [7:4] rom_1_data;

  // AND_Gate _1_and is placed but not wired
  // Probe on nothing
  Multiplexer #(.select(2), .enable("false")) multiplexer_1 ();  // open: in0, in1, in2, in3, out, sel
  Adder adder_1 ();  // open: a, b, out, cin, cout
  D_Flip_Flop d_ff_1 ();  // open: clk, D, Q, Qn, preset, en, reset
  Register register_1 ();  // open: D, en, Q, clk, clr
  ROM #(.addrWidth(2)) rom_1 (.addr(in_1), .data({rom_1_data, _01}));  // open: sel
  // Probe on _01
  // Probe on _01
  // Probe on rom_1_data

  // Notes on the sheet:
  //   contents of rom_1 (hex, n*v repeats v):
  //   1 2 3 4
endmodule
