// Logisim project 2次幂mod5的余数_mealy机.circ as structural Verilog
module \状态转移_真值表一键生成  (
  input  S1,
  input  S0,
  input  A,
  output S_1,
  output S_0
);


  assign S_0 = A;
  assign S_1 = S0;
endmodule

module \即时输出_真值表一键生成  (
  input  S1,
  input  S0,
  input  A,
  output s0_2,
  output s1_2,
  output s2,
  output s3,
  output s4
);

  wire nand_1_out, nand_2_out, nand_3_out, nand_4_out, nand_5_out, nand_6_out, nand_7_out, nand_9_out;

  nand nand_1 (nand_1_out, S0, S0);
  nand nand_2 (nand_2_out, A, A);
  nand nand_3 (nand_3_out, S0, S0);
  nand nand_4 (nand_4_out, S0, A);
  nand nand_5 (nand_5_out, A, A);
  nand nand_6 (nand_6_out, nand_1_out, nand_2_out);
  nand nand_7 (nand_7_out, nand_3_out, A);
  nand nand_8 (s3, nand_4_out, nand_4_out);
  nand nand_9 (nand_9_out, S0, nand_5_out);
  nand nand_10 (s1_2, nand_6_out, nand_6_out);
  nand nand_11 (s2, nand_7_out, nand_7_out);
  nand nand_12 (s4, nand_9_out, nand_9_out);

  assign s0_2 = 1'b0;
endmodule

module mod5 (
  input  In,
  output s0,
  output s1,
  output s2,
  output s3,
  output s4
);

  wire clock_1_out;
  wire [1:0] register_1_q, \状态转移_真值表一键生成_1_s_1 ;

  \状态转移_真值表一键生成  \u_状态转移_真值表一键生成_1  (
    .S1(register_1_q[0]), .S0(register_1_q[1]), .A(In), .S_1(\状态转移_真值表一键生成_1_s_1 [0]),
    .S_0(\状态转移_真值表一键生成_1_s_1 [1]));
  Register #(.width(2)) register_1 (.D(\状态转移_真值表一键生成_1_s_1 ), .Q(register_1_q), .clk(clock_1_out));  // open: en, clr
  Clock clock_1 (.out(clock_1_out));
  \即时输出_真值表一键生成  \u_即时输出_真值表一键生成_1  (
    .S1(register_1_q[0]), .S0(register_1_q[1]), .A(In), .s0_2(s0), .s1_2(s1), .s2(s2), .s3(s3), .s4(s4));
endmodule
