// Logisim project Pre_ChoicesProblems.circ as structural Verilog: 1 circuit, main circuit main
module main (
  input  [7:0] in_1,
  output [1:0] out_2
);

  and and_1 (out_2[0], in_1[0], in_1[2]);
  xnor xnor_1 (out_2[1], in_1[4], in_1[6]);
endmodule
