// Logisim project Pre_FilesGroups.circ as structural Verilog: 5 circuits, main circuit swap
module swap (
  input  I1,
  input  I2,
  input  S,
  output O1,
  output O2
);

  wire and_1_out, and_2_out, and_3_out, and_4_out;

  and and_1 (and_1_out, ~S, I1);  // AND_Gate
  and and_2 (and_2_out, S, I2);
  and and_3 (and_3_out, S, I1);
  and and_4 (and_4_out, ~S, I2);  // AND_Gate
  or or_1 (O1, and_1_out, and_2_out);
  or or_2 (O2, and_3_out, and_4_out);
endmodule

module _1bit_swap (
  input  I1,
  input  I2,
  input  S,
  output O1,
  output O2
);

  wire and_1_out, and_2_out, and_3_out, and_4_out;

  and and_1 (and_1_out, ~S, I1);  // AND_Gate
  and and_2 (and_2_out, S, I2);
  and and_3 (and_3_out, S, I1);
  and and_4 (and_4_out, ~S, I2);  // AND_Gate
  or or_1 (O1, and_1_out, and_2_out);
  or or_2 (O2, and_3_out, and_4_out);
endmodule

module _4bit_swap (
  input  [3:0] In_01,
  input  [3:0] In_02,
  input  Enable,
  output [3:0] out_4,
  output [3:0] out_5
);

  _1bit_swap u_1bit_swap_1 (.I1(In_01[0]), .I2(In_02[0]), .S(Enable), .O1(out_4[0]), .O2(out_5[0]));
  _1bit_swap u_1bit_swap_2 (.I1(In_01[1]), .I2(In_02[1]), .S(Enable), .O1(out_4[1]), .O2(out_5[1]));
  _1bit_swap u_1bit_swap_3 (.I1(In_01[2]), .I2(In_02[2]), .S(Enable), .O1(out_4[2]), .O2(out_5[2]));
  _1bit_swap u_1bit_swap_4 (.I1(In_01[3]), .I2(In_02[3]), .S(Enable), .O1(out_4[3]), .O2(out_5[3]));
endmodule

module _4bit_if_swap (
  input  [3:0] In_01,
  input  [3:0] In_02,
  output [3:0] Out_01,
  output [3:0] Out_02
);

  wire comparator_1_gt;

  Comparator #(.width(4), .mode("unsigned")) comparator_1 (.a(In_01), .b(In_02), .gt(comparator_1_gt));  // open: eq, lt
  // Probe on In_01
  // Probe on comparator_1_gt
  _4bit_swap u_4bit_swap_1 (.In_01(In_01), .In_02(In_02), .Enable(comparator_1_gt), .out_4(Out_01), .out_5(Out_02));
  // Probe on In_02
endmodule

module _4bit_sort (
  input  [3:0] in_1,
  input  [3:0] in_2,
  input  [3:0] in_3,
  input  [3:0] in_4,
  output [3:0] out_5,
  output [3:0] out_6,
  output [3:0] out_7,
  output [3:0] out_8
);

  wire [3:0] n4bit_if_swap_1_out_01, n4bit_if_swap_1_out_02, n4bit_if_swap_2_out_01, n4bit_if_swap_2_out_02,
       n4bit_if_swap_3_out_01, n4bit_if_swap_3_out_02, n4bit_if_swap_5_out_01, n4bit_if_swap_6_out_01;

  _4bit_if_swap u_4bit_if_swap_1 (
    .In_01(in_1), .In_02(in_2), .Out_01(n4bit_if_swap_1_out_01), .Out_02(n4bit_if_swap_1_out_02));
  // Probe on nothing
  _4bit_if_swap u_4bit_if_swap_2 (
    .In_01(n4bit_if_swap_1_out_01), .In_02(n4bit_if_swap_3_out_01), .Out_01(n4bit_if_swap_2_out_01),
    .Out_02(n4bit_if_swap_2_out_02));
  _4bit_if_swap u_4bit_if_swap_3 (
    .In_01(n4bit_if_swap_1_out_02), .In_02(in_3), .Out_01(n4bit_if_swap_3_out_01),
    .Out_02(n4bit_if_swap_3_out_02));
  _4bit_if_swap u_4bit_if_swap_4 (
    .In_01(n4bit_if_swap_2_out_01), .In_02(n4bit_if_swap_5_out_01), .Out_01(out_5), .Out_02(out_6));
  _4bit_if_swap u_4bit_if_swap_5 (
    .In_01(n4bit_if_swap_2_out_02), .In_02(n4bit_if_swap_6_out_01), .Out_01(n4bit_if_swap_5_out_01),
    .Out_02(out_7));
  _4bit_if_swap u_4bit_if_swap_6 (
    .In_01(n4bit_if_swap_3_out_02), .In_02(in_4), .Out_01(n4bit_if_swap_6_out_01), .Out_02(out_8));
endmodule
