// Logisim project Pre_Learn.circ as structural Verilog
module e_Memory (
  input  [3:0] in_1,
  input  in_2,
  input  in_3,
  input  in_4,
  input  in_5,
  input  [7:0] in_6,
  output out_7,
  output [3:0] out_8,
  output [7:0] out_9
);

  wire clock_1_out, clock_3_out, shift_register_1_p2;

  Clock clock_1 (.out(clock_1_out));
  D_Flip_Flop d_ff_1 ();  // open: clk, D, Q, Qn, preset, en, reset
  T_Flip_Flop t_ff_1 ();  // open: clk, T, Q, Qn, preset, reset, en
  J_K_Flip_Flop j_k_ff_1 (.J(in_2), .clk(clock_1_out), .K(in_3), .Q(out_7), .en(in_5));  // open: Qn, preset, reset
  S_R_Flip_Flop s_r_ff_1 ();  // open: S, clk, R, Q, Qn, preset, reset, en
  // Shift_Register #(.width(4), .length(4), .parallel("false")) shift_register_1: pin names not known; wires that end beside it: in_1, shift_register_1_p2, out_8
  Clock clock_2 (.out(shift_register_1_p2));
  Shift_Register #(.width(8), .length(4)) shift_register_2 (
    .shift(in_4), .in(in_6), .clk(clock_3_out), .out(out_9));  // open: load, clr, d0, q0, d1, q1, d2, q2, d3, q3
  Clock clock_3 (.out(clock_3_out));
  Register register_1 ();  // open: D, en, Q, clk, clr
  Counter counter_1 ();  // open: load, D, count, Q, carry, clk, clr
  Random random_1 ();  // open: clk, next, out, clr
  RAM ram_1 ();  // open: addr, data, sel, clk, ld, clr
  ROM rom_1 ();  // open: addr, data, sel
endmodule
