// Logisim project RAM_Test.circ as structural Verilog: 1 circuit, main circuit main
module main (
  input  in_1
);

  wire clock_1_out;
  wire [7:0] counter_1_q, xnor_1_out;

  // Probe on counter_1_q
  Counter counter_1 (.Q(counter_1_q), .clk(clock_1_out), .clr(in_1));  // open: load, D, count, carry
  // Probe on xnor_1_out
  assign xnor_1_out = ~(counter_1_q ^ 8'h23);  // XNOR_Gate xnor_1, 8 bits wide
  Clock clock_1 (.out(clock_1_out));
  RAM #(.bus("separate")) ram_1 (
    .addr(xnor_1_out), .din(counter_1_q), .clk(clock_1_out));  // open: data, str, sel, ld, clr
endmodule
