// Logisim project 斐波那契_快速幂_2的32次幂的F.circ as structural Verilog: 8 circuits, main circuit main
module main (
  input  in_1,
  input  [31:0] N,
  output [31:0] out_3
);

  wire A_enable, clk, E0_A1, enable, init, \总运算周期_s乘法选择_最后输出控制_1_s12_mux ;
  wire [31:0] a_11, a_12, a_21, a_22, A_A_result_11, A_A_result_12, A_A_result_21, A_A_result_22, \A初值_a_11 ,
       \A初值_a_12 , \A初值_a_21 , \A初值_a_22 , E_e_11, E_e_12, E_e_21, E_e_22, \n2_2同型矩阵乘法_8_4个引脚_1_result_11 ,
       \n2_2同型矩阵乘法_8_4个引脚_1_result_12 , \n2_2同型矩阵乘法_8_4个引脚_1_result_21 , \n2_2同型矩阵乘法_8_4个引脚_1_result_22 ,
       \n4和1的mux_对应同一矩阵的4个元素_1__11_3 , \n4和1的mux_对应同一矩阵的4个元素_1__12_3 , \n4和1的mux_对应同一矩阵的4个元素_1__21_3 ,
       \n4和1的mux_对应同一矩阵的4个元素_1__22_3 , \n4和1的mux_对应同一矩阵的4个元素_2__11_3 , \n4和1的mux_对应同一矩阵的4个元素_2__12_3 ,
       \n4和1的mux_对应同一矩阵的4个元素_2__21_3 , \n4和1的mux_对应同一矩阵的4个元素_2__22_3 , \n4和1的mux_对应同一矩阵的4个元素_3__11_3 ,
       \n4和1的mux_对应同一矩阵的4个元素_3__12_3 , \n4和1的mux_对应同一矩阵的4个元素_3__21_3 , \n4和1的mux_对应同一矩阵的4个元素_3__22_3 , s_11,
       s_12, s_21, s_22, \S初值_e_11 , \S初值_e_12 , \S初值_e_21 , \S初值_e_22 ;

  Clock clock_1 (.out(clk));
  // Probe on \A初值_a_11 
  // Probe on \A初值_a_21 
  // Probe on \A初值_a_12 
  // Probe on \A初值_a_22 
  \S的初始单位矩阵_也作E  E (.E_11(E_e_11), .E_12(E_e_12), .E_21(E_e_21), .E_22(E_e_22));
  \_2_2同型矩阵乘法_8_4个引脚  A_A (
    .x_11(a_11), .x_12(a_12), .x_21(a_21), .x_22(a_22), .y_11(a_11), .y_12(a_12), .y_21(a_21), .y_22(a_22),
    .result_11(A_A_result_11), .result_12(A_A_result_12), .result_21(A_A_result_21), .result_22(A_A_result_22));
  \_4和1的mux_对应同一矩阵的4个元素  \u_4和1的mux_对应同一矩阵的4个元素_1  (
    ._11(E_e_11), ._12(E_e_12), ._21(E_e_21), ._22(E_e_22), ._11_2(a_11), ._12_2(a_12), ._21_2(a_21),
    ._22_2(a_22), .sel(E0_A1), ._11_3(\n4和1的mux_对应同一矩阵的4个元素_1__11_3 ),
    ._12_3(\n4和1的mux_对应同一矩阵的4个元素_1__12_3 ), ._21_3(\n4和1的mux_对应同一矩阵的4个元素_1__21_3 ),
    ._22_3(\n4和1的mux_对应同一矩阵的4个元素_1__22_3 ));
  \A的初始矩阵  \A初值  (.a_11(\A初值_a_11 ), .a_12(\A初值_a_12 ), .a_21(\A初值_a_21 ), .a_22(\A初值_a_22 ));
  // Probe on init
  \初始化控制器_clk作输入_控制mux  \u_初始化控制器_clk作输入_控制mux_1  (.chs(init), .clk(clk), .reset(in_1));
  \_2_2同型矩阵乘法_8_4个引脚  \u_2_2同型矩阵乘法_8_4个引脚_1  (
    .x_11(s_11), .x_12(s_12), .x_21(s_21), .x_22(s_22), .y_11(\n4和1的mux_对应同一矩阵的4个元素_1__11_3 ),
    .y_12(\n4和1的mux_对应同一矩阵的4个元素_1__12_3 ), .y_21(\n4和1的mux_对应同一矩阵的4个元素_1__21_3 ),
    .y_22(\n4和1的mux_对应同一矩阵的4个元素_1__22_3 ), .result_11(\n2_2同型矩阵乘法_8_4个引脚_1_result_11 ),
    .result_12(\n2_2同型矩阵乘法_8_4个引脚_1_result_12 ), .result_21(\n2_2同型矩阵乘法_8_4个引脚_1_result_21 ),
    .result_22(\n2_2同型矩阵乘法_8_4个引脚_1_result_22 ));
  \总运算周期_S乘法选择_最后输出控制  \u_总运算周期_s乘法选择_最后输出控制_1  (
    .N(N), .clk(clk), .reset(in_1), .enable(enable), .s12_mux(\总运算周期_s乘法选择_最后输出控制_1_s12_mux ), .A1_E0(E0_A1));
  \_4和1的mux_对应同一矩阵的4个元素  \u_4和1的mux_对应同一矩阵的4个元素_2  (
    ._11(A_A_result_11), ._12(A_A_result_12), ._21(A_A_result_21), ._22(A_A_result_22), ._11_2(\A初值_a_11 ),
    ._12_2(\A初值_a_12 ), ._21_2(\A初值_a_21 ), ._22_2(\A初值_a_22 ), .sel(init),
    ._11_3(\n4和1的mux_对应同一矩阵的4个元素_2__11_3 ), ._12_3(\n4和1的mux_对应同一矩阵的4个元素_2__12_3 ),
    ._21_3(\n4和1的mux_对应同一矩阵的4个元素_2__21_3 ), ._22_3(\n4和1的mux_对应同一矩阵的4个元素_2__22_3 ));
  \_2_2矩阵寄存器堆_4个reg  A (
    .a_11(\n4和1的mux_对应同一矩阵的4个元素_2__11_3 ), .a_12(\n4和1的mux_对应同一矩阵的4个元素_2__12_3 ),
    .a_21(\n4和1的mux_对应同一矩阵的4个元素_2__21_3 ), .a_22(\n4和1的mux_对应同一矩阵的4个元素_2__22_3 ), .enable(A_enable),
    .clk(clk), .a_11_2(a_11), .a_12_2(a_12), .a_21_2(a_21), .a_22_2(a_22));
  \S的初始单位矩阵_也作E  \S初值  (.E_11(\S初值_e_11 ), .E_12(\S初值_e_12 ), .E_21(\S初值_e_21 ), .E_22(\S初值_e_22 ));
  Multiplexer #(.enable("false")) multiplexer_1 (.in0(enable), .in1(1'b1), .out(A_enable), .sel(init));
  \_4和1的mux_对应同一矩阵的4个元素  \u_4和1的mux_对应同一矩阵的4个元素_3  (
    ._11(\n2_2同型矩阵乘法_8_4个引脚_1_result_11 ), ._12(\n2_2同型矩阵乘法_8_4个引脚_1_result_12 ),
    ._21(\n2_2同型矩阵乘法_8_4个引脚_1_result_21 ), ._22(\n2_2同型矩阵乘法_8_4个引脚_1_result_22 ), ._11_2(\S初值_e_11 ),
    ._12_2(\S初值_e_12 ), ._21_2(\S初值_e_21 ), ._22_2(\S初值_e_22 ), .sel(init),
    ._11_3(\n4和1的mux_对应同一矩阵的4个元素_3__11_3 ), ._12_3(\n4和1的mux_对应同一矩阵的4个元素_3__12_3 ),
    ._21_3(\n4和1的mux_对应同一矩阵的4个元素_3__21_3 ), ._22_3(\n4和1的mux_对应同一矩阵的4个元素_3__22_3 ));
  \_2_2矩阵寄存器堆_4个reg  S (
    .a_11(\n4和1的mux_对应同一矩阵的4个元素_3__11_3 ), .a_12(\n4和1的mux_对应同一矩阵的4个元素_3__12_3 ),
    .a_21(\n4和1的mux_对应同一矩阵的4个元素_3__21_3 ), .a_22(\n4和1的mux_对应同一矩阵的4个元素_3__22_3 ), .enable(A_enable),
    .clk(clk), .a_11_2(s_11), .a_12_2(s_12), .a_21_2(s_21), .a_22_2(s_22));
  Multiplexer #(.width(32), .enable("false")) multiplexer_2 (
    .in0({32{1'b0}}), .in1(s_12), .out(out_3), .sel(\总运算周期_s乘法选择_最后输出控制_1_s12_mux ));
  // Probe on a_11
  // Probe on a_21
  // Probe on a_12
  // Probe on a_22
  // Probe on s_11
  // Probe on s_21
  // Probe on s_12
  // Probe on s_22
endmodule

module \_2_2矩阵寄存器堆_4个reg  (
  input  [31:0] a_11,
  input  [31:0] a_12,
  input  [31:0] a_21,
  input  [31:0] a_22,
  input  enable,
  input  clk,
  output [31:0] a_11_2,
  output [31:0] a_12_2,
  output [31:0] a_21_2,
  output [31:0] a_22_2
);

  Register #(.width(32)) register_1 (.D(a_11), .en(enable), .Q(a_11_2), .clk(clk));  // open: clr
  Register #(.width(32)) register_2 (.D(a_12), .en(enable), .Q(a_12_2), .clk(clk));  // open: clr
  Register #(.width(32)) register_3 (.D(a_21), .en(enable), .Q(a_21_2), .clk(clk));  // open: clr
  Register #(.width(32)) register_4 (.D(a_22), .en(enable), .Q(a_22_2), .clk(clk));  // open: clr
endmodule

module \_2_2同型矩阵乘法_8_4个引脚  (
  input  [31:0] x_11,
  input  [31:0] x_12,
  input  [31:0] x_21,
  input  [31:0] x_22,
  input  [31:0] y_11,
  input  [31:0] y_12,
  input  [31:0] y_21,
  input  [31:0] y_22,
  output [31:0] result_11,
  output [31:0] result_12,
  output [31:0] result_21,
  output [31:0] result_22
);

  wire [31:0] multiplier_1_out, multiplier_2_out, multiplier_3_out, multiplier_4_out, multiplier_5_out,
       multiplier_6_out, multiplier_7_out, multiplier_8_out;

  Multiplier #(.width(32)) multiplier_1 (.a(x_11), .b(y_11), .out(multiplier_1_out));  // open: cin, cout
  Multiplier #(.width(32)) multiplier_2 (.a(x_12), .b(y_21), .out(multiplier_2_out));  // open: cin, cout
  Multiplier #(.width(32)) multiplier_3 (.a(x_11), .b(y_12), .out(multiplier_3_out));  // open: cin, cout
  Multiplier #(.width(32)) multiplier_4 (.a(x_12), .b(y_22), .out(multiplier_4_out));  // open: cin, cout
  Multiplier #(.width(32)) multiplier_5 (.a(x_21), .b(y_11), .out(multiplier_5_out));  // open: cin, cout
  Multiplier #(.width(32)) multiplier_6 (.a(x_22), .b(y_21), .out(multiplier_6_out));  // open: cin, cout
  Multiplier #(.width(32)) multiplier_7 (.a(x_21), .b(y_12), .out(multiplier_7_out));  // open: cin, cout
  Multiplier #(.width(32)) multiplier_8 (.a(x_22), .b(y_22), .out(multiplier_8_out));  // open: cin, cout
  Adder #(.width(32)) adder_1 (.a(multiplier_1_out), .b(multiplier_2_out), .out(result_11));  // open: cin, cout
  Adder #(.width(32)) adder_2 (.a(multiplier_3_out), .b(multiplier_4_out), .out(result_12));  // open: cin, cout
  Adder #(.width(32)) adder_3 (.a(multiplier_5_out), .b(multiplier_6_out), .out(result_21));  // open: cin, cout
  Adder #(.width(32)) adder_4 (.a(multiplier_7_out), .b(multiplier_8_out), .out(result_22));  // open: cin, cout
endmodule

module \A的初始矩阵  (
  output [31:0] a_11,
  output [31:0] a_12,
  output [31:0] a_21,
  output [31:0] a_22
);


  assign a_11 = 32'h1;
  assign a_12 = 32'h1;
  assign a_21 = 32'h1;
  assign a_22 = {32{1'b0}};
endmodule

module \S的初始单位矩阵_也作E  (
  output [31:0] E_11,
  output [31:0] E_12,
  output [31:0] E_21,
  output [31:0] E_22
);


  assign E_11 = 32'h1;
  assign E_12 = {32{1'b0}};
  assign E_21 = {32{1'b0}};
  assign E_22 = 32'h1;
endmodule

// init
module \初始化控制器_clk作输入_控制mux  (
  input  clk,
  input  reset,
  output chs
);

  wire [1:0] counter_1_q;

  Counter #(.width(2), .max('h2), .ongoal("stay")) counter_1 (
    .Q(counter_1_q), .clk(clk), .clr(reset));  // open: load, D, count, carry
  Comparator #(.width(2), .mode("unsigned")) comparator_1 (.a(2'b01), .b(counter_1_q), .gt(chs));  // open: eq, lt
endmodule

// control
module \总运算周期_S乘法选择_最后输出控制  (
  input  [31:0] N,
  input  clk,
  input  reset,
  output enable,
  output s12_mux,
  output A1_E0
);

  wire not_1_out, \初始化控制器_clk作输入_控制mux_1_chs ;
  wire [31:0] multiplexer_1_out, register_1_q, shifter_1_out;

  \初始化控制器_clk作输入_控制mux  \u_初始化控制器_clk作输入_控制mux_1  (.chs(\初始化控制器_clk作输入_控制mux_1_chs ), .clk(clk), .reset(reset));
  Multiplexer #(.width(32), .enable("false")) multiplexer_1 (
    .in0(N), .in1(shifter_1_out), .out(multiplexer_1_out), .sel(not_1_out));
  not not_1 (not_1_out, \初始化控制器_clk作输入_控制mux_1_chs );
  Register #(.width(32)) register_1 (.D(multiplexer_1_out), .Q(register_1_q), .clk(clk));  // open: en, clr
  Comparator #(.width(32), .mode("unsigned")) comparator_1 (
    .a({32{1'b0}}), .b(register_1_q), .eq(s12_mux));  // open: gt, lt
  Bit_Extender #(.in_width(32), .out_width(1)) bit_extender_1 (.in(register_1_q), .out(A1_E0));
  Shifter #(.width(32), .shift("lr")) shifter_1 (.in(register_1_q), .\dist (5'b00001), .out(shifter_1_out));
  not not_2 (enable, s12_mux);
endmodule

// mux
module \_4和1的mux_对应同一矩阵的4个元素  (
  input  [31:0] _11,
  input  [31:0] _12,
  input  [31:0] _21,
  input  [31:0] _22,
  input  [31:0] _11_2,
  input  [31:0] _12_2,
  input  [31:0] _21_2,
  input  [31:0] _22_2,
  input  sel,
  output [31:0] _11_3,
  output [31:0] _12_3,
  output [31:0] _21_3,
  output [31:0] _22_3
);

  Multiplexer #(.width(32), .enable("false")) multiplexer_1 (.in0(_11), .in1(_11_2), .out(_11_3), .sel(sel));
  Multiplexer #(.width(32), .enable("false")) multiplexer_2 (.in0(_12), .in1(_12_2), .out(_12_3), .sel(sel));
  Multiplexer #(.width(32), .enable("false")) multiplexer_3 (.in0(_21), .in1(_21_2), .out(_21_3), .sel(sel));
  Multiplexer #(.width(32), .enable("false")) multiplexer_4 (.in0(_22), .in1(_22_2), .out(_22_3), .sel(sel));
endmodule
