// Logisim project 斐波那契_计数器寄存器.circ as structural Verilog: 1 circuit, main circuit main
module main (
  input  [2:0] N,
  output [3:0] out_2
);

  wire clk, comparator_1_gt, control;
  wire [1:0] counter_1_q;
  wire [3:0] adder_1_out, adder_2_out, bit_extender_1_out, counter_2_q, Fib, Fn_1_q, multiplexer_1_out,
       multiplexer_2_out;

  Counter #(.width(2), .max('h3), .ongoal("stay")) counter_1 (
    .Q(counter_1_q), .clk(clk));  // open: load, D, count, carry, clr
  // Probe on counter_1_q
  Clock clock_1 (.out(clk));
  // Probe on comparator_1_gt
  Comparator #(.width(2), .mode("unsigned")) comparator_1 (
    .a(2'b01), .b(counter_1_q), .gt(comparator_1_gt));  // open: eq, lt
  assign bit_extender_1_out = {{1{1'b0}}, N};  // Bit_Extender bit_extender_1
  Counter #(.width(4), .max('hf), .ongoal("stay")) counter_2 (
    .Q(counter_2_q), .clk(clk));  // open: load, D, count, carry, clr
  // Probe on multiplexer_1_out
  Multiplexer #(.width(4), .enable("false")) multiplexer_1 (
    .in0(adder_2_out), .in1(4'b0000), .out(multiplexer_1_out), .sel(comparator_1_gt));
  // Probe on Fib
  Multiplexer #(.width(4), .enable("false")) multiplexer_2 (
    .in0(Fib), .in1(4'b0001), .out(multiplexer_2_out), .sel(comparator_1_gt));
  Adder #(.width(4)) adder_1 (.a(bit_extender_1_out), .b(4'b0001), .out(adder_1_out));  // open: cin, cout
  // Probe on counter_2_q
  // Probe on Fib
  Register #(.width(4)) Fn (.D(multiplexer_1_out), .en(control), .Q(Fib), .clk(clk));  // open: clr
  Register #(.width(4)) Fn_1 (.D(multiplexer_2_out), .en(control), .Q(Fn_1_q), .clk(clk));  // open: clr
  // Probe on adder_1_out
  Adder #(.width(4)) adder_2 (.a(Fib), .b(Fn_1_q), .out(adder_2_out));  // open: cin, cout
  Comparator #(.width(4), .mode("unsigned")) comparator_2 (
    .a(adder_1_out), .b(counter_2_q), .gt(control));  // open: eq, lt
  // Probe on control
  Multiplexer #(.width(4), .enable("false")) multiplexer_3 (.in0(Fib), .in1(4'b0000), .out(out_2), .sel(control));
endmodule
