// Logisim project Pre_俄罗斯方块回忆.circ as structural Verilog: 1 circuit, main circuit main
module main (
  input  [7:0] \input ,
  input  reset,
  input  clk,
  output [1:0] \output 
);

  wire comparator_1_eq;
  wire [1:0] multiplexer_3_out;
  wire [2:0] bitfinder_1_index;
  wire [3:0] bitadder_1_out;
  wire [7:0] multiplexer_1_out, multiplexer_2_out, or_1_out, or_2_out, \reg ;

  assign or_1_out = \reg  | \input ;  // OR_Gate or_1, 8 bits wide
  Multiplexer #(.width(8), .enable("false")) multiplexer_1 (
    .in0(\input ), .in1(\reg ), .out(multiplexer_1_out), .sel(multiplexer_3_out[0]));
  assign or_2_out = multiplexer_1_out | \reg ;  // OR_Gate or_2, 8 bits wide
  Comparator comparator_1 (.a(or_1_out), .b({8{1'b1}}), .eq(comparator_1_eq));  // open: gt, lt
  Register register_1 (.D(multiplexer_2_out), .Q(\reg ), .clk(clk), .clr(reset));  // open: en
  Multiplexer #(.width(8), .enable("false")) multiplexer_2 (
    .in0(or_2_out), .in1({8{1'b0}}), .out(multiplexer_2_out), .sel(comparator_1_eq));
  BitFinder bitfinder_1 (.in(\input ), .index(bitfinder_1_index));  // open: found
  Multiplexer #(.select(3), .enable("false")) multiplexer_3 (
    .in0(\reg [0]), .in1(\reg [1]), .in2(\reg [2]), .in3(\reg [3]), .in4(\reg [4]), .in5(\reg [5]),
    .in6(\reg [6]), .in7(\reg [7]), .out(multiplexer_3_out[0]), .sel(bitfinder_1_index));
  BitAdder bitadder_1 (.in0(\reg ), .out(bitadder_1_out));
  Comparator #(.width(4), .mode("unsigned")) comparator_2 (
    .a(bitadder_1_out), .b(4'b0111), .eq(multiplexer_3_out[1]));  // open: gt, lt
  Multiplexer #(.select(2), .width(2), .enable("false")) multiplexer_4 (
    .in0(2'b10), .in1(2'b01), .in2(2'b11), .in3(2'b01), .out(\output ), .sel(multiplexer_3_out));

  // Other names for the same wires on the sheet: rst = reset
endmodule
