// Logisim project 01_CRC-不断异或.circ as structural Verilog: 2 circuits, main circuit CRC
module CRC (
  input  [7:0] \被除数 ,
  input  [3:0] \除数 ,
  output [10:0] out_3
);

  wire [2:0] xor_1_out_3, xor_2_out_3, xor_3_out_3, xor_4_out_3, xor_5_out_3, xor_6_out_3, xor_7_out_3;

  \xor  xor_1 (.\被除数 (\被除数 [7:4]), .\除数 (\除数 ), .out_3(xor_1_out_3));
  \xor  xor_2 (.\被除数 ({xor_1_out_3, \被除数 [3]}), .\除数 (\除数 ), .out_3(xor_2_out_3));
  \xor  xor_3 (.\被除数 ({xor_2_out_3, \被除数 [2]}), .\除数 (\除数 ), .out_3(xor_3_out_3));
  \xor  xor_4 (.\被除数 ({xor_3_out_3, \被除数 [1]}), .\除数 (\除数 ), .out_3(xor_4_out_3));
  \xor  xor_5 (.\被除数 ({xor_4_out_3, \被除数 [0]}), .\除数 (\除数 ), .out_3(xor_5_out_3));
  \xor  xor_6 (.\被除数 ({xor_5_out_3, 1'b0}), .\除数 (\除数 ), .out_3(xor_6_out_3));
  // Probe on {xor_6_out_3, 1'b0}
  \xor  xor_7 (.\被除数 ({xor_6_out_3, 1'b0}), .\除数 (\除数 ), .out_3(xor_7_out_3));
  // Probe on {xor_7_out_3, 1'b0}
  \xor  xor_8 (.\被除数 ({xor_7_out_3, 1'b0}), .\除数 (\除数 ), .out_3(out_3[2:0]));

  assign out_3[10:3] = \被除数 ;

  // Other names for the same wires on the sheet: chushu[3:0] = \除数 ; _0 = \被除数 [0]; beichushu[7:0] = \被除数 ;
  //   _1 = \被除数 [1]; _2 = \被除数 [2]; _3 = \被除数 [3]; _4 = \被除数 [4]; _5 = \被除数 [5]; _6 = \被除数 [6]; _7 = \被除数 [7]
endmodule

module \xor  (
  input  [3:0] \被除数 ,
  input  [3:0] \除数 ,
  output [2:0] out_3
);

  wire [3:0] xor_1_out;

  assign xor_1_out = \被除数  ^ \除数 ;  // XOR_Gate xor_1, 4 bits wide
  Multiplexer #(.width(3), .enable("false")) multiplexer_1 (
    .in0(\被除数 [2:0]), .in1(xor_1_out[2:0]), .out(out_3), .sel(\被除数 [3]));
endmodule
