// Logisim project 03_ftoi_只有组合逻辑.circ as structural Verilog: 3 circuits, main circuit ftoi
module ftoi (
  input  [15:0] \input ,
  output [31:0] \output 
);

  wire and_1_out, comparator_1_lt, comparator_2_lt, comparator_3_eq, not_2_out;
  wire [31:0] _2__E_0_1111, adder_1_out, multiplexer_1_out, not_1_out, \计算2_n_____2__n_10_output ;

  _2__E_0_1111 \u_计算2__E_0_1111  (.E(\input [14:10]), ._2__E_0_1111(_2__E_0_1111));
  frac__2n_2n_1_2n_10 \u_计算2_n_____2__n_10  (
    .in_1(_2__E_0_1111), .in_2(\input [9:0]), .\output (\计算2_n_____2__n_10_output ));
  assign not_1_out = ~\计算2_n_____2__n_10_output ;  // NOT_Gate not_1, 32 bits wide
  Comparator #(.width(5), .mode("unsigned")) comparator_1 (
    .a(\input [14:10]), .b(5'b01111), .lt(comparator_1_lt));  // open: gt, eq
  Comparator #(.width(5), .mode("unsigned")) comparator_2 (
    .a(\input [14:10]), .b({5{1'b1}}), .lt(comparator_2_lt));  // open: gt, eq
  Adder #(.width(32)) adder_1 (.a(not_1_out), .b(32'h1), .out(adder_1_out));  // open: cin, cout
  Comparator #(.width(1), .mode("unsigned")) comparator_3 (
    .a(\input [15]), .b(1'b1), .eq(comparator_3_eq));  // open: gt, lt
  not not_2 (not_2_out, comparator_1_lt);
  Multiplexer #(.width(32), .enable("false")) multiplexer_1 (
    .in0(\计算2_n_____2__n_10_output ), .in1(adder_1_out), .out(multiplexer_1_out), .sel(comparator_3_eq));
  and and_1 (and_1_out, not_2_out, comparator_2_lt);
  // Probe on \output 
  Multiplexer #(.width(32), .enable("false")) multiplexer_2 (
    .in0({32{1'b0}}), .in1(multiplexer_1_out), .out(\output ), .sel(and_1_out));

  // Other names for the same wires on the sheet: frac[9:0] = \input [9:0]; E[4:0] = \input [14:10]; S = \input [15]

  // Notes on the sheet:
  //   1.判断E的四种情况
  //   E=1_1111
  //   E>=0_1111
  //   E<0_1111
  //   E=0_0000
  //   2.E-0_1111
  //   5.根据S决定是否取反+1
  //   4.根据frac计算2^n+2^(n-1)+...+2^(n-10)
  //   3.计算2^(E-0_1111) 注意是2^16*2^8*...，不是+
endmodule

module _2__E_0_1111 (
  input  [4:0] E,
  output [31:0] _2__E_0_1111
);

  wire [4:0] subtractor_1_out;
  wire [31:0] multiplexer_1_out, multiplexer_2_out, multiplexer_3_out, multiplexer_4_out, multiplexer_5_out,
       multiplier_1_out, multiplier_2_out, multiplier_3_out;

  // Probe on subtractor_1_out
  Multiplexer #(.width(32), .enable("false")) multiplexer_1 (
    .in0(32'h1), .in1(32'h2), .out(multiplexer_1_out), .sel(subtractor_1_out[0]));
  Subtractor #(.width(5)) subtractor_1 (.a(E), .b(5'b01111), .out(subtractor_1_out));  // open: bin, bout
  Multiplexer #(.width(32), .enable("false")) multiplexer_2 (
    .in0(32'h1), .in1(32'h10), .out(multiplexer_2_out), .sel(subtractor_1_out[2]));
  Multiplexer #(.width(32), .enable("false")) multiplexer_3 (
    .in0(32'h1), .in1(32'h4), .out(multiplexer_3_out), .sel(subtractor_1_out[1]));
  Multiplexer #(.width(32), .enable("false")) multiplexer_4 (
    .in0(32'h1), .in1(32'h10000), .out(multiplexer_4_out), .sel(subtractor_1_out[4]));
  Multiplexer #(.width(32), .enable("false")) multiplexer_5 (
    .in0(32'h1), .in1(32'h100), .out(multiplexer_5_out), .sel(subtractor_1_out[3]));
  Multiplier #(.width(32)) multiplier_1 (
    .a(multiplexer_2_out), .b(multiplier_2_out), .out(multiplier_1_out));  // open: cin, cout
  Multiplier #(.width(32)) multiplier_2 (
    .a(multiplexer_3_out), .b(multiplexer_1_out), .out(multiplier_2_out));  // open: cin, cout
  Multiplier #(.width(32)) multiplier_3 (
    .a(multiplexer_5_out), .b(multiplier_1_out), .out(multiplier_3_out));  // open: cin, cout
  Multiplier #(.width(32)) multiplier_4 (
    .a(multiplexer_4_out), .b(multiplier_3_out), .out(_2__E_0_1111));  // open: cin, cout
endmodule

module frac__2n_2n_1_2n_10 (
  input  [31:0] in_1,
  input  [9:0] in_2,
  output [31:0] \output 
);

  wire [31:0] adder_1_out, adder_2_out, adder_3_out, adder_4_out, adder_5_out, adder_6_out, adder_7_out,
       adder_8_out, adder_9_out, divider_1_out, divider_2_out, divider_3_out, divider_4_out, divider_5_out,
       divider_6_out, divider_7_out, divider_8_out, divider_9_out, divider_10_out, multiplexer_1_out,
       multiplexer_2_out, multiplexer_3_out, multiplexer_4_out, multiplexer_5_out, multiplexer_6_out,
       multiplexer_7_out, multiplexer_8_out, multiplexer_9_out, multiplexer_10_out;

  Divider #(.width(32)) divider_1 (.a(in_1), .b(32'h400), .out(divider_1_out));  // open: upper, rem
  Divider #(.width(32)) divider_2 (.a(in_1), .b(32'h200), .out(divider_2_out));  // open: upper, rem
  Divider #(.width(32)) divider_3 (.a(in_1), .b(32'h100), .out(divider_3_out));  // open: upper, rem
  Divider #(.width(32)) divider_4 (.a(in_1), .b(32'h80), .out(divider_4_out));  // open: upper, rem
  Divider #(.width(32)) divider_5 (.a(in_1), .b(32'h40), .out(divider_5_out));  // open: upper, rem
  Divider #(.width(32)) divider_6 (.a(in_1), .b(32'h20), .out(divider_6_out));  // open: upper, rem
  Divider #(.width(32)) divider_7 (.a(in_1), .b(32'h10), .out(divider_7_out));  // open: upper, rem
  Divider #(.width(32)) divider_8 (.a(in_1), .b(32'h8), .out(divider_8_out));  // open: upper, rem
  Divider #(.width(32)) divider_9 (.a(in_1), .b(32'h4), .out(divider_9_out));  // open: upper, rem
  Divider #(.width(32)) divider_10 (.a(in_1), .b(32'h2), .out(divider_10_out));  // open: upper, rem
  Multiplexer #(.width(32), .enable("false")) multiplexer_1 (
    .in0({32{1'b0}}), .in1(divider_1_out), .out(multiplexer_1_out), .sel(in_2[0]));
  Multiplexer #(.width(32), .enable("false")) multiplexer_2 (
    .in0({32{1'b0}}), .in1(divider_2_out), .out(multiplexer_2_out), .sel(in_2[1]));
  Adder #(.width(32)) adder_1 (.a(multiplexer_1_out), .b(multiplexer_2_out), .out(adder_1_out));  // open: cin, cout
  Multiplexer #(.width(32), .enable("false")) multiplexer_3 (
    .in0({32{1'b0}}), .in1(divider_3_out), .out(multiplexer_3_out), .sel(in_2[2]));
  Multiplexer #(.width(32), .enable("false")) multiplexer_4 (
    .in0({32{1'b0}}), .in1(divider_4_out), .out(multiplexer_4_out), .sel(in_2[3]));
  Adder #(.width(32)) adder_2 (.a(adder_1_out), .b(multiplexer_3_out), .out(adder_2_out));  // open: cin, cout
  Multiplexer #(.width(32), .enable("false")) multiplexer_5 (
    .in0({32{1'b0}}), .in1(divider_5_out), .out(multiplexer_5_out), .sel(in_2[4]));
  Multiplexer #(.width(32), .enable("false")) multiplexer_6 (
    .in0({32{1'b0}}), .in1(divider_6_out), .out(multiplexer_6_out), .sel(in_2[5]));
  Multiplexer #(.width(32), .enable("false")) multiplexer_7 (
    .in0({32{1'b0}}), .in1(divider_7_out), .out(multiplexer_7_out), .sel(in_2[6]));
  Adder #(.width(32)) adder_3 (.a(adder_2_out), .b(multiplexer_4_out), .out(adder_3_out));  // open: cin, cout
  Multiplexer #(.width(32), .enable("false")) multiplexer_8 (
    .in0({32{1'b0}}), .in1(divider_8_out), .out(multiplexer_8_out), .sel(in_2[7]));
  Multiplexer #(.width(32), .enable("false")) multiplexer_9 (
    .in0({32{1'b0}}), .in1(divider_9_out), .out(multiplexer_9_out), .sel(in_2[8]));
  Adder #(.width(32)) adder_4 (.a(adder_3_out), .b(multiplexer_5_out), .out(adder_4_out));  // open: cin, cout
  Multiplexer #(.width(32), .enable("false")) multiplexer_10 (
    .in0({32{1'b0}}), .in1(divider_10_out), .out(multiplexer_10_out), .sel(in_2[9]));
  Adder #(.width(32)) adder_5 (.a(adder_4_out), .b(multiplexer_6_out), .out(adder_5_out));  // open: cin, cout
  Adder #(.width(32)) adder_6 (.a(adder_5_out), .b(multiplexer_7_out), .out(adder_6_out));  // open: cin, cout
  Adder #(.width(32)) adder_7 (.a(adder_6_out), .b(multiplexer_8_out), .out(adder_7_out));  // open: cin, cout
  Adder #(.width(32)) adder_8 (.a(adder_7_out), .b(multiplexer_9_out), .out(adder_8_out));  // open: cin, cout
  Adder #(.width(32)) adder_9 (.a(adder_8_out), .b(multiplexer_10_out), .out(adder_9_out));  // open: cin, cout
  Adder #(.width(32)) adder_10 (.a(adder_9_out), .b(in_1), .out(\output ));  // open: cin, cout

  // Other names for the same wires on the sheet: _2__E_0_1111[31:0] = in_1; frac[9:0] = in_2
endmodule
