// Logisim project 04_导航-moore.circ as structural Verilog: 2 circuits, main circuit navigation
module navigation (
  input  [1:0] dir,
  input  clk,
  input  reset,
  output arrive,
  output hit
);

  wire nextstateandoutputs_1_hit;
  wire [2:0] nextstateandoutputs_1_ns0, state_q;

  // Probe on state_q
  Register #(.width(3)) state (.D(nextstateandoutputs_1_ns0), .Q(state_q), .clk(clk), .clr(reset));  // open: en
  Register #(.width(1)) u_hit (.D(nextstateandoutputs_1_hit), .Q(hit), .clk(clk), .clr(reset));  // open: en
  nextstateAndOutputs nextstateandoutputs_1 (
    .s2(state_q[2]), .s1(state_q[1]), .s0(state_q[0]), .in1(dir[1]), .in0(dir[0]),
    .ns2(nextstateandoutputs_1_ns0[2]), .ns1(nextstateandoutputs_1_ns0[1]),
    .ns0(nextstateandoutputs_1_ns0[0]), .arrive(arrive), .hit(nextstateandoutputs_1_hit));
endmodule

module nextstateAndOutputs (
  input  s2,
  input  s1,
  input  s0,
  input  in1,
  input  in0,
  output ns2,
  output ns1,
  output ns0,
  output arrive,
  output hit
);

  wire and_1_out, and_2_out, and_3_out, and_4_out, and_5_out, and_6_out, and_7_out, and_8_out, and_9_out,
       and_10_out, and_11_out, and_12_out, and_13_out, and_14_out, and_15_out, and_16_out, and_17_out,
       and_18_out, and_19_out, and_20_out, and_21_out, and_22_out, not_1_out, not_2_out, not_3_out,
       not_4_out, not_5_out, not_6_out, not_7_out, not_8_out, not_9_out, not_10_out, not_11_out, not_12_out,
       not_13_out, not_14_out, not_15_out, not_16_out, not_17_out, not_18_out, not_19_out, not_20_out,
       not_21_out, not_22_out, not_23_out, not_24_out, not_25_out, not_26_out, not_27_out, not_28_out,
       not_29_out, not_30_out, not_31_out, not_32_out;

  not not_1 (not_1_out, s0);
  not not_2 (not_2_out, in1);
  not not_3 (not_3_out, in0);
  not not_4 (not_4_out, in1);
  not not_5 (not_5_out, in1);
  not not_6 (not_6_out, in1);
  not not_7 (not_7_out, s1);
  not not_8 (not_8_out, in1);
  not not_9 (not_9_out, in1);
  not not_10 (not_10_out, in0);
  not not_11 (not_11_out, s0);
  not not_12 (not_12_out, in1);
  not not_13 (not_13_out, s0);
  not not_14 (not_14_out, in0);
  not not_15 (not_15_out, s2);
  not not_16 (not_16_out, s1);
  not not_17 (not_17_out, in1);
  not not_18 (not_18_out, in0);
  not not_19 (not_19_out, in0);
  not not_20 (not_20_out, s2);
  not not_21 (not_21_out, s1);
  not not_22 (not_22_out, s0);
  not not_23 (not_23_out, s2);
  not not_24 (not_24_out, s0);
  not not_25 (not_25_out, in1);
  not not_26 (not_26_out, s2);
  not not_27 (not_27_out, s0);
  not not_28 (not_28_out, in0);
  not not_29 (not_29_out, in1);
  not not_30 (not_30_out, in0);
  not not_31 (not_31_out, in1);
  not not_32 (not_32_out, in1);
  and and_1 (and_1_out, s1, not_1_out, not_2_out, not_3_out);
  and and_2 (and_2_out, s1, s0, not_4_out, in0);
  and and_3 (and_3_out, s2, s0, not_5_out);
  and and_4 (and_4_out, s2, s1, not_6_out);
  and and_5 (and_5_out, not_7_out, s0, not_8_out);
  and and_6 (and_6_out, s0, not_9_out, not_10_out);
  and and_7 (and_7_out, s1, not_11_out, not_12_out, in0);
  and and_8 (and_8_out, s1, not_13_out, in1, not_14_out);
  and and_9 (and_9_out, s1, s0, in1, in0);
  and and_10 (and_10_out, s2, s0, in1);
  and and_11 (and_11_out, s2, s1, in1);
  and and_12 (and_12_out, not_15_out, not_16_out, not_17_out, not_18_out);
  and and_13 (and_13_out, s0, in1, in0);
  and and_14 (and_14_out, s1, in1, in0);
  and and_15 (and_15_out, s1, s0, not_19_out);
  and and_16 (and_16_out, not_20_out, not_21_out, not_22_out, in0);
  and and_17 (and_17_out, not_23_out, not_24_out, not_25_out, in0);
  and and_18 (and_18_out, not_26_out, not_27_out, in1, not_28_out);
  and and_19 (and_19_out, s0, in1, in0);
  and and_20 (and_20_out, s1, s0, not_29_out, not_30_out);
  and and_21 (and_21_out, s2, s0, not_31_out);
  and and_22 (and_22_out, s2, s1, not_32_out);
  or or_1 (ns2, and_1_out, and_2_out, and_3_out, and_4_out);
  or or_2 (ns1, and_5_out, and_6_out, and_7_out, and_8_out, and_9_out, and_10_out, and_11_out);
  or or_3 (ns0, and_12_out, and_13_out, and_14_out, and_15_out);
  or or_4 (hit, and_16_out, and_17_out, and_18_out, and_19_out, and_20_out, and_21_out, and_22_out);

  assign arrive = s2;
endmodule
