// Logisim project 05_正则fsm-mealy.circ as structural Verilog: 2 circuits, main circuit fsm
module fsm (
  input  clr,
  input  [1:0] \input ,
  output \output 
);

  wire clk, comparator_1_eq, comparator_2_eq;
  wire [1:0] multiplexer_1_out, nextstate_1_ns0, \reg ;

  Clock u_clk (.out(clk));
  nextState nextstate_1 (
    .state1(\reg [1]), .state0(\reg [0]), .in1(\input [1]), .in0(\input [0]), .ns1(nextstate_1_ns0[1]),
    .ns0(nextstate_1_ns0[0]));
  Multiplexer #(.width(2), .enable("false")) multiplexer_1 (
    .in0(nextstate_1_ns0), .in1(2'b00), .out(multiplexer_1_out), .sel(clr));
  // Probe on \reg 
  // Probe on \input 
  // Probe on \output 
  Register #(.width(2)) register_1 (.D(multiplexer_1_out), .Q(\reg ), .clk(clk));  // open: en, clr
  Comparator #(.width(4)) comparator_1 (.a({\reg , \input }), .b(4'b1000), .eq(comparator_1_eq));  // open: gt, lt
  Comparator #(.width(4)) comparator_2 (.a({\reg , \input }), .b(4'b1010), .eq(comparator_2_eq));  // open: gt, lt
  or or_1 (\output , comparator_1_eq, comparator_2_eq);
endmodule

module nextState (
  input  state1,
  input  state0,
  input  in1,
  input  in0,
  output ns1,
  output ns0
);

  wire and_1_out, and_2_out, and_3_out, and_4_out, not_1_out, not_2_out, not_3_out, not_4_out, not_5_out,
       not_6_out, not_7_out;

  not not_1 (not_1_out, state1);
  and and_1 (and_1_out, not_1_out, state0, not_2_out);
  not not_2 (not_2_out, in0);
  and and_2 (and_2_out, state1, not_3_out, not_4_out);
  not not_3 (not_3_out, state0);
  not not_4 (not_4_out, in0);
  not not_5 (not_5_out, in1);
  and and_3 (and_3_out, not_5_out, in0);
  and and_4 (and_4_out, state1, not_6_out, not_7_out);
  not not_6 (not_6_out, state0);
  not not_7 (not_7_out, in0);
  or or_1 (ns1, and_1_out, and_2_out);
  or or_2 (ns0, and_3_out, and_4_out);
endmodule
