// Logisim project Fib快速幂.circ as structural Verilog: 8 circuits, main circuit main
module main (
  input  [31:0] N,
  output [31:0] Nth
);

  wire \_0110_n是否为1以上 , \_0110_n最低位是否为1 , \_1000_只在第一个上升沿之前为1 , _1110, clk;
  wire [31:0] _1, _1_prime, _2, _2_prime, _3, _3_prime, _4, _4_prime, \A初始化_a_11 , \A初始化_a_12 , \A初始化_a_21 ,
       \A初始化_a_22 , \E单位阵_2_e_11 , \E单位阵_2_e_12 , \E单位阵_2_e_21 , \E单位阵_2_e_22 , \E单位阵_e_11 , \E单位阵_e_12 ,
       \E单位阵_e_21 , \E单位阵_e_22 , \乘_2_result_11 , \乘_2_result_12 , \乘_2_result_21 , \乘_2_result_22 ,
       \乘_result_11 , \乘_result_12 , \乘_result_21 , \乘_result_22 , \选_2__11_3 , \选_2__12_3 , \选_2__21_3 ,
       \选_2__22_3 , \选_3__11_3 , \选_3__12_3 , \选_3__21_3 , \选_3__22_3 , \选__11_3 , \选__12_3 , \选__21_3 ,
       \选__22_3 ;

  \CombLogic_E单位阵  \E单位阵  (.E_11(\E单位阵_e_11 ), .E_12(\E单位阵_e_12 ), .E_21(\E单位阵_e_21 ), .E_22(\E单位阵_e_22 ));
  \CombLogic_4个数同时选择  \u_选  (
    ._11(\E单位阵_e_11 ), ._12(\E单位阵_e_12 ), ._21(\E单位阵_e_21 ), ._22(\E单位阵_e_22 ), ._11_2(_1), ._12_2(_2),
    ._21_2(_3), ._22_2(_4), .select(\_0110_n最低位是否为1 ), ._11_3(\选__11_3 ), ._12_3(\选__12_3 ),
    ._21_3(\选__21_3 ), ._22_3(\选__22_3 ));
  Clock clock_1 (.out(clk));
  \CombLogic_矩阵乘法  \u_乘  (
    .x_11(_1), .x_12(_2), .x_21(_3), .x_22(_4), .y_11(_1), .y_12(_2), .y_21(_3), .y_22(_4),
    .result_11(\乘_result_11 ), .result_12(\乘_result_12 ), .result_21(\乘_result_21 ), .result_22(\乘_result_22 ));
  \CombLogic_A初始化矩阵  \A初始化  (.a_11(\A初始化_a_11 ), .a_12(\A初始化_a_12 ), .a_21(\A初始化_a_21 ), .a_22(\A初始化_a_22 ));
  \CombLogic_矩阵乘法  \u_乘_2  (
    .x_11(_1_prime), .x_12(_2_prime), .x_21(_3_prime), .x_22(_4_prime), .y_11(\选__11_3 ), .y_12(\选__12_3 ),
    .y_21(\选__21_3 ), .y_22(\选__22_3 ), .result_11(\乘_2_result_11 ), .result_12(\乘_2_result_12 ),
    .result_21(\乘_2_result_21 ), .result_22(\乘_2_result_22 ));
  \CombLogic_E单位阵  \E单位阵_2  (.E_11(\E单位阵_2_e_11 ), .E_12(\E单位阵_2_e_12 ), .E_21(\E单位阵_2_e_21 ), .E_22(\E单位阵_2_e_22 ));
  \_1T高电平_第一个上升沿后为0的初始化控制器  _1000 (.clk(clk), .\只在第一个上升沿之前为1 (\_1000_只在第一个上升沿之前为1 ));
  \CombLogic_4个数同时选择  \u_选_2  (
    ._11(\乘_result_11 ), ._12(\乘_result_12 ), ._21(\乘_result_21 ), ._22(\乘_result_22 ), ._11_2(\A初始化_a_11 ),
    ._12_2(\A初始化_a_12 ), ._21_2(\A初始化_a_21 ), ._22_2(\A初始化_a_22 ), .select(\_1000_只在第一个上升沿之前为1 ),
    ._11_3(\选_2__11_3 ), ._12_3(\选_2__12_3 ), ._21_3(\选_2__21_3 ), ._22_3(\选_2__22_3 ));
  \CombLogic_4个数同时选择  \u_选_3  (
    ._11(\乘_2_result_11 ), ._12(\乘_2_result_12 ), ._21(\乘_2_result_21 ), ._22(\乘_2_result_22 ),
    ._11_2(\E单位阵_2_e_11 ), ._12_2(\E单位阵_2_e_12 ), ._21_2(\E单位阵_2_e_21 ), ._22_2(\E单位阵_2_e_22 ),
    .select(\_1000_只在第一个上升沿之前为1 ), ._11_3(\选_3__11_3 ), ._12_3(\选_3__12_3 ), ._21_3(\选_3__21_3 ),
    ._22_3(\选_3__22_3 ));
  \控制存N判断N使能AS  _0110 (.N(N), .clk(clk), .\N是否为1以上 (\_0110_n是否为1以上 ), .\N最低位是否为1 (\_0110_n最低位是否为1 ));
  \CombLogic_Reg但是4个数  \A寄存器  (
    .a11(\选_2__11_3 ), .a12(\选_2__12_3 ), .a21(\选_2__21_3 ), .a22(\选_2__22_3 ), .enable(_1110), .clk(clk),
    .a11_2(_1), .a12_2(_2), .a21_2(_3), .a22_2(_4));
  \CombLogic_Reg但是4个数  \S寄存器  (
    .a11(\选_3__11_3 ), .a12(\选_3__12_3 ), .a21(\选_3__21_3 ), .a22(\选_3__22_3 ), .enable(_1110), .clk(clk),
    .a11_2(_1_prime), .a12_2(_2_prime), .a21_2(_3_prime), .a22_2(_4_prime));
  or or_1 (_1110, \_1000_只在第一个上升沿之前为1 , \_0110_n是否为1以上 );
  Multiplexer #(.width(32), .enable("false")) multiplexer_1 (.in0(_2_prime), .in1({32{1'b0}}), .out(Nth), .sel(_1110));
endmodule

module \控制存N判断N使能AS  (
  input  [31:0] N,
  input  clk,
  output \N是否为1以上 ,
  output \N最低位是否为1 
);

  wire comparator_1_eq, \n1t高电平_第一个上升沿后为0的初始化控制器_1_只在第一个上升沿之前为1 ;
  wire [31:0] multiplexer_1_out, \N右移 , \N当前状态 ;

  Multiplexer #(.width(32), .enable("false")) multiplexer_1 (
    .in0(\N右移 ), .in1(N), .out(multiplexer_1_out), .sel(\n1t高电平_第一个上升沿后为0的初始化控制器_1_只在第一个上升沿之前为1 ));
  \_1T高电平_第一个上升沿后为0的初始化控制器  \u_1t高电平_第一个上升沿后为0的初始化控制器_1  (
    .clk(clk), .\只在第一个上升沿之前为1 (\n1t高电平_第一个上升沿后为0的初始化控制器_1_只在第一个上升沿之前为1 ));
  Register #(.width(32)) \u_存N和N逻辑右移  (.D(multiplexer_1_out), .Q(\N当前状态 ));  // open: en, clk, clr
  Shifter #(.width(32), .shift("lr")) shifter_1 (.in(\N当前状态 ), .\dist (5'b00001), .out(\N右移 ));
  Comparator #(.width(32), .mode("unsigned")) comparator_1 (
    .a(\N当前状态 ), .b({32{1'b0}}), .eq(comparator_1_eq));  // open: gt, lt
  not not_1 (\N是否为1以上 , comparator_1_eq);
  Bit_Extender #(.in_width(32), .out_width(1)) bit_extender_1 (.in(\N当前状态 ), .out(\N最低位是否为1 ));

  // Notes on the sheet:
  //   循环控制：输入N=100，第一个上升沿后存入Reg，等于0时候直接输出S12作为结果
endmodule

module \_1T高电平_第一个上升沿后为0的初始化控制器  (
  input  clk,
  output \只在第一个上升沿之前为1 
);

  wire counter_1_q;

  Counter #(.width(1), .max('h1), .ongoal("stay")) counter_1 (
    .Q(counter_1_q), .clk(clk));  // open: load, D, count, carry, clr
  Comparator #(.width(1), .mode("unsigned")) comparator_1 (
    .a(counter_1_q), .b(1'b1), .lt(\只在第一个上升沿之前为1 ));  // open: gt, eq
endmodule

module \CombLogic_Reg但是4个数  (
  input  [31:0] a11,
  input  [31:0] a12,
  input  [31:0] a21,
  input  [31:0] a22,
  input  enable,
  input  clk,
  output [31:0] a11_2,
  output [31:0] a12_2,
  output [31:0] a21_2,
  output [31:0] a22_2
);

  Register #(.width(32)) register_1 (.D(a11), .en(enable), .Q(a11_2), .clk(clk));  // open: clr
  Register #(.width(32)) register_2 (.D(a12), .en(enable), .Q(a12_2), .clk(clk));  // open: clr
  Register #(.width(32)) register_3 (.D(a21), .en(enable), .Q(a21_2), .clk(clk));  // open: clr
  Register #(.width(32)) register_4 (.D(a22), .en(enable), .Q(a22_2), .clk(clk));  // open: clr
endmodule

module \CombLogic_矩阵乘法  (
  input  [31:0] x_11,
  input  [31:0] x_12,
  input  [31:0] x_21,
  input  [31:0] x_22,
  input  [31:0] y_11,
  input  [31:0] y_12,
  input  [31:0] y_21,
  input  [31:0] y_22,
  output [31:0] result_11,
  output [31:0] result_12,
  output [31:0] result_21,
  output [31:0] result_22
);

  wire [31:0] multiplier_1_out, multiplier_2_out, multiplier_3_out, multiplier_4_out, multiplier_5_out,
       multiplier_6_out, multiplier_7_out, multiplier_8_out;

  Multiplier #(.width(32)) multiplier_1 (.a(x_11), .b(y_11), .out(multiplier_1_out));  // open: cin, cout
  Multiplier #(.width(32)) multiplier_2 (.a(x_12), .b(y_21), .out(multiplier_2_out));  // open: cin, cout
  Multiplier #(.width(32)) multiplier_3 (.a(x_11), .b(y_12), .out(multiplier_3_out));  // open: cin, cout
  Multiplier #(.width(32)) multiplier_4 (.a(x_12), .b(y_22), .out(multiplier_4_out));  // open: cin, cout
  Multiplier #(.width(32)) multiplier_5 (.a(x_21), .b(y_11), .out(multiplier_5_out));  // open: cin, cout
  Multiplier #(.width(32)) multiplier_6 (.a(x_22), .b(y_21), .out(multiplier_6_out));  // open: cin, cout
  Multiplier #(.width(32)) multiplier_7 (.a(x_21), .b(y_12), .out(multiplier_7_out));  // open: cin, cout
  Multiplier #(.width(32)) multiplier_8 (.a(x_22), .b(y_22), .out(multiplier_8_out));  // open: cin, cout
  Adder #(.width(32)) adder_1 (.a(multiplier_1_out), .b(multiplier_2_out), .out(result_11));  // open: cin, cout
  Adder #(.width(32)) adder_2 (.a(multiplier_3_out), .b(multiplier_4_out), .out(result_12));  // open: cin, cout
  Adder #(.width(32)) adder_3 (.a(multiplier_5_out), .b(multiplier_6_out), .out(result_21));  // open: cin, cout
  Adder #(.width(32)) adder_4 (.a(multiplier_7_out), .b(multiplier_8_out), .out(result_22));  // open: cin, cout
endmodule

module \CombLogic_A初始化矩阵  (
  output [31:0] a_11,
  output [31:0] a_12,
  output [31:0] a_21,
  output [31:0] a_22
);


  assign a_11 = 32'h1;
  assign a_12 = 32'h1;
  assign a_21 = 32'h1;
  assign a_22 = {32{1'b0}};
endmodule

module \CombLogic_E单位阵  (
  output [31:0] E_11,
  output [31:0] E_12,
  output [31:0] E_21,
  output [31:0] E_22
);


  assign E_11 = 32'h1;
  assign E_12 = {32{1'b0}};
  assign E_21 = {32{1'b0}};
  assign E_22 = 32'h1;
endmodule

module \CombLogic_4个数同时选择  (
  input  [31:0] _11,
  input  [31:0] _12,
  input  [31:0] _21,
  input  [31:0] _22,
  input  [31:0] _11_2,
  input  [31:0] _12_2,
  input  [31:0] _21_2,
  input  [31:0] _22_2,
  input  select,
  output [31:0] _11_3,
  output [31:0] _12_3,
  output [31:0] _21_3,
  output [31:0] _22_3
);

  Multiplexer #(.width(32), .enable("false")) multiplexer_1 (.in0(_11), .in1(_11_2), .out(_11_3), .sel(select));
  Multiplexer #(.width(32), .enable("false")) multiplexer_2 (.in0(_12), .in1(_12_2), .out(_12_3), .sel(select));
  Multiplexer #(.width(32), .enable("false")) multiplexer_3 (.in0(_21), .in1(_21_2), .out(_21_3), .sel(select));
  Multiplexer #(.width(32), .enable("false")) multiplexer_4 (.in0(_22), .in1(_22_2), .out(_22_3), .sel(select));
endmodule
