// Logisim project 27位U寻找高位1.circ as structural Verilog: 5 circuits, main circuit main
module main (
  input  [31:0] \input ,
  output [31:0] out_2
);

  wire \情况分类__25 , \情况分类__26 , \情况分类__27 ;
  wire [4:0] bitfinder_1_index;
  wire [26:0] \_25到0情况_out_3 , \_26到0情况_out_3 , \小于等于24到0情况_out_4 ;

  BitFinder #(.width(32), .\type ("high1")) bitfinder_1 (.in(\input ), .index(bitfinder_1_index));  // open: found
  Subtractor #(.width(5)) subtractor_1 (.a(bitfinder_1_index), .b(5'b00101), .out(out_2[4:0]));  // open: bin, bout
  // Probe on \input 
  // Probe on out_2[4:0]
  // Probe on out_2
  \情况分类_27_26_小于等于25  \u_情况分类  (.\最高位1 (out_2[4:0]), ._27(\情况分类__27 ), ._26(\情况分类__26 ), ._25(\情况分类__25 ));
  \_26到0情况  \_26到0情况  (.inputRaw(\input ), .enable(\情况分类__27 ), .out_3(\_26到0情况_out_3 ));
  \_25到0情况  \_25到0情况  (.inputRaw(\input ), .enable(\情况分类__26 ), .out_3(\_25到0情况_out_3 ));
  \小于等于24到0情况  \u_小于等于24到0情况  (
    .inputRaw(\input ), .\起始位置 (out_2[4:0]), .enable(\情况分类__25 ), .out_4(\小于等于24到0情况_out_4 ));
  assign out_2[31:5] = \_26到0情况_out_3  | \_25到0情况_out_3  | \小于等于24到0情况_out_4 ;  // OR_Gate or_1, 27 bits wide

  // Other names for the same wires on the sheet: U起始位置[4:0] = out_2[4:0]
endmodule

module \情况分类_27_26_小于等于25  (
  input  [4:0] \最高位1 ,
  output _27,
  output _26,
  output _25
);

  Comparator #(.width(5), .mode("unsigned")) comparator_1 (.a(\最高位1 ), .b(5'b11010), .eq(_27));  // open: gt, lt
  Comparator #(.width(5), .mode("unsigned")) comparator_2 (.a(\最高位1 ), .b(5'b11001), .eq(_26));  // open: gt, lt
  nor nor_1 (_25, _27, _26);
endmodule

module \_26到0情况  (
  input  [31:0] inputRaw,
  input  enable,
  output [26:0] out_3
);

  wire [26:0] bit_extender_1_out;

  Multiplexer #(.width(27), .enable("false")) multiplexer_1 (
    .in0({27{1'b0}}), .in1(bit_extender_1_out), .out(out_3), .sel(enable));
  Bit_Extender #(.in_width(32), .out_width(27)) bit_extender_1 (.in(inputRaw), .out(bit_extender_1_out));
endmodule

module \_25到0情况  (
  input  [31:0] inputRaw,
  input  enable,
  output [26:0] out_3
);

  wire [25:0] bit_extender_1_out;

  Multiplexer #(.width(27), .enable("false")) multiplexer_1 (
    .in0({27{1'b0}}), .in1({bit_extender_1_out, 1'b1}), .out(out_3), .sel(enable));
  Bit_Extender #(.in_width(32), .out_width(26)) bit_extender_1 (.in(inputRaw), .out(bit_extender_1_out));
endmodule

module \小于等于24到0情况  (
  input  [31:0] inputRaw,
  input  [4:0] \起始位置 ,
  input  enable,
  output [26:0] out_4
);

  wire [4:0] subtractor_1_out, subtractor_2_out;
  wire [31:0] \_1左移结果 , \U左移结果 , \拼接结果 ;

  Subtractor #(.width(5)) subtractor_1 (.a({5{1'b1}}), .b(\起始位置 ), .out(subtractor_1_out));  // open: bin, bout
  Subtractor #(.width(5)) subtractor_2 (.a(5'b11110), .b(\起始位置 ), .out(subtractor_2_out));  // open: bin, bout
  Shifter #(.width(32)) shifter_1 (.in(inputRaw), .\dist (subtractor_1_out), .out(\U左移结果 ));
  Shifter #(.width(32)) shifter_2 (.in(32'h1), .\dist (subtractor_2_out), .out(\_1左移结果 ));
  Adder #(.width(32)) adder_1 (.a(\U左移结果 ), .b(\_1左移结果 ), .out(\拼接结果 ));  // open: cin, cout
  // Probe on \U左移结果 
  // Probe on \_1左移结果 
  // Probe on \拼接结果 
  Multiplexer #(.width(27), .enable("false")) multiplexer_1 (
    .in0({27{1'b0}}), .in1(\拼接结果 [31:5]), .out(out_4), .sel(enable));

  // Other names for the same wires on the sheet: input[31:0] = inputRaw; shmat[4:0] = \起始位置 
endmodule
