// Logisim project CombLogic_5计算分数.circ as structural Verilog: 2 circuits, main circuit main
module main (
  input  [2:0] tea,
  input  [1:0] s1,
  input  [1:0] s2,
  output [3:0] total
);

  wire comparator_1_eq;
  wire [3:0] sum3bit2bit2bit_1_out;

  sum3bit2bit2bit sum3bit2bit2bit_1 (.tea(tea), .s1(s1), .s2(s2), .out(sum3bit2bit2bit_1_out));
  Comparator #(.width(3), .mode("unsigned")) comparator_1 (.a(tea), .b(3'b000), .eq(comparator_1_eq));  // open: gt, lt
  Multiplexer #(.width(4), .enable("false")) multiplexer_1 (
    .in0(sum3bit2bit2bit_1_out), .in1(4'b0000), .out(total), .sel(comparator_1_eq));
endmodule

module sum3bit2bit2bit (
  input  [2:0] tea,
  input  [1:0] s1,
  input  [1:0] s2,
  output [3:0] out
);

  wire [3:0] adder_1_out, bit_extender_1_out, bit_extender_2_out, bit_extender_3_out;

  assign bit_extender_1_out = {{1{1'b0}}, tea};  // Bit_Extender bit_extender_1
  assign bit_extender_2_out = {{2{1'b0}}, s1};  // Bit_Extender bit_extender_2
  assign bit_extender_3_out = {{2{1'b0}}, s2};  // Bit_Extender bit_extender_3
  Adder #(.width(4)) adder_1 (.a(bit_extender_1_out), .b(bit_extender_2_out), .out(adder_1_out));  // open: cin, cout
  Adder #(.width(4)) adder_2 (.a(adder_1_out), .b(bit_extender_3_out), .out(out));  // open: cin, cout
endmodule
