// Logisim project 2的n次幂mod5.circ as structural Verilog: 3 circuits, main circuit mod5
module mod5 (
  input  in,
  output s0,
  output s1,
  output s2,
  output s3,
  output s4
);

  wire clock_1_out;
  wire [1:0] \状态寄存器_s , \组合逻辑_ns0 ;

  \状态寄存器  \u_状态寄存器  (.ns(\组合逻辑_ns0 ), .clk(clock_1_out), .s(\状态寄存器_s ));
  Clock clock_1 (.out(clock_1_out));
  \组合逻辑  \u_组合逻辑  (
    .s1(\状态寄存器_s [1]), .s0(\状态寄存器_s [0]), .in(in), .ns1(\组合逻辑_ns0 [1]), .ns0(\组合逻辑_ns0 [0]), .op4(s4),
    .op3(s3), .op2(s2), .op1(s1), .op0(s0));

  // Other names for the same wires on the sheet: _0 = s0; _1 = s1; _2 = s2; _3 = s3; _4 = s4
endmodule

module \状态寄存器  (
  input  [1:0] ns,
  input  clk,
  output [1:0] s
);

  Register #(.width(2)) register_1 (.D(ns), .Q(s), .clk(clk));  // open: en, clr
endmodule

module \组合逻辑  (
  input  s1,
  input  s0,
  input  in,
  output ns1,
  output ns0,
  output op4,
  output op3,
  output op2,
  output op1,
  output op0
);

  wire not_1_out, not_2_out, not_3_out, not_4_out;

  not not_1 (not_1_out, in);
  and and_1 (op3, s0, in);
  not not_2 (not_2_out, s0);
  not not_3 (not_3_out, s0);
  not not_4 (not_4_out, in);
  and and_2 (op4, s0, not_1_out);
  and and_3 (op2, not_2_out, in);
  and and_4 (op1, not_3_out, not_4_out);

  assign ns0 = in;
  assign ns1 = s0;
  assign op0 = 1'b0;
endmodule
