// Logisim project 字符串匹配.circ as structural Verilog: 3 circuits, main circuit fsm
module fsm (
  input  CLR,
  input  [1:0] in,
  output out
);

  wire clock_1_out;
  wire [1:0] \状态寄存器_s , \组合逻辑_ns0 ;

  \状态寄存器  \u_状态寄存器  (.ns(\组合逻辑_ns0 ), .rst(CLR), .clk(clock_1_out), .s(\状态寄存器_s ));
  Clock clock_1 (.out(clock_1_out));
  // Probe on \状态寄存器_s 
  // Probe on in
  \组合逻辑  \u_组合逻辑  (
    .s1(\状态寄存器_s [1]), .s0(\状态寄存器_s [0]), .in1(in[1]), .in0(in[0]), .ns1(\组合逻辑_ns0 [1]), .ns0(\组合逻辑_ns0 [0]),
    .out(out));
  // Probe on out
endmodule

module \组合逻辑  (
  input  s1,
  input  s0,
  input  in1,
  input  in0,
  output ns1,
  output ns0,
  output out
);

  wire not_1_out, not_2_out, not_3_out;

  and and_1 (ns1, s0, not_1_out);
  not not_1 (not_1_out, in0);
  not not_2 (not_2_out, in1);
  and and_2 (ns0, not_2_out, in0);
  and and_3 (out, s1, not_3_out);
  not not_3 (not_3_out, in0);
endmodule

module \状态寄存器  (
  input  [1:0] ns,
  input  rst,
  input  clk,
  output [1:0] s
);

  wire [1:0] multiplexer_1_out;

  Multiplexer #(.width(2), .enable("false")) multiplexer_1 (.in0(ns), .in1(2'b00), .out(multiplexer_1_out), .sel(rst));
  Register #(.width(2)) register_1 (.D(multiplexer_1_out), .Q(s), .clk(clk));  // open: en, clr
endmodule
