// Logisim project A走B教室.circ as structural Verilog: 4 circuits, main circuit navigation
module navigation (
  input  [1:0] dir,
  input  clk,
  input  rst,
  output arrive,
  output hit
);

  wire \组合逻辑_nhit ;
  wire [2:0] \状态寄存器_s , \组合逻辑_ns0 ;

  // Probe on \状态寄存器_s 
  // Probe on dir
  // Probe on arrive
  // Probe on hit
  \状态寄存器_输出  \u_状态寄存器  (.ns(\组合逻辑_ns0 ), .clk(clk), .rst(rst), .s(\状态寄存器_s ), .arrive(arrive));
  \组合逻辑  \u_组合逻辑  (
    .s2(\状态寄存器_s [2]), .s1(\状态寄存器_s [1]), .s0(\状态寄存器_s [0]), .in1(dir[1]), .in0(dir[0]), .ns2(\组合逻辑_ns0 [2]),
    .ns1(\组合逻辑_ns0 [1]), .ns0(\组合逻辑_ns0 [0]), .nhit(\组合逻辑_nhit ));
  \hit寄存器  hit_2 (.nh(\组合逻辑_nhit ), .clk(clk), .rst(rst), .h(hit));
endmodule

module \状态寄存器_输出  (
  input  [2:0] ns,
  input  clk,
  input  rst,
  output [2:0] s,
  output arrive
);

  Register #(.width(3)) \u_状态寄存器  (.D(ns), .Q(s), .clk(clk), .clr(rst));  // open: en
  Comparator #(.width(3), .mode("unsigned")) comparator_1 (.a(s), .b(3'b100), .eq(arrive));  // open: gt, lt
endmodule

module \组合逻辑  (
  input  s2,
  input  s1,
  input  s0,
  input  in1,
  input  in0,
  output ns2,
  output ns1,
  output ns0,
  output nhit
);

  wire and_1_out, and_2_out, and_3_out, and_4_out, and_5_out, and_6_out, and_7_out, and_8_out, and_9_out,
       and_10_out, and_11_out, and_12_out, and_13_out, and_14_out, and_15_out, and_16_out, not_1_out,
       not_2_out, not_3_out, not_4_out, not_5_out, not_6_out, not_7_out, not_8_out, not_9_out, not_10_out,
       not_11_out, not_12_out, not_13_out, not_14_out, not_15_out, not_16_out, not_17_out, not_18_out,
       not_19_out, not_20_out, not_21_out, not_22_out, not_23_out, not_24_out, not_25_out, not_26_out,
       not_27_out, not_28_out;

  not not_1 (not_1_out, s0);
  not not_2 (not_2_out, in1);
  not not_3 (not_3_out, in0);
  not not_4 (not_4_out, in1);
  not not_5 (not_5_out, s1);
  not not_6 (not_6_out, in1);
  not not_7 (not_7_out, in1);
  not not_8 (not_8_out, in0);
  not not_9 (not_9_out, s0);
  not not_10 (not_10_out, in1);
  not not_11 (not_11_out, s0);
  not not_12 (not_12_out, in0);
  not not_13 (not_13_out, s2);
  not not_14 (not_14_out, s1);
  not not_15 (not_15_out, in1);
  not not_16 (not_16_out, in0);
  not not_17 (not_17_out, in0);
  not not_18 (not_18_out, s2);
  not not_19 (not_19_out, s0);
  not not_20 (not_20_out, in1);
  not not_21 (not_21_out, s2);
  not not_22 (not_22_out, s1);
  not not_23 (not_23_out, s0);
  not not_24 (not_24_out, s2);
  not not_25 (not_25_out, s0);
  not not_26 (not_26_out, in0);
  not not_27 (not_27_out, in1);
  not not_28 (not_28_out, in0);
  and and_1 (and_1_out, s1, not_1_out, not_2_out, not_3_out);
  and and_2 (and_2_out, s1, s0, not_4_out, in0);
  and and_3 (and_3_out, not_5_out, s0, not_6_out);
  and and_4 (and_4_out, s0, not_7_out, not_8_out);
  and and_5 (and_5_out, s1, not_9_out, not_10_out, in0);
  and and_6 (and_6_out, s1, not_11_out, in1, not_12_out);
  and and_7 (and_7_out, s1, s0, in1, in0);
  and and_8 (and_8_out, not_13_out, not_14_out, not_15_out, not_16_out);
  and and_9 (and_9_out, s0, in1, in0);
  and and_10 (and_10_out, s1, in1, in0);
  and and_11 (and_11_out, s1, s0, not_17_out);
  and and_12 (and_12_out, not_18_out, not_19_out, not_20_out, in0);
  and and_13 (and_13_out, not_21_out, not_22_out, not_23_out, in1);
  and and_14 (and_14_out, not_24_out, not_25_out, in1, not_26_out);
  and and_15 (and_15_out, s0, in1, in0);
  and and_16 (and_16_out, s1, s0, not_27_out, not_28_out);
  or or_1 (ns2, and_1_out, and_2_out);
  or or_2 (ns1, and_3_out, and_4_out, and_5_out, and_6_out, and_7_out);
  or or_3 (ns0, and_8_out, and_9_out, and_10_out, and_11_out);
  or or_4 (nhit, and_12_out, and_13_out, and_14_out, and_15_out, and_16_out);
endmodule

module \hit寄存器  (
  input  nh,
  input  clk,
  input  rst,
  output h
);

  Register #(.width(1)) register_1 (.D(nh), .Q(h), .clk(clk), .clr(rst));  // open: en
endmodule
