// Logisim project 斐波那契.circ as structural Verilog: 3 circuits, main circuit main
module main (
  input  [2:0] N,
  output [3:0] Nth
);

  wire clock_1_out, enable;
  wire [3:0] \Fn计算_fn ;

  Clock clock_1 (.out(clock_1_out));
  \循环次数控制  \u_循环控制  (.N(N), .clk(clock_1_out), .enable(enable));
  // Probe on \Fn计算_fn 
  \Fn计算  \Fn计算  (.enable(enable), .clk(clock_1_out), .Fn(\Fn计算_fn ));
  Multiplexer #(.width(4), .enable("false")) multiplexer_1 (.in0(\Fn计算_fn ), .in1(4'b0000), .out(Nth), .sel(enable));
endmodule

module \Fn计算  (
  input  enable,
  input  clk,
  output [3:0] Fn
);

  wire counter_1_q;
  wire [3:0] adder_1_out, Fn_1, multiplexer_1_out;

  Multiplexer #(.width(4), .enable("false")) multiplexer_1 (
    .in0(4'b0001), .in1(Fn), .out(multiplexer_1_out), .sel(counter_1_q));
  Counter #(.width(1), .max('h1), .ongoal("stay")) counter_1 (
    .Q(counter_1_q), .clk(clk));  // open: load, D, count, carry, clr
  Adder #(.width(4)) adder_1 (.a(Fn_1), .b(Fn), .out(adder_1_out));  // open: cin, cout
  Register #(.width(4)) u_Fn_1 (.D(multiplexer_1_out), .en(enable), .Q(Fn_1), .clk(clk));  // open: clr
  Register #(.width(4)) u_Fn (.D(adder_1_out), .en(enable), .Q(Fn), .clk(clk));  // open: clr
endmodule

module \循环次数控制  (
  input  [2:0] N,
  input  clk,
  output enable
);

  wire [3:0] adder_1_out, bit_extender_1_out, counter_1_q;

  Counter #(.width(4), .max('hf), .ongoal("stay")) counter_1 (
    .Q(counter_1_q), .clk(clk));  // open: load, D, count, carry, clr
  assign bit_extender_1_out = {{1{1'b0}}, N};  // Bit_Extender bit_extender_1
  Adder #(.width(4)) adder_1 (.a(bit_extender_1_out), .b(4'b0001), .out(adder_1_out));  // open: cin, cout
  Comparator #(.width(4)) comparator_1 (.a(counter_1_q), .b(adder_1_out), .lt(enable));  // open: gt, eq
endmodule
