// Logisim project L2.circ as structural Verilog: 8 circuits, main circuit main
module main (
  input  [7:0] in1,
  input  [7:0] in2,
  input  [7:0] in3,
  input  [7:0] in4,
  input  [7:0] in5,
  output [7:0] out
);

  wire exist1_1_out, exist2_1_out, exist3_1_out, exist4_1_out, exist5_1_out;
  wire [2:0] choice_1_o0;

  exist1 exist1_1 (.in1(in1), .in1_2(in2), .in1_3(in3), .in1_4(in4), .in1_5(in5), .out(exist1_1_out));
  exist2 exist2_1 (.in1(in1), .in1_2(in2), .in1_3(in3), .in1_4(in4), .in1_5(in5), .out(exist2_1_out));
  exist3 exist3_1 (.in1(in1), .in1_2(in2), .in1_3(in3), .in1_4(in4), .in1_5(in5), .out(exist3_1_out));
  exist4 exist4_1 (.in1(in1), .in1_2(in2), .in1_3(in3), .in1_4(in4), .in1_5(in5), .out(exist4_1_out));
  exist5 exist5_1 (.in1(in1), .in1_2(in2), .in1_3(in3), .in1_4(in4), .in1_5(in5), .out(exist5_1_out));
  choice choice_1 (
    .is1(exist1_1_out), .is2(exist2_1_out), .is3(exist3_1_out), .is4(exist4_1_out), .is5(exist5_1_out),
    .o2(choice_1_o0[2]), .o1(choice_1_o0[1]), .o0(choice_1_o0[0]));
  assign out = {{5{1'b0}}, choice_1_o0};  // Bit_Extender bit_extender_1

  // Other names for the same wires on the sheet: _1[7:0] = in1; _2[7:0] = in2; _3[7:0] = in3; _4[7:0] = in4;
  //   _5[7:0] = in5
endmodule

module exist1 (
  input  [7:0] in1,
  input  [7:0] in1_2,
  input  [7:0] in1_3,
  input  [7:0] in1_4,
  input  [7:0] in1_5,
  output out
);

  wire comparator_1_eq, comparator_2_eq, comparator_3_eq, comparator_4_eq, comparator_5_eq;

  Comparator #(.mode("unsigned")) comparator_1 (.a(8'h1), .b(in1), .eq(comparator_1_eq));  // open: gt, lt
  Comparator #(.mode("unsigned")) comparator_2 (.a(8'h1), .b(in1_2), .eq(comparator_2_eq));  // open: gt, lt
  Comparator #(.mode("unsigned")) comparator_3 (.a(8'h1), .b(in1_3), .eq(comparator_3_eq));  // open: gt, lt
  Comparator #(.mode("unsigned")) comparator_4 (.a(8'h1), .b(in1_4), .eq(comparator_4_eq));  // open: gt, lt
  Comparator #(.mode("unsigned")) comparator_5 (.a(8'h1), .b(in1_5), .eq(comparator_5_eq));  // open: gt, lt
  or or_1 (out, comparator_1_eq, comparator_2_eq, comparator_3_eq, comparator_4_eq, comparator_5_eq);
endmodule

module exist2 (
  input  [7:0] in1,
  input  [7:0] in1_2,
  input  [7:0] in1_3,
  input  [7:0] in1_4,
  input  [7:0] in1_5,
  output out
);

  wire comparator_1_eq, comparator_2_eq, comparator_3_eq, comparator_4_eq, comparator_5_eq;

  Comparator #(.mode("unsigned")) comparator_1 (.a(8'h2), .b(in1), .eq(comparator_1_eq));  // open: gt, lt
  Comparator #(.mode("unsigned")) comparator_2 (.a(8'h2), .b(in1_2), .eq(comparator_2_eq));  // open: gt, lt
  Comparator #(.mode("unsigned")) comparator_3 (.a(8'h2), .b(in1_3), .eq(comparator_3_eq));  // open: gt, lt
  Comparator #(.mode("unsigned")) comparator_4 (.a(8'h2), .b(in1_4), .eq(comparator_4_eq));  // open: gt, lt
  Comparator #(.mode("unsigned")) comparator_5 (.a(8'h2), .b(in1_5), .eq(comparator_5_eq));  // open: gt, lt
  or or_1 (out, comparator_1_eq, comparator_2_eq, comparator_3_eq, comparator_4_eq, comparator_5_eq);
endmodule

module exist3 (
  input  [7:0] in1,
  input  [7:0] in1_2,
  input  [7:0] in1_3,
  input  [7:0] in1_4,
  input  [7:0] in1_5,
  output out
);

  wire comparator_1_eq, comparator_2_eq, comparator_3_eq, comparator_4_eq, comparator_5_eq;

  Comparator #(.mode("unsigned")) comparator_1 (.a(8'h3), .b(in1), .eq(comparator_1_eq));  // open: gt, lt
  Comparator #(.mode("unsigned")) comparator_2 (.a(8'h3), .b(in1_2), .eq(comparator_2_eq));  // open: gt, lt
  Comparator #(.mode("unsigned")) comparator_3 (.a(8'h3), .b(in1_3), .eq(comparator_3_eq));  // open: gt, lt
  Comparator #(.mode("unsigned")) comparator_4 (.a(8'h3), .b(in1_4), .eq(comparator_4_eq));  // open: gt, lt
  Comparator #(.mode("unsigned")) comparator_5 (.a(8'h3), .b(in1_5), .eq(comparator_5_eq));  // open: gt, lt
  or or_1 (out, comparator_1_eq, comparator_2_eq, comparator_3_eq, comparator_4_eq, comparator_5_eq);
endmodule

module exist4 (
  input  [7:0] in1,
  input  [7:0] in1_2,
  input  [7:0] in1_3,
  input  [7:0] in1_4,
  input  [7:0] in1_5,
  output out
);

  wire comparator_1_eq, comparator_2_eq, comparator_3_eq, comparator_4_eq, comparator_5_eq;

  Comparator #(.mode("unsigned")) comparator_1 (.a(8'h4), .b(in1), .eq(comparator_1_eq));  // open: gt, lt
  Comparator #(.mode("unsigned")) comparator_2 (.a(8'h4), .b(in1_2), .eq(comparator_2_eq));  // open: gt, lt
  Comparator #(.mode("unsigned")) comparator_3 (.a(8'h4), .b(in1_3), .eq(comparator_3_eq));  // open: gt, lt
  Comparator #(.mode("unsigned")) comparator_4 (.a(8'h4), .b(in1_4), .eq(comparator_4_eq));  // open: gt, lt
  Comparator #(.mode("unsigned")) comparator_5 (.a(8'h4), .b(in1_5), .eq(comparator_5_eq));  // open: gt, lt
  or or_1 (out, comparator_1_eq, comparator_2_eq, comparator_3_eq, comparator_4_eq, comparator_5_eq);
endmodule

module exist5 (
  input  [7:0] in1,
  input  [7:0] in1_2,
  input  [7:0] in1_3,
  input  [7:0] in1_4,
  input  [7:0] in1_5,
  output out
);

  wire comparator_1_eq, comparator_2_eq, comparator_3_eq, comparator_4_eq, comparator_5_eq;

  Comparator #(.mode("unsigned")) comparator_1 (.a(8'h5), .b(in1), .eq(comparator_1_eq));  // open: gt, lt
  Comparator #(.mode("unsigned")) comparator_2 (.a(8'h5), .b(in1_2), .eq(comparator_2_eq));  // open: gt, lt
  Comparator #(.mode("unsigned")) comparator_3 (.a(8'h5), .b(in1_3), .eq(comparator_3_eq));  // open: gt, lt
  Comparator #(.mode("unsigned")) comparator_4 (.a(8'h5), .b(in1_4), .eq(comparator_4_eq));  // open: gt, lt
  Comparator #(.mode("unsigned")) comparator_5 (.a(8'h5), .b(in1_5), .eq(comparator_5_eq));  // open: gt, lt
  or or_1 (out, comparator_1_eq, comparator_2_eq, comparator_3_eq, comparator_4_eq, comparator_5_eq);
endmodule

module exist6 (
  input  [7:0] in1,
  input  [7:0] in1_2,
  input  [7:0] in1_3,
  input  [7:0] in1_4,
  input  [7:0] in1_5,
  output out
);

  wire comparator_1_eq, comparator_2_eq, comparator_3_eq, comparator_4_eq, comparator_5_eq;

  Comparator #(.mode("unsigned")) comparator_1 (.a(8'h6), .b(in1), .eq(comparator_1_eq));  // open: gt, lt
  Comparator #(.mode("unsigned")) comparator_2 (.a(8'h6), .b(in1_2), .eq(comparator_2_eq));  // open: gt, lt
  Comparator #(.mode("unsigned")) comparator_3 (.a(8'h6), .b(in1_3), .eq(comparator_3_eq));  // open: gt, lt
  Comparator #(.mode("unsigned")) comparator_4 (.a(8'h6), .b(in1_4), .eq(comparator_4_eq));  // open: gt, lt
  Comparator #(.mode("unsigned")) comparator_5 (.a(8'h6), .b(in1_5), .eq(comparator_5_eq));  // open: gt, lt
  or or_1 (out, comparator_1_eq, comparator_2_eq, comparator_3_eq, comparator_4_eq, comparator_5_eq);
endmodule

module choice (
  input  is1,
  input  is2,
  input  is3,
  input  is4,
  input  is5,
  output o2,
  output o1,
  output o0
);

  wire and_2_out, and_3_out, and_4_out, and_5_out, and_6_out, not_1_out, not_2_out, not_3_out, not_4_out,
       not_5_out;

  and and_1 (o2, is1, is2, is3);
  not not_1 (not_1_out, is2);
  not not_2 (not_2_out, is3);
  not not_3 (not_3_out, is3);
  not not_4 (not_4_out, is5);
  and and_2 (and_2_out, is1, not_1_out);
  and and_3 (and_3_out, is1, not_2_out);
  and and_4 (and_4_out, is1, is4, is5);
  not not_5 (not_5_out, is1);
  and and_5 (and_5_out, is2, not_3_out);
  and and_6 (and_6_out, is2, is4, not_4_out);
  or or_1 (o1, and_2_out, and_3_out, and_4_out);
  or or_2 (o0, not_5_out, and_5_out, and_6_out);
endmodule
