// Logisim project L3.circ as structural Verilog: 2 circuits, main circuit main
module main (
  input  [1:0] \input ,
  input  reset,
  input  clk,
  output [3:0] out_4
);

  wire comparator_1_eq;
  wire [3:0] now_state, register_1_q;

  Register #(.width(4)) register_1 (.D(out_4), .Q(register_1_q), .clk(clk), .clr(reset));  // open: en
  comblogic comblogic_1 (
    .s3(now_state[3]), .s2(now_state[2]), .s1(now_state[1]), .s0(now_state[0]), .in1(\input [1]),
    .in0(\input [0]), .s3_2(out_4[3]), .s2_2(out_4[2]), .s1_2(out_4[1]), .s0_2(out_4[0]));
  Comparator #(.width(4), .mode("unsigned")) comparator_1 (
    .a(register_1_q), .b(4'b0000), .eq(comparator_1_eq));  // open: gt, lt
  // Probe on now_state
  // Probe on \input 
  // Probe on out_4
  Multiplexer #(.width(4), .enable("false")) multiplexer_1 (
    .in0(register_1_q), .in1(4'b0001), .out(now_state), .sel(comparator_1_eq));

  // Other names for the same wires on the sheet: next_state[3:0] = out_4; rst = reset
endmodule

module comblogic (
  input  s3,
  input  s2,
  input  s1,
  input  s0,
  input  in1,
  input  in0,
  output s3_2,
  output s2_2,
  output s1_2,
  output s0_2
);

  wire and_1_out, and_2_out, and_3_out, and_4_out, and_5_out, and_6_out, and_7_out, and_8_out, and_9_out,
       and_10_out, and_11_out, and_12_out, and_13_out, and_14_out, and_15_out, and_16_out, and_17_out,
       and_18_out, and_19_out, and_20_out, and_21_out, and_22_out, and_23_out, and_24_out, not_1_out,
       not_2_out, not_3_out, not_4_out, not_5_out, not_6_out, not_7_out, not_8_out, not_9_out, not_10_out,
       not_11_out, not_12_out, not_13_out, not_14_out, not_15_out, not_16_out, not_17_out, not_18_out,
       not_19_out, not_20_out, not_21_out, not_22_out, not_23_out, not_24_out, not_25_out, not_26_out,
       not_27_out, not_28_out, not_29_out, not_30_out, not_31_out, not_32_out, not_33_out, not_34_out,
       not_35_out, not_36_out, not_37_out, not_38_out, not_39_out, not_40_out, not_41_out;

  not not_1 (not_1_out, s3);
  not not_2 (not_2_out, s2);
  not not_3 (not_3_out, s1);
  not not_4 (not_4_out, in0);
  not not_5 (not_5_out, in1);
  not not_6 (not_6_out, s1);
  not not_7 (not_7_out, s0);
  not not_8 (not_8_out, in0);
  not not_9 (not_9_out, in0);
  not not_10 (not_10_out, in1);
  not not_11 (not_11_out, s1);
  not not_12 (not_12_out, s0);
  not not_13 (not_13_out, s3);
  not not_14 (not_14_out, s2);
  not not_15 (not_15_out, in1);
  not not_16 (not_16_out, s3);
  not not_17 (not_17_out, s0);
  not not_18 (not_18_out, s2);
  not not_19 (not_19_out, s0);
  not not_20 (not_20_out, in1);
  not not_21 (not_21_out, in1);
  not not_22 (not_22_out, in0);
  not not_23 (not_23_out, in0);
  not not_24 (not_24_out, in0);
  not not_25 (not_25_out, s3);
  not not_26 (not_26_out, s2);
  not not_27 (not_27_out, s1);
  not not_28 (not_28_out, in1);
  not not_29 (not_29_out, in0);
  not not_30 (not_30_out, s1);
  not not_31 (not_31_out, s0);
  not not_32 (not_32_out, s2);
  not not_33 (not_33_out, s1);
  not not_34 (not_34_out, s0);
  not not_35 (not_35_out, in1);
  not not_36 (not_36_out, s2);
  not not_37 (not_37_out, s1);
  not not_38 (not_38_out, in0);
  not not_39 (not_39_out, s1);
  not not_40 (not_40_out, in1);
  not not_41 (not_41_out, in0);
  and and_1 (and_1_out, not_1_out, not_2_out, not_3_out, in1, not_4_out);
  and and_2 (and_2_out, s2, s1, s0, in1, in0);
  and and_3 (and_3_out, s3, not_5_out);
  and and_4 (and_4_out, not_6_out, not_7_out, in1, not_8_out);
  and and_5 (and_5_out, s1, s0, in1, not_9_out);
  and and_6 (and_6_out, s2, not_10_out);
  and and_7 (and_7_out, s2, not_11_out, s0);
  and and_8 (and_8_out, s2, s1, not_12_out);
  and and_9 (and_9_out, not_13_out, not_14_out, not_15_out, in0);
  and and_10 (and_10_out, not_16_out, not_17_out, in1, in0);
  and and_11 (and_11_out, not_18_out, s1, in0);
  and and_12 (and_12_out, s1, not_19_out, in1);
  and and_13 (and_13_out, s1, s0, not_20_out);
  and and_14 (and_14_out, s2, s0, not_21_out, not_22_out);
  and and_15 (and_15_out, s2, s1, not_23_out);
  and and_16 (and_16_out, s3, in1, not_24_out);
  and and_17 (and_17_out, not_25_out, not_26_out, not_27_out, not_28_out, not_29_out);
  and and_18 (and_18_out, not_30_out, not_31_out, in1);
  and and_19 (and_19_out, not_32_out, not_33_out, in1, in0);
  and and_20 (and_20_out, s1, not_34_out, not_35_out);
  and and_21 (and_21_out, not_36_out, s1, s0, in0);
  and and_22 (and_22_out, s2, not_37_out, in1, not_38_out);
  and and_23 (and_23_out, s2, not_39_out, s0, not_40_out, in0);
  and and_24 (and_24_out, s2, s1, s0, not_41_out);
  or or_1 (s3_2, and_1_out, and_2_out, and_3_out);
  or or_2 (s2_2, and_4_out, and_5_out, and_6_out, and_7_out, and_8_out);
  or or_3 (s1_2, and_9_out, and_10_out, and_11_out, and_12_out, and_13_out, and_14_out, and_15_out, and_16_out);
  or or_4 (s0_2, and_17_out, and_18_out, and_19_out, and_20_out, and_21_out, and_22_out, and_23_out, and_24_out);
endmodule
