// Logisim project 4-异步复位单周期-增加指令.circ as structural Verilog: 12 circuits, main circuit main
module main (
  input  rst,
  output [31:0] Instr,
  output [31:0] pc,
  output RegWrite,
  output [4:0] RegAddr,
  output [31:0] RegData,
  output MenWrite,
  output [31:0] MemAddr,
  output [31:0] MemData
);

  wire ALU_B_04, ALU_immExt_05, ALUIsEqual, clk, isBranch_08, isJal_11, isJalr_10, isJOrJal_11,
       isJrOrJalr_09, isLb_13, isSll_12;
  wire [1:0] A3_RdRt_ra_01, GRF_WD_03;
  wire [2:0] ALU_Op_06;
  wire [7:0] multiplexer_1_out;
  wire [31:0] bit_extender_1_out, bit_extender_2_out, DM_lwOrlb, EXT_07_immhasexted, multiplexer_2_out,
       multiplexer_5_out, multiplexer_6_out, NPC, PC_4, RD1;

  Clock clock_1 (.out(clk));
  NPC_03 NPC_03 (
    .PC(pc), .Rs(RD1), .imm(Instr[15:0]), .ins_index(Instr[25:0]), .isJrOrjalr(isJrOrJalr_09),
    .isJOrJal(isJOrJal_11), .isBranch(isBranch_08), .isBranchSuccess(ALUIsEqual), .PC_4(PC_4), .NPC(NPC));
  Multiplexer #(.select(2), .width(8), .enable("false")) multiplexer_1 (
    .in0(DM_lwOrlb[7:0]), .in1(DM_lwOrlb[15:8]), .in2(DM_lwOrlb[23:16]), .in3(DM_lwOrlb[31:24]),
    .out(multiplexer_1_out), .sel(MemAddr[1:0]));
  PC_02 PC_02 (.NPC(NPC), .clk(clk), .rst(rst), .PC(pc));
  assign bit_extender_1_out = {{24{multiplexer_1_out[7]}}, multiplexer_1_out};  // Bit_Extender bit_extender_1
  Multiplexer #(.width(32), .enable("false")) multiplexer_2 (
    .in0(DM_lwOrlb), .in1(bit_extender_1_out), .out(multiplexer_2_out), .sel(isLb_13));
  IM_01 IM_01 (.PC(pc), .Ins(Instr));
  // Probe on GRF_WD_03
  // Probe on NPC
  // Probe on pc
  // Probe on Instr
  // Probe on isJrOrJalr_09
  // Probe on RD1
  Multiplexer #(.select(2), .width(5), .enable("false")) multiplexer_3 (
    .in0(Instr[15:11]), .in1(Instr[20:16]), .in2({5{1'b1}}), .out(RegAddr), .sel(A3_RdRt_ra_01));  // open: in3
  // Probe on A3_RdRt_ra_01
  Multiplexer #(.select(2), .width(32), .enable("false")) multiplexer_4 (
    .in0(MemAddr), .in1(multiplexer_2_out), .in2(PC_4), .out(RegData), .sel(GRF_WD_03));  // open: in3
  Controller_08 controller_08_1 (
    .ins(Instr), .A3_RdRt_ra_01(A3_RdRt_ra_01), .GRF_WE_02(RegWrite), .GRF_WD_03(GRF_WD_03),
    .ALU_B_04(ALU_B_04), .ALU_immExt_05(ALU_immExt_05), .ALU_Op_06(ALU_Op_06), .DM_WE_07(MenWrite),
    .isBranch_08(isBranch_08), .isJrOrJalr_09(isJrOrJalr_09), .isJalr_10(isJalr_10),
    .isJOrJal_11(isJOrJal_11), .isJal_11(isJal_11), .isSll_12(isSll_12), .isLb_13(isLb_13));
  GRF_04 GRF_04 (
    .A1(Instr[25:21]), .A2(Instr[20:16]), .A3(RegAddr), .WD(RegData), .RD1(RD1), .RD2(MemData), .clk(clk),
    .rst(rst), .WE(RegWrite));
  // Probe on ALU_immExt_05
  assign bit_extender_2_out = {{27{1'b0}}, Instr[10:6]};  // Bit_Extender bit_extender_2
  EXT_07 EXT_07 (.imm(Instr[15:0]), .zeroOrSigned(ALU_immExt_05), .immHasExted(EXT_07_immhasexted));
  Multiplexer #(.width(32), .enable("false")) multiplexer_5 (
    .in0(RD1), .in1(bit_extender_2_out), .out(multiplexer_5_out), .sel(isSll_12));
  Multiplexer #(.width(32), .enable("false")) multiplexer_6 (
    .in0(MemData), .in1(EXT_07_immhasexted), .out(multiplexer_6_out), .sel(ALU_B_04));
  ALU_05 ALU_05 (.A(multiplexer_5_out), .B(multiplexer_6_out), .ALUOp(ALU_Op_06), .C(MemAddr), .isEqual(ALUIsEqual));
  // Probe on ALU_Op_06
  DM_06 DM_06 (.A({MemAddr[31:2], 2'b00}), .WD(MemData), .RD(DM_lwOrlb), .WE(MenWrite), .clk(clk), .reset(rst));

  // Other names for the same wires on the sheet: ALUResult[31:0] = MemAddr; A3[4:0] = RegAddr; DM_WE_07 = MenWrite;
  //   GRF_WD[31:0] = RegData; GRF_WE_02 = RegWrite; ins[31:0] = Instr; op[5:0] = Instr[31:26]; func[5:0] = Instr[5:0];
  //   imm[15:0] = Instr[15:0]; ins_index[25:0] = Instr[25:0]; shamt[4:0] = Instr[10:6]; Rd[4:0] = Instr[15:11];
  //   Rt[4:0] = Instr[20:16]; Rs[4:0] = Instr[25:21]; RD2[31:0] = MemData

  // Notes on the sheet:
  //   需要接入clk的模块:
  //   R: sll slt
  //   R: jr jalr
  //   2.PC 4.GRF 6.DM
  //   R: add(addu操作) sub(subu操作) 
  //   R
  //   I
  //   J
  //   R
endmodule

module IM_01 (
  input  [31:0] PC,
  output [31:0] Ins
);

  wire [31:0] subtractor_1_out;

  Subtractor #(.width(32)) subtractor_1 (.a(PC), .b(32'h3000), .out(subtractor_1_out));  // open: bin, bout
  ROM #(.addrWidth(12), .dataWidth(32)) rom_1 (.addr(subtractor_1_out[13:2]), .data(Ins));  // open: sel

  // Notes on the sheet:
  //   输入：PC，用于选择需要ROM中的哪个指令
  //   contents of rom_1 (hex, n*v repeats v):
  //   34040100 34850123 3c0601c8 3c07ffff 34e7ffff 868020 878820 e7a020 869022 879822 ac040000 ac050004
  //   ac060008 ac07000c ac100010 ac110014 ac120018 ac13002c ac140030 8c040000 8c05000c ac04001c ac050020
  //   34040001 34050002 34060001 10850001 10860001 ad040024 ad050028 c000c23 c000c23 ad150040 34a50004
  //   c000c27 ad050038 ad1f003c 36b50005 3e00008 ad050044 ad1f0048
  //   输出：instr，ROM中指令被取出
endmodule

module PC_02 (
  input  [31:0] NPC,
  input  clk,
  input  rst,
  output [31:0] PC
);

  wire comparator_1_eq;
  wire [31:0] PC_q;

  Register #(.width(32)) u_PC (.D(NPC), .Q(PC_q), .clk(clk), .clr(rst));  // open: en
  Multiplexer #(.width(32), .enable("false")) multiplexer_1 (
    .in0(PC_q), .in1(32'h3000), .out(PC), .sel(comparator_1_eq));
  Comparator #(.width(32), .mode("unsigned")) comparator_1 (
    .a(PC_q), .b({32{1'b0}}), .eq(comparator_1_eq));  // open: gt, lt

  // Notes on the sheet:
  //   输入：时钟；异步复位
  //   输入：NPC，下一条指令地址
  //   输出：PC，当前指令地址
endmodule

module NPC_03 (
  input  [31:0] PC,
  input  [31:0] Rs,
  input  [15:0] imm,
  input  [25:0] ins_index,
  input  isJrOrjalr,
  input  isJOrJal,
  input  isBranch,
  input  isBranchSuccess,
  output [31:0] PC_4,
  output [31:0] NPC
);

  wire and_1_out;
  wire [31:0] bit_extender_1_out, \desBranch_b指令 , multiplexer_1_out, multiplexer_2_out;

  assign bit_extender_1_out = {{14{imm[15]}}, {imm, 2'b00}};  // Bit_Extender bit_extender_1
  Adder #(.width(32)) adder_1 (.a(bit_extender_1_out), .b(PC_4), .out(\desBranch_b指令 ));  // open: cin, cout
  Adder #(.width(32)) adder_2 (.a(PC), .b(32'h4), .out(PC_4));  // open: cin, cout
  Multiplexer #(.width(32), .enable("false")) multiplexer_1 (
    .in0(PC_4), .in1(Rs), .out(multiplexer_1_out), .sel(isJrOrjalr));
  Multiplexer #(.width(32), .enable("false")) multiplexer_2 (
    .in0(multiplexer_1_out), .in1(\desBranch_b指令 ), .out(multiplexer_2_out), .sel(and_1_out));
  and and_1 (and_1_out, isBranch, isBranchSuccess);
  Multiplexer #(.width(32), .enable("false")) multiplexer_3 (
    .in0(multiplexer_2_out), .in1({PC[31:28], ins_index, 2'b00}), .out(NPC), .sel(isJOrJal));

  // Other names for the same wires on the sheet: des_JorJal[31:2] = {PC[31:28], ins_index}; desRs_JrOrJalr[31:0] = Rs

  // Notes on the sheet:
  //   指令有：
  //   输入：PC，当前PC值
  //   R: addu 下一跳是PC+4
  //   R: subu 下一跳是PC+4
  //   R: jr 下一跳是Rs的内容
  //   I: ori 下一跳是PC+4
  //   I: lw 下一跳是PC+4
  //   I: sw 下一跳是PC+4
  //   I: lui 下一条是PC+4
  //   J: jal 下一条是PC[31:28]|26|00
  //   I: beq 下一跳是PC+4+imm(符扩)|00
  //   输入：Rs内容,是不是j,是不是jr
  //   输入：imm,是不是branch,有没有成功beq
  //   输入：ins_index，是不是j，是不是jal
  //   输出：PC+4，jal要用，要存进$ra
  //   输出：NPC，根据输入层层选择后得到
endmodule

module GRF_04 (
  input  clk,
  input  rst,
  input  WE,
  input  [4:0] A1,
  input  [4:0] A2,
  input  [4:0] A3,
  input  [31:0] WD,
  output [31:0] RD1,
  output [31:0] RD2
);

  wire [31:0] in01, in02, in03, in04, in05, in06, in07, in08, in09, in10, in11, in12, in13, in14, in15, in16,
       in17, in18, in19, in20, in21, in22, in23, in24, in25, in26, in27, in28, in29, in30, in31, out00,
       out01, out02, out03, out04, out05, out06, out07, out08, out09, out10, out11, out12, out13, out14,
       out15, out16, out17, out18, out19, out20, out21, out22, out23, out24, out25, out26, out27, out28,
       out29, out30, out31;

  Register #(.width(32)) register_1 (.D({32{1'b0}}), .en(WE), .Q(out00), .clk(clk), .clr(rst));
  Register #(.width(32)) register_2 (.D(in01), .en(WE), .Q(out01), .clk(clk), .clr(rst));
  Register #(.width(32)) register_3 (.D(in02), .en(WE), .Q(out02), .clk(clk), .clr(rst));
  Register #(.width(32)) register_4 (.D(in03), .en(WE), .Q(out03), .clk(clk), .clr(rst));
  Register #(.width(32)) register_5 (.D(in04), .en(WE), .Q(out04), .clk(clk), .clr(rst));
  Register #(.width(32)) register_6 (.D(in05), .en(WE), .Q(out05), .clk(clk), .clr(rst));
  Register #(.width(32)) register_7 (.D(in06), .en(WE), .Q(out06), .clk(clk), .clr(rst));
  Register #(.width(32)) register_8 (.D(in07), .en(WE), .Q(out07), .clk(clk), .clr(rst));
  Multiplexer #(.select(5), .width(32), .enable("false")) multiplexer_1 (
    .in0(out00), .in1(out01), .in2(out02), .in3(out03), .in4(out04), .in5(out05), .in6(out06), .in7(out07),
    .in8(out08), .in9(out09), .in10(out10), .in11(out11), .in12(out12), .in13(out13), .in14(out14),
    .in15(out15), .in16(out16), .in17(out17), .in18(out18), .in19(out19), .in20(out20), .in21(out21),
    .in22(out22), .in23(out23), .in24(out24), .in25(out25), .in26(out26), .in27(out27), .in28(out28),
    .in29(out29), .in30(out30), .in31(out31), .out(RD1), .sel(A1));
  Register #(.width(32)) register_9 (.D(in08), .en(WE), .Q(out08), .clk(clk), .clr(rst));
  Register #(.width(32)) register_10 (.D(in09), .en(WE), .Q(out09), .clk(clk), .clr(rst));
  Register #(.width(32)) register_11 (.D(in10), .en(WE), .Q(out10), .clk(clk), .clr(rst));
  Register #(.width(32)) register_12 (.D(in11), .en(WE), .Q(out11), .clk(clk), .clr(rst));
  Multiplexer #(.select(5), .width(32), .enable("false")) multiplexer_2 (
    .in0(out00), .in1(out01), .in2(out02), .in3(out03), .in4(out04), .in5(out05), .in6(out06), .in7(out07),
    .in8(out08), .in9(out09), .in10(out10), .in11(out11), .in12(out12), .in13(out13), .in14(out14),
    .in15(out15), .in16(out16), .in17(out17), .in18(out18), .in19(out19), .in20(out20), .in21(out21),
    .in22(out22), .in23(out23), .in24(out24), .in25(out25), .in26(out26), .in27(out27), .in28(out28),
    .in29(out29), .in30(out30), .in31(out31), .out(RD2), .sel(A2));
  Register #(.width(32)) register_13 (.D(in12), .en(WE), .Q(out12), .clk(clk), .clr(rst));
  Register #(.width(32)) register_14 (.D(in13), .en(WE), .Q(out13), .clk(clk), .clr(rst));
  Register #(.width(32)) register_15 (.D(in14), .en(WE), .Q(out14), .clk(clk), .clr(rst));
  Register #(.width(32)) register_16 (.D(in15), .en(WE), .Q(out15), .clk(clk), .clr(rst));
  Demultiplexer #(.select(5), .width(32), .tristate("true"), .enable("false")) demultiplexer_1 (
    .out1(in01), .out2(in02), .out3(in03), .out4(in04), .out5(in05), .out6(in06), .out7(in07), .out8(in08),
    .out9(in09), .out10(in10), .out11(in11), .out12(in12), .out13(in13), .out14(in14), .out15(in15),
    .out16(in16), .out17(in17), .out18(in18), .out19(in19), .out20(in20), .out21(in21), .out22(in22),
    .out23(in23), .out24(in24), .out25(in25), .out26(in26), .out27(in27), .out28(in28), .out29(in29),
    .out30(in30), .out31(in31), .in(WD), .sel(A3));  // open: out0
  Register #(.width(32)) register_17 (.D(in16), .en(WE), .Q(out16), .clk(clk), .clr(rst));
  Register #(.width(32)) register_18 (.D(in17), .en(WE), .Q(out17), .clk(clk), .clr(rst));
  Register #(.width(32)) register_19 (.D(in18), .en(WE), .Q(out18), .clk(clk), .clr(rst));
  Register #(.width(32)) register_20 (.D(in19), .en(WE), .Q(out19), .clk(clk), .clr(rst));
  Register #(.width(32)) register_21 (.D(in20), .en(WE), .Q(out20), .clk(clk), .clr(rst));
  Register #(.width(32)) register_22 (.D(in21), .en(WE), .Q(out21), .clk(clk), .clr(rst));
  Register #(.width(32)) register_23 (.D(in22), .en(WE), .Q(out22), .clk(clk), .clr(rst));
  Register #(.width(32)) register_24 (.D(in23), .en(WE), .Q(out23), .clk(clk), .clr(rst));
  Register #(.width(32)) register_25 (.D(in24), .en(WE), .Q(out24), .clk(clk), .clr(rst));
  Register #(.width(32)) register_26 (.D(in25), .en(WE), .Q(out25), .clk(clk), .clr(rst));
  Register #(.width(32)) register_27 (.D(in26), .en(WE), .Q(out26), .clk(clk), .clr(rst));
  Register #(.width(32)) register_28 (.D(in27), .en(WE), .Q(out27), .clk(clk), .clr(rst));
  Register #(.width(32)) register_29 (.D(in28), .en(WE), .Q(out28), .clk(clk), .clr(rst));
  Register #(.width(32)) register_30 (.D(in29), .en(WE), .Q(out29), .clk(clk), .clr(rst));
  Register #(.width(32)) register_31 (.D(in30), .en(WE), .Q(out30), .clk(clk), .clr(rst));
  Register #(.width(32)) register_32 (.D(in31), .en(WE), .Q(out31), .clk(clk), .clr(rst));

  // Notes on the sheet:
  //   输入：A1，A2，A3选址
  //   输入：时钟；异步复位；写入使能
  //   输出：RD1，RD2读出
endmodule

module ALU_05 (
  input  [31:0] A,
  input  [31:0] B,
  input  [2:0] ALUOp,
  output [31:0] C,
  output isEqual
);

  wire comparator_1_lt;
  wire [4:0] bit_extender_1_out;
  wire [31:0] adder_1_out, multiplexer_1_out, or_1_out, shifter_1_out, shifter_2_out, subtractor_1_out;

  Bit_Extender #(.in_width(32), .out_width(5)) bit_extender_1 (.in(A), .out(bit_extender_1_out));
  Adder #(.width(32)) adder_1 (.a(A), .b(B), .out(adder_1_out));  // open: cin, cout
  Subtractor #(.width(32)) subtractor_1 (.a(A), .b(B), .out(subtractor_1_out));  // open: bin, bout
  Shifter #(.width(32)) shifter_1 (.in(B), .\dist (bit_extender_1_out), .out(shifter_1_out));
  assign or_1_out = A | B;  // OR_Gate or_1, 32 bits wide
  Shifter #(.width(32)) shifter_2 (.in(B), .\dist (5'b10000), .out(shifter_2_out));
  Multiplexer #(.width(32), .enable("false")) multiplexer_1 (
    .in0({32{1'b0}}), .in1(32'h1), .out(multiplexer_1_out), .sel(comparator_1_lt));
  Comparator #(.width(32)) comparator_1 (.a(A), .b(B), .lt(comparator_1_lt));  // open: gt, eq
  Multiplexer #(.select(3), .width(32), .enable("false")) multiplexer_2 (
    .in0(adder_1_out), .in1(subtractor_1_out), .in2(shifter_1_out), .in3(or_1_out), .in4(shifter_2_out),
    .in5(multiplexer_1_out), .out(C), .sel(ALUOp));  // open: in6, in7
  Comparator #(.width(32), .mode("unsigned")) comparator_2 (.a(A), .b(B), .eq(isEqual));  // open: gt, lt

  // Notes on the sheet:
  //   输入：计算方式选择
  //   R: jr 无
  //   I: ori 011
  //   I: lw 无
  //   I: sw 无
  //   I: beq 无
  //   J: jal 无
  //   输入：A，B两个等待计算的数字
  //   R: addu 000
  //   R: subu 001
  //   I: andi 010-实验中不涉及这条指令，但还是预留一个坑位
  //   I: lui 100 lui对于imm，0扩成32位后传入输入A，之后的处理在ALU中完成
  //   输出：C计算结果
  //   输出：A是否等于B
  //   输出：C计算结果
endmodule

module DM_06 (
  input  [31:0] A,
  input  [31:0] WD,
  input  WE,
  input  clk,
  input  reset,
  output [31:0] RD
);

  RAM #(.addrWidth(12), .dataWidth(32), .bus("separate")) ram_1 (
    .addr(A[13:2]), .din(WD), .data(RD), .str(WE), .clk(clk), .clr(reset));  // open: sel, ld

  // Notes on the sheet:
  //   输入:clk，reset
  //   输入:写使能，写内容
  //   输入:选址信号[31:0]，取[13:2]用来选址
  //   输出：读内容
endmodule

module EXT_07 (
  input  [15:0] imm,
  input  zeroOrSigned,
  output [31:0] immHasExted
);

  wire [31:0] bit_extender_1_out, bit_extender_2_out;

  assign bit_extender_1_out = {{16{1'b0}}, imm};  // Bit_Extender bit_extender_1
  assign bit_extender_2_out = {{16{imm[15]}}, imm};  // Bit_Extender bit_extender_2
  Multiplexer #(.width(32), .enable("false")) multiplexer_1 (
    .in0(bit_extender_1_out), .in1(bit_extender_2_out), .out(immHasExted), .sel(zeroOrSigned));

  // Notes on the sheet:
  //   输入:0扩展还是符号扩展
  //   I: ori 0扩展
  //   I: lw 符号扩展
  //   I: sw 符号扩展
  //   I: beq NPC中处理
  //   I: lui ALU中处理
  //   输入:imm[15:0]，不经过任何处理输入
  //   输出：扩展成32位
endmodule

module Controller_08 (
  input  [31:0] ins,
  output [1:0] A3_RdRt_ra_01,
  output GRF_WE_02,
  output [1:0] GRF_WD_03,
  output ALU_B_04,
  output ALU_immExt_05,
  output [2:0] ALU_Op_06,
  output DM_WE_07,
  output isBranch_08,
  output isJrOrJalr_09,
  output isJalr_10,
  output isJOrJal_11,
  output isJal_11,
  output isSll_12,
  output isLb_13
);

  wire A3_Rd, A3_Rt, addu, GRF_WD_ALU, GRF_WD_DM, GRF_WD_PC_4, isR, j, jr, lui, lw, not_1_out, not_2_out,
       not_3_out, not_4_out, not_5_out, not_6_out, not_7_out, not_8_out, not_9_out, not_10_out, not_11_out,
       not_12_out, or_6_out, ori, slt, subu;

  not not_1 (not_1_out, ins[31]);
  not not_2 (not_2_out, ins[29]);
  not not_3 (not_3_out, ins[30]);
  not not_4 (not_4_out, ins[28]);
  not not_5 (not_5_out, ins[26]);
  not not_6 (not_6_out, ins[27]);
  not not_7 (not_7_out, ins[3]);
  not not_8 (not_8_out, ins[4]);
  not not_9 (not_9_out, ins[5]);
  not not_10 (not_10_out, ins[2]);
  not not_11 (not_11_out, ins[0]);
  not not_12 (not_12_out, ins[1]);
  and and_1 (isR, not_1_out, not_3_out, not_2_out, not_4_out, not_6_out, not_5_out);
  and and_2 (addu, isR, ins[5], not_8_out, not_7_out, not_10_out, not_12_out, not_11_out);
  and and_3 (subu, isR, ins[5], not_8_out, not_7_out, not_10_out, ins[1], not_11_out);
  and and_4 (isSll_12, isR, not_9_out, not_8_out, not_7_out, not_10_out, not_12_out, not_11_out);
  and and_5 (slt, isR, ins[5], not_8_out, ins[3], not_10_out, ins[1], not_11_out);
  and and_6 (jr, isR, not_9_out, not_8_out, ins[3], not_10_out, not_12_out, not_11_out);
  and and_7 (isJalr_10, isR, not_9_out, not_8_out, ins[3], not_10_out, not_12_out, ins[0]);
  and and_8 (ori, not_1_out, not_3_out, ins[29], ins[28], not_6_out, ins[26]);
  and and_9 (lw, ins[31], not_3_out, not_2_out, not_4_out, ins[27], ins[26]);
  and and_10 (DM_WE_07, ins[31], not_3_out, ins[29], not_4_out, ins[27], ins[26]);
  and and_11 (isBranch_08, not_1_out, not_3_out, not_2_out, ins[28], not_6_out, not_5_out);
  and and_12 (lui, not_1_out, not_3_out, ins[29], ins[28], ins[27], ins[26]);
  and and_13 (isLb_13, ins[31], not_3_out, not_2_out, not_4_out, not_6_out, not_5_out);
  and and_14 (j, not_1_out, not_3_out, not_2_out, not_4_out, ins[27], not_5_out);
  and and_15 (isJal_11, not_1_out, not_3_out, not_2_out, not_4_out, ins[27], ins[26]);
  or or_1 (A3_Rd, addu, subu, isSll_12, slt, isJalr_10);
  or or_2 (A3_Rt, ori, lw, lui, isLb_13);
  or or_3 (GRF_WD_DM, lw, isLb_13);
  or or_4 (GRF_WD_PC_4, isJalr_10, isJal_11);
  or or_5 (GRF_WD_ALU, addu, subu, isSll_12, slt, ori, lui);
  or or_6 (or_6_out, addu, lw, DM_WE_07, isLb_13);
  A3_3to2zip a3_3to2zip_1 (.Rd(A3_Rd), .Rt(A3_Rt), .ra(isJal_11), .o1(A3_RdRt_ra_01[1]), .o0(A3_RdRt_ra_01[0]));
  or or_7 (GRF_WE_02, addu, subu, isSll_12, slt, isJalr_10, ori, lw, lui, isLb_13, isJal_11);
  GRF_WD_3to2zip grf_wd_3to2zip_1 (
    .ALU(GRF_WD_ALU), .DM(GRF_WD_DM), .PC4(GRF_WD_PC_4), .o1(GRF_WD_03[1]), .o0(GRF_WD_03[0]));
  ALUOp_5to3zip aluop_5to3zip_1 (
    .addu(or_6_out), .subu(subu), .sll(isSll_12), .ori(ori), .lui(lui), .slt(slt), .o2(ALU_Op_06[0]),
    .o1(ALU_Op_06[1]), .o0(ALU_Op_06[2]));
  or or_8 (ALU_B_04, ori, lw, DM_WE_07, lui, isLb_13);
  or or_9 (ALU_immExt_05, lw, DM_WE_07, isLb_13);
  or or_10 (isJrOrJalr_09, jr, isJalr_10);
  or or_11 (isJOrJal_11, j, isJal_11);

  // Other names for the same wires on the sheet: beq = isBranch_08; op[5:0] = ins[31:26]; func[5:0] = ins[5:0];
  //   imm[15:0] = ins[15:0]; ins_index[25:0] = ins[25:0]; shamt[4:0] = ins[10:6]; Rd[4:0] = ins[15:11];
  //   Rt[4:0] = ins[20:16]; Rs[4:0] = ins[25:21]; A3__ra = isJal_11; jal = isJal_11; jalr = isJalr_10; lb = isLb_13;
  //   sll = isSll_12; sw = DM_WE_07

  // Notes on the sheet:
  //   R: addu 下一跳是PC+4
  //   R: subu 下一跳是PC+4
  //   R: jr 下一跳是Rs的内容
  //   I: ori 下一跳是PC+4
  //   I: lw 下一跳是PC+4
  //   I: sw 下一跳是PC+4
  //   I: lui 下一条是PC+4
  //   R
  //   I: beq 下一跳是PC+4+imm(符扩)|00
  //   J: jal 下一条是PC[31:28]|26|00
  //   I
  //   J
  //   00为Rd，01为Rt，10为$ra
  //   addu,subu;ori,lw,lui;jal
  //   R: addu 000
  //   R: subu 001
  //   I: ori 011
  //   00为ALU，01为DM-lw，10为PC+4-jal
  //   0为RD2,1为imm
  //   addu subu为RD2
  //   ori lw sw为imm
  //   beq为RD2
  //   lui为imm
  //   0为0扩展，1为Signed扩展
  //   ori 0扩展；lw sw符扩
  //   beq lui不用管
  //   I: lui 100 lui对于imm，0扩成32位后传入输入A，之后的处理在ALU中完成
  //   I: andi 010-实验中不涉及这条指令，但还是预留一个坑位，目前放置了常数0
  //   R
endmodule

module A3_3to2zip (
  input  Rd,
  input  Rt,
  input  ra,
  output o1,
  output o0
);


  assign o0 = Rt;
  assign o1 = ra;
endmodule

module GRF_WD_3to2zip (
  input  ALU,
  input  DM,
  input  PC4,
  output o1,
  output o0
);


  assign o0 = DM;
  assign o1 = PC4;
endmodule

module ALUOp_5to3zip (
  input  addu,
  input  subu,
  input  sll,
  input  ori,
  input  lui,
  input  slt,
  output o2,
  output o1,
  output o0
);

  wire and_1_out, and_2_out, and_3_out, and_4_out, not_1_out, not_2_out, not_3_out, not_4_out, not_5_out,
       not_6_out, not_7_out, not_8_out, not_9_out, not_10_out, not_11_out, not_12_out, not_13_out,
       not_14_out, not_15_out, not_16_out, not_17_out;

  not not_1 (not_1_out, addu);
  not not_2 (not_2_out, subu);
  not not_3 (not_3_out, sll);
  not not_4 (not_4_out, ori);
  not not_5 (not_5_out, addu);
  not not_6 (not_6_out, subu);
  not not_7 (not_7_out, lui);
  not not_8 (not_8_out, slt);
  not not_9 (not_9_out, addu);
  not not_10 (not_10_out, subu);
  not not_11 (not_11_out, lui);
  not not_12 (not_12_out, addu);
  not not_13 (not_13_out, subu);
  not not_14 (not_14_out, lui);
  not not_15 (not_15_out, addu);
  not not_16 (not_16_out, sll);
  not not_17 (not_17_out, lui);
  and and_1 (and_1_out, not_1_out, not_2_out, not_3_out, not_4_out, slt);
  and and_2 (and_2_out, not_5_out, not_6_out, not_7_out, not_8_out);
  and and_3 (and_3_out, not_9_out, not_10_out, ori, not_11_out);
  and and_4 (and_4_out, not_12_out, not_13_out, sll, not_14_out);
  and and_5 (o0, not_15_out, not_16_out, not_17_out);
  or or_1 (o2, and_1_out, lui);
  or or_2 (o1, and_2_out, and_3_out, and_4_out);
endmodule
