// Logisim project 同步复位流水线.circ as structural Verilog: 20 circuits, main circuit IM_01
module IM_01 (
  input  [31:0] PC,
  output [31:0] Ins
);

  wire [31:0] subtractor_1_out;

  Subtractor #(.width(32)) subtractor_1 (.a(PC), .b(32'h3000), .out(subtractor_1_out));  // open: bin, bout
  ROM #(.addrWidth(12), .dataWidth(32)) rom_1 (.addr(subtractor_1_out[13:2]), .data(Ins));  // open: sel

  // Notes on the sheet:
  //   输入：PC，用于选择需要ROM中的哪个指令
  //   contents of rom_1 (hex, n*v repeats v):
  //   34013018 201020 400008 3c01ffff 3c01ffff 3c01ffff 3c081100
  //   输出：instr，ROM中指令被取出
endmodule

module PC_02 (
  input  [31:0] NPC,
  input  clk,
  input  rst,
  input  en,
  output [31:0] PC
);

  wire comparator_1_eq;
  wire [31:0] PC_q;

  Register #(.width(32)) u_PC (.D(NPC), .en(en), .Q(PC_q), .clk(clk), .clr(rst));
  Multiplexer #(.width(32), .enable("false")) multiplexer_1 (
    .in0(PC_q), .in1(32'h3000), .out(PC), .sel(comparator_1_eq));
  Comparator #(.width(32), .mode("unsigned")) comparator_1 (
    .a(PC_q), .b({32{1'b0}}), .eq(comparator_1_eq));  // open: gt, lt

  // Notes on the sheet:
  //   输入：时钟；异步复位
  //   输入：NPC，下一条指令地址
  //   输出：PC，当前指令地址
endmodule

module NPC_03 (
  input  [31:0] PC_F,
  input  [31:0] PC_D,
  input  [31:0] Rs,
  input  [15:0] imm,
  input  [25:0] ins_index,
  input  isJr,
  input  isJal,
  input  isBranch,
  input  isBranchSuccess,
  output [31:0] NPC
);

  wire and_1_out;
  wire [31:0] bit_extender_1_out, \desBranch_b指令 , multiplexer_1_out, multiplexer_2_out, PC4_D, PC4_F;

  assign bit_extender_1_out = {{14{imm[15]}}, {imm, 2'b00}};  // Bit_Extender bit_extender_1
  Adder #(.width(32)) adder_1 (.a(bit_extender_1_out), .b(PC4_D), .out(\desBranch_b指令 ));  // open: cin, cout
  Adder #(.width(32)) adder_2 (.a(PC_F), .b(32'h4), .out(PC4_F));  // open: cin, cout
  Adder #(.width(32)) adder_3 (.a(PC_D), .b(32'h4), .out(PC4_D));  // open: cin, cout
  Multiplexer #(.width(32), .enable("false")) multiplexer_1 (
    .in0(PC4_F), .in1(Rs), .out(multiplexer_1_out), .sel(isJr));
  Multiplexer #(.width(32), .enable("false")) multiplexer_2 (
    .in0(multiplexer_1_out), .in1(\desBranch_b指令 ), .out(multiplexer_2_out), .sel(and_1_out));
  and and_1 (and_1_out, isBranch, isBranchSuccess);
  Multiplexer #(.width(32), .enable("false")) multiplexer_3 (
    .in0(multiplexer_2_out), .in1({PC_D[31:28], ins_index, 2'b00}), .out(NPC), .sel(isJal));

  // Other names for the same wires on the sheet: desJal_jal[31:2] = {PC_D[31:28], ins_index}; desRs_jr[31:0] = Rs

  // Notes on the sheet:
  //   指令有：
  //   输入：PC，当前PC值
  //   R: addu 下一跳是PC+4
  //   R: subu 下一跳是PC+4
  //   R: jr 下一跳是Rs的内容
  //   I: ori 下一跳是PC+4
  //   I: lw 下一跳是PC+4
  //   I: sw 下一跳是PC+4
  //   I: lui 下一条是PC+4
  //   J: jal 下一条是PC[31:28]|26|00
  //   I: beq 下一跳是PC+4+imm(符扩)|00
  //   输入：Rs内容,是不是j,是不是jr
  //   输入：imm,是不是branch,有没有成功beq
  //   输入：ins_index，是不是j，是不是jal
  //   输出：PC+4，jal要用，要存进$ra
  //   输出：NPC，根据输入层层选择后得到
endmodule

module GRF_04 (
  input  clk,
  input  rst,
  input  WE,
  input  [4:0] A1,
  input  [4:0] A2,
  input  [4:0] A3,
  input  [31:0] WD,
  output [31:0] RD1,
  output [31:0] RD2
);

  wire and_1_out, and_2_out, comparator_1_eq, comparator_2_eq, comparator_3_eq, comparator_4_eq, not_1_out,
       not_2_out;
  wire [31:0] in01, in02, in03, in04, in05, in06, in07, in08, in09, in10, in11, in12, in13, in14, in15, in16,
       in17, in18, in19, in20, in21, in22, in23, in24, in25, in26, in27, in28, in29, in30, in31,
       multiplexer_1_out, multiplexer_2_out, out00, out01, out02, out03, out04, out05, out06, out07, out08,
       out09, out10, out11, out12, out13, out14, out15, out16, out17, out18, out19, out20, out21, out22,
       out23, out24, out25, out26, out27, out28, out29, out30, out31;

  Register #(.width(32)) register_1 (.D({32{1'b0}}), .en(WE), .Q(out00), .clk(clk), .clr(rst));
  Register #(.width(32)) register_2 (.D(in01), .en(WE), .Q(out01), .clk(clk), .clr(rst));
  Register #(.width(32)) register_3 (.D(in02), .en(WE), .Q(out02), .clk(clk), .clr(rst));
  Register #(.width(32)) register_4 (.D(in03), .en(WE), .Q(out03), .clk(clk), .clr(rst));
  // Probe on out00
  // Probe on out01
  // Probe on out02
  // Probe on out03
  // Probe on out04
  // Probe on out05
  // Probe on out06
  // Probe on out07
  // Probe on out08
  // Probe on out09
  // Probe on out10
  // Probe on out11
  // Probe on out12
  // Probe on out13
  // Probe on out14
  // Probe on out15
  // Probe on out16
  // Probe on out17
  // Probe on out18
  // Probe on out19
  // Probe on out20
  // Probe on out21
  // Probe on out22
  // Probe on out23
  // Probe on out24
  // Probe on out25
  // Probe on out26
  // Probe on out27
  // Probe on out28
  // Probe on out29
  // Probe on out30
  // Probe on out31
  Register #(.width(32)) register_5 (.D(in04), .en(WE), .Q(out04), .clk(clk), .clr(rst));
  Register #(.width(32)) register_6 (.D(in05), .en(WE), .Q(out05), .clk(clk), .clr(rst));
  Register #(.width(32)) register_7 (.D(in06), .en(WE), .Q(out06), .clk(clk), .clr(rst));
  Register #(.width(32)) register_8 (.D(in07), .en(WE), .Q(out07), .clk(clk), .clr(rst));
  Multiplexer #(.select(5), .width(32), .enable("false")) multiplexer_1 (
    .in0(out00), .in1(out01), .in2(out02), .in3(out03), .in4(out04), .in5(out05), .in6(out06), .in7(out07),
    .in8(out08), .in9(out09), .in10(out10), .in11(out11), .in12(out12), .in13(out13), .in14(out14),
    .in15(out15), .in16(out16), .in17(out17), .in18(out18), .in19(out19), .in20(out20), .in21(out21),
    .in22(out22), .in23(out23), .in24(out24), .in25(out25), .in26(out26), .in27(out27), .in28(out28),
    .in29(out29), .in30(out30), .in31(out31), .out(multiplexer_1_out), .sel(A1));
  Register #(.width(32)) register_9 (.D(in08), .en(WE), .Q(out08), .clk(clk), .clr(rst));
  Register #(.width(32)) register_10 (.D(in09), .en(WE), .Q(out09), .clk(clk), .clr(rst));
  Register #(.width(32)) register_11 (.D(in10), .en(WE), .Q(out10), .clk(clk), .clr(rst));
  Register #(.width(32)) register_12 (.D(in11), .en(WE), .Q(out11), .clk(clk), .clr(rst));
  Multiplexer #(.select(5), .width(32), .enable("false")) multiplexer_2 (
    .in0(out00), .in1(out01), .in2(out02), .in3(out03), .in4(out04), .in5(out05), .in6(out06), .in7(out07),
    .in8(out08), .in9(out09), .in10(out10), .in11(out11), .in12(out12), .in13(out13), .in14(out14),
    .in15(out15), .in16(out16), .in17(out17), .in18(out18), .in19(out19), .in20(out20), .in21(out21),
    .in22(out22), .in23(out23), .in24(out24), .in25(out25), .in26(out26), .in27(out27), .in28(out28),
    .in29(out29), .in30(out30), .in31(out31), .out(multiplexer_2_out), .sel(A2));
  Register #(.width(32)) register_13 (.D(in12), .en(WE), .Q(out12), .clk(clk), .clr(rst));
  Register #(.width(32)) register_14 (.D(in13), .en(WE), .Q(out13), .clk(clk), .clr(rst));
  Register #(.width(32)) register_15 (.D(in14), .en(WE), .Q(out14), .clk(clk), .clr(rst));
  Register #(.width(32)) register_16 (.D(in15), .en(WE), .Q(out15), .clk(clk), .clr(rst));
  Demultiplexer #(.select(5), .width(32), .tristate("true"), .enable("false")) demultiplexer_1 (
    .out1(in01), .out2(in02), .out3(in03), .out4(in04), .out5(in05), .out6(in06), .out7(in07), .out8(in08),
    .out9(in09), .out10(in10), .out11(in11), .out12(in12), .out13(in13), .out14(in14), .out15(in15),
    .out16(in16), .out17(in17), .out18(in18), .out19(in19), .out20(in20), .out21(in21), .out22(in22),
    .out23(in23), .out24(in24), .out25(in25), .out26(in26), .out27(in27), .out28(in28), .out29(in29),
    .out30(in30), .out31(in31), .in(WD), .sel(A3));  // open: out0
  Register #(.width(32)) register_17 (.D(in16), .en(WE), .Q(out16), .clk(clk), .clr(rst));
  Register #(.width(32)) register_18 (.D(in17), .en(WE), .Q(out17), .clk(clk), .clr(rst));
  Register #(.width(32)) register_19 (.D(in18), .en(WE), .Q(out18), .clk(clk), .clr(rst));
  Register #(.width(32)) register_20 (.D(in19), .en(WE), .Q(out19), .clk(clk), .clr(rst));
  Register #(.width(32)) register_21 (.D(in20), .en(WE), .Q(out20), .clk(clk), .clr(rst));
  Register #(.width(32)) register_22 (.D(in21), .en(WE), .Q(out21), .clk(clk), .clr(rst));
  Register #(.width(32)) register_23 (.D(in22), .en(WE), .Q(out22), .clk(clk), .clr(rst));
  Register #(.width(32)) register_24 (.D(in23), .en(WE), .Q(out23), .clk(clk), .clr(rst));
  Comparator #(.width(5), .mode("unsigned")) comparator_1 (.a(A1), .b(A3), .eq(comparator_1_eq));  // open: gt, lt
  not not_1 (not_1_out, comparator_2_eq);
  Comparator #(.width(5), .mode("unsigned")) comparator_2 (
    .a(A1), .b({5{1'b0}}), .eq(comparator_2_eq));  // open: gt, lt
  Comparator #(.width(5), .mode("unsigned")) comparator_3 (.a(A2), .b(A3), .eq(comparator_3_eq));  // open: gt, lt
  not not_2 (not_2_out, comparator_4_eq);
  Comparator #(.width(5), .mode("unsigned")) comparator_4 (
    .a(A2), .b({5{1'b0}}), .eq(comparator_4_eq));  // open: gt, lt
  Multiplexer #(.width(32), .enable("false")) multiplexer_3 (
    .in0(multiplexer_1_out), .in1(WD), .out(RD1), .sel(and_1_out));
  and and_1 (and_1_out, comparator_1_eq, WE, not_1_out);
  Multiplexer #(.width(32), .enable("false")) multiplexer_4 (
    .in0(multiplexer_2_out), .in1(WD), .out(RD2), .sel(and_2_out));
  and and_2 (and_2_out, comparator_3_eq, WE, not_2_out);
  Register #(.width(32)) register_25 (.D(in24), .en(WE), .Q(out24), .clk(clk), .clr(rst));
  Register #(.width(32)) register_26 (.D(in25), .en(WE), .Q(out25), .clk(clk), .clr(rst));
  Register #(.width(32)) register_27 (.D(in26), .en(WE), .Q(out26), .clk(clk), .clr(rst));
  Register #(.width(32)) register_28 (.D(in27), .en(WE), .Q(out27), .clk(clk), .clr(rst));
  Register #(.width(32)) register_29 (.D(in28), .en(WE), .Q(out28), .clk(clk), .clr(rst));
  Register #(.width(32)) register_30 (.D(in29), .en(WE), .Q(out29), .clk(clk), .clr(rst));
  Register #(.width(32)) register_31 (.D(in30), .en(WE), .Q(out30), .clk(clk), .clr(rst));
  Register #(.width(32)) register_32 (.D(in31), .en(WE), .Q(out31), .clk(clk), .clr(rst));

  // Notes on the sheet:
  //   输入：A1，A2，A3选址
  //   输入：时钟；异步复位；写入使能
  //   输出：RD1，RD2读出
  //   输出：RD1，RD2读出
endmodule

module ALU_05 (
  input  [31:0] A,
  input  [31:0] B,
  input  [2:0] ALUOp,
  output [31:0] C
);

  wire [31:0] adder_1_out, and_1_out, or_1_out, shifter_1_out, subtractor_1_out;

  Adder #(.width(32)) adder_1 (.a(A), .b(B), .out(adder_1_out));  // open: cin, cout
  Subtractor #(.width(32)) subtractor_1 (.a(A), .b(B), .out(subtractor_1_out));  // open: bin, bout
  assign and_1_out = A & B;  // AND_Gate and_1, 32 bits wide
  assign or_1_out = A | B;  // OR_Gate or_1, 32 bits wide
  Shifter #(.width(32)) shifter_1 (.in(B), .\dist (5'b10000), .out(shifter_1_out));
  Multiplexer #(.select(3), .width(32), .enable("false")) multiplexer_1 (
    .in0(adder_1_out), .in1(subtractor_1_out), .in2(and_1_out), .in3(or_1_out), .in4(shifter_1_out), .out(C),
    .sel(ALUOp));  // open: in5, in6, in7

  // Notes on the sheet:
  //   输入：计算方式选择
  //   R: jr 无
  //   I: ori 011
  //   I: lw 无
  //   I: sw 无
  //   I: beq 无
  //   J: jal 无
  //   输入：A，B两个等待计算的数字
  //   R: addu 000
  //   R: subu 001
  //   I: andi 010-实验中不涉及这条指令，但还是预留一个坑位
  //   I: lui 100 lui对于imm，0扩成32位后传入输入A，之后的处理在ALU中完成
  //   输出：C计算结果
  //   输出：A是否等于B
  //   输出：A是否等于B
endmodule

module DM_06 (
  input  [31:0] A,
  input  [31:0] WD,
  input  WE,
  input  clk,
  input  reset,
  output [31:0] RD
);

  RAM #(.addrWidth(12), .dataWidth(32), .bus("separate")) ram_1 (
    .addr(A[13:2]), .din(WD), .data(RD), .str(WE), .clk(clk), .clr(reset));  // open: sel, ld

  // Notes on the sheet:
  //   输入:clk，reset
  //   输入:写使能，写内容
  //   输入:选址信号[31:0]，取[13:2]用来选址
  //   输出：读内容
endmodule

module EXT_07 (
  input  [15:0] imm,
  input  zeroOrSigned,
  output [31:0] immHasExted
);

  wire [31:0] bit_extender_1_out, bit_extender_2_out;

  assign bit_extender_1_out = {{16{1'b0}}, imm};  // Bit_Extender bit_extender_1
  assign bit_extender_2_out = {{16{imm[15]}}, imm};  // Bit_Extender bit_extender_2
  Multiplexer #(.width(32), .enable("false")) multiplexer_1 (
    .in0(bit_extender_1_out), .in1(bit_extender_2_out), .out(immHasExted), .sel(zeroOrSigned));

  // Notes on the sheet:
  //   输入:0扩展还是符号扩展
  //   I: ori 0扩展
  //   I: lw 符号扩展
  //   I: sw 符号扩展
  //   I: beq NPC中处理
  //   I: lui ALU中处理
  //   输入:imm[15:0]，不经过任何处理输入
  //   输出：扩展成32位
endmodule

module Controller_08 (
  input  [31:0] ins,
  output [1:0] GRF_A3_01,
  output GRF_WE_02,
  output [1:0] GRF_WD_03,
  output ALU_B_01,
  output ALU_immExt_02,
  output [2:0] ALU_Op_03,
  output DM_WE_01,
  output NPC_isJr_01,
  output NPC_isJal_02,
  output NPC_isBranch_03,
  output [4:0] Rs,
  output [4:0] Rt,
  output [4:0] Rd,
  output [15:0] imm,
  output [25:0] ins_index
);

  wire A3_Rd, A3_Rt, addu, GRF_WD_ALU, GRF_WD_DM, isR, lui, not_1_out, not_2_out, not_3_out, not_4_out,
       not_5_out, not_6_out, not_7_out, not_8_out, not_9_out, not_10_out, not_11_out, not_12_out, or_4_out,
       ori, subu;

  not not_1 (not_1_out, ins[31]);
  not not_2 (not_2_out, ins[30]);
  not not_3 (not_3_out, ins[28]);
  not not_4 (not_4_out, ins[29]);
  not not_5 (not_5_out, ins[26]);
  not not_6 (not_6_out, ins[27]);
  not not_7 (not_7_out, ins[4]);
  not not_8 (not_8_out, ins[5]);
  not not_9 (not_9_out, ins[3]);
  not not_10 (not_10_out, ins[1]);
  not not_11 (not_11_out, ins[0]);
  not not_12 (not_12_out, ins[2]);
  and and_1 (isR, not_1_out, not_2_out, not_4_out, not_3_out, not_6_out, not_5_out);
  and and_2 (addu, isR, ins[5], not_7_out, not_9_out, not_12_out, not_10_out, not_11_out);
  and and_3 (subu, isR, ins[5], not_7_out, not_9_out, not_12_out, ins[1], not_11_out);
  and and_4 (NPC_isJr_01, isR, not_8_out, not_7_out, ins[3], not_12_out, not_10_out, not_11_out);
  and and_5 (ori, not_1_out, not_2_out, ins[29], ins[28], not_6_out, ins[26]);
  and and_6 (GRF_WD_DM, ins[31], not_2_out, not_4_out, not_3_out, ins[27], ins[26]);
  and and_7 (DM_WE_01, ins[31], not_2_out, ins[29], not_3_out, ins[27], ins[26]);
  and and_8 (NPC_isBranch_03, not_1_out, not_2_out, not_4_out, ins[28], not_6_out, not_5_out);
  and and_9 (lui, not_1_out, not_2_out, ins[29], ins[28], ins[27], ins[26]);
  and and_10 (NPC_isJal_02, not_1_out, not_2_out, not_4_out, not_3_out, ins[27], ins[26]);
  or or_1 (A3_Rd, addu, subu);
  or or_2 (A3_Rt, ori, GRF_WD_DM, lui);
  or or_3 (GRF_WD_ALU, addu, subu, ori, lui);
  or or_4 (or_4_out, addu, GRF_WD_DM, DM_WE_01);
  A3_3to2zip a3_3to2zip_1 (.Rd(A3_Rd), .Rt(A3_Rt), .ra(NPC_isJal_02), .o1(GRF_A3_01[1]), .o0(GRF_A3_01[0]));
  or or_5 (GRF_WE_02, addu, subu, ori, GRF_WD_DM, lui, NPC_isJal_02);
  GRF_WD_3to2zip grf_wd_3to2zip_1 (
    .ALU(GRF_WD_ALU), .DM(GRF_WD_DM), .PC4(NPC_isJal_02), .o1(GRF_WD_03[1]), .o0(GRF_WD_03[0]));
  ALUOp_5to3zip aluop_5to3zip_1 (
    .addu(or_4_out), .subu(subu), .andi(1'b0), .ori(ori), .lui(lui), .o2(ALU_Op_03[2]), .o1(ALU_Op_03[1]),
    .o0(ALU_Op_03[0]));
  or or_6 (ALU_B_01, ori, GRF_WD_DM, DM_WE_01, lui);
  or or_7 (ALU_immExt_02, GRF_WD_DM, DM_WE_01);

  assign imm = ins[15:0];
  assign ins_index = ins[25:0];
  assign Rd = ins[15:11];
  assign Rs = ins[25:21];
  assign Rt = ins[20:16];

  // Other names for the same wires on the sheet: beq = NPC_isBranch_03; op[5:0] = ins[31:26]; func[5:0] = ins[5:0];
  //   shamt[4:0] = ins[10:6]; A3__ra = NPC_isJal_02; GRF_WD_PC_4 = NPC_isJal_02; jal = NPC_isJal_02; jr = NPC_isJr_01;
  //   lw = GRF_WD_DM; sw = DM_WE_01

  // Notes on the sheet:
  //   R: addu 下一跳是PC+4
  //   R: subu 下一跳是PC+4
  //   R: jr 下一跳是Rs的内容
  //   I: ori 下一跳是PC+4
  //   I: lw 下一跳是PC+4
  //   I: sw 下一跳是PC+4
  //   I: lui 下一条是PC+4
  //   R
  //   I: beq 下一跳是PC+4+imm(符扩)|00
  //   J: jal 下一条是PC[31:28]|26|00
  //   I
  //   J
  //   00为Rd，01为Rt，10为$ra
  //   addu,subu;ori,lw,lui;jal
  //   lui为imm
  //   R: addu 000
  //   R: subu 001
  //   I: ori 011
  //   00为ALU，01为DM-lw，10为PC+4-jal
  //   0为RD2,1为imm
  //   addu subu为RD2
  //   ori lw sw为imm
  //   beq为RD2
  //   0为0扩展，1为Signed扩展
  //   ori 0扩展；lw sw符扩
  //   beq lui不用管
  //   I: lui 100 lui对于imm，0扩成32位后传入输入A，之后的处理在ALU中完成
  //   I: andi 010-实验中不涉及这条指令，但还是预留一个坑位，目前放置了常数0
  //   R
endmodule

module A3_3to2zip (
  input  Rd,
  input  Rt,
  input  ra,
  output o1,
  output o0
);


  assign o0 = Rt;
  assign o1 = ra;
endmodule

module GRF_WD_3to2zip (
  input  ALU,
  input  DM,
  input  PC4,
  output o1,
  output o0
);


  assign o0 = DM;
  assign o1 = PC4;
endmodule

module ALUOp_5to3zip (
  input  addu,
  input  subu,
  input  andi,
  input  ori,
  input  lui,
  output o2,
  output o1,
  output o0
);

  wire not_1_out, not_2_out, not_3_out, not_4_out, not_5_out, not_6_out;

  not not_1 (not_1_out, addu);
  not not_2 (not_2_out, subu);
  not not_3 (not_3_out, lui);
  not not_4 (not_4_out, addu);
  not not_5 (not_5_out, andi);
  not not_6 (not_6_out, lui);
  and and_1 (o1, not_1_out, not_2_out, not_3_out);
  and and_2 (o0, not_4_out, not_5_out, not_6_out);

  assign o2 = lui;
endmodule

module ID_beforeD (
  input  [31:0] IR_F,
  input  [31:0] PC_F,
  input  clk,
  input  reset,
  input  en,
  output [31:0] IR_D,
  output [31:0] PC_D,
  output [31:0] PC4_D,
  output [31:0] PC8_D
);

  wire [31:0] adder_1_out, adder_2_out;

  Adder #(.width(32)) adder_1 (.a(PC_F), .b(32'h4), .out(adder_1_out));  // open: cin, cout
  Adder #(.width(32)) adder_2 (.a(adder_1_out), .b(32'h4), .out(adder_2_out));  // open: cin, cout
  Register #(.width(32)) register_1 (.D(IR_F), .en(en), .Q(IR_D), .clk(clk), .clr(reset));
  Register #(.width(32)) register_2 (.D(PC_F), .en(en), .Q(PC_D), .clk(clk), .clr(reset));
  Register #(.width(32)) register_3 (.D(adder_1_out), .en(en), .Q(PC4_D), .clk(clk), .clr(reset));
  Register #(.width(32)) register_4 (.D(adder_2_out), .en(en), .Q(PC8_D), .clk(clk), .clr(reset));
endmodule

module EX_beforeE (
  input  [31:0] IR_D,
  input  [31:0] PC_D,
  input  [31:0] PC4_D,
  input  [31:0] PC8_D,
  input  [31:0] RF_RD1,
  input  [31:0] RF_RD2,
  input  [31:0] EXT,
  input  clk,
  input  reset,
  input  en,
  output [31:0] IR_E,
  output [31:0] PC_E,
  output [31:0] PC4_E,
  output [31:0] PC8_E,
  output [31:0] RS_E,
  output [31:0] RT_E,
  output [31:0] EXT_E
);

  wire [31:0] multiplexer_1_out, multiplexer_2_out, multiplexer_3_out, multiplexer_4_out, multiplexer_5_out,
       multiplexer_6_out, multiplexer_7_out;

  Multiplexer #(.width(32), .enable("false")) multiplexer_1 (
    .in0(IR_D), .in1({32{1'b0}}), .out(multiplexer_1_out), .sel(reset));
  Multiplexer #(.width(32), .enable("false")) multiplexer_2 (
    .in0(PC_D), .in1({32{1'b0}}), .out(multiplexer_2_out), .sel(reset));
  Multiplexer #(.width(32), .enable("false")) multiplexer_3 (
    .in0(PC4_D), .in1({32{1'b0}}), .out(multiplexer_3_out), .sel(reset));
  Multiplexer #(.width(32), .enable("false")) multiplexer_4 (
    .in0(PC8_D), .in1({32{1'b0}}), .out(multiplexer_4_out), .sel(reset));
  Multiplexer #(.width(32), .enable("false")) multiplexer_5 (
    .in0(RF_RD1), .in1({32{1'b0}}), .out(multiplexer_5_out), .sel(reset));
  Multiplexer #(.width(32), .enable("false")) multiplexer_6 (
    .in0(RF_RD2), .in1({32{1'b0}}), .out(multiplexer_6_out), .sel(reset));
  Multiplexer #(.width(32), .enable("false")) multiplexer_7 (
    .in0(EXT), .in1({32{1'b0}}), .out(multiplexer_7_out), .sel(reset));
  Register #(.width(32)) register_1 (.D(multiplexer_1_out), .en(en), .Q(IR_E), .clk(clk));  // open: clr
  Register #(.width(32)) register_2 (.D(multiplexer_2_out), .en(en), .Q(PC_E), .clk(clk));  // open: clr
  Register #(.width(32)) register_3 (.D(multiplexer_3_out), .en(en), .Q(PC4_E), .clk(clk));  // open: clr
  Register #(.width(32)) register_4 (.D(multiplexer_4_out), .en(en), .Q(PC8_E), .clk(clk));  // open: clr
  Register #(.width(32)) register_5 (.D(multiplexer_5_out), .en(en), .Q(RS_E), .clk(clk));  // open: clr
  Register #(.width(32)) register_6 (.D(multiplexer_6_out), .en(en), .Q(RT_E), .clk(clk));  // open: clr
  Register #(.width(32)) register_7 (.D(multiplexer_7_out), .en(en), .Q(EXT_E), .clk(clk));  // open: clr
endmodule

module MEM_beforeM (
  input  [31:0] IR_E,
  input  [31:0] PC_E,
  input  [31:0] PC4_E,
  input  [31:0] PC8_E,
  input  [31:0] ALU,
  input  [31:0] RT_E,
  input  clk,
  input  reset,
  input  en,
  output [31:0] IR_M,
  output [31:0] PC_M,
  output [31:0] PC4_M,
  output [31:0] PC8_M,
  output [31:0] A0_M,
  output [31:0] RT_M
);

  Register #(.width(32)) register_1 (.D(IR_E), .en(en), .Q(IR_M), .clk(clk), .clr(reset));
  Register #(.width(32)) register_2 (.D(PC_E), .en(en), .Q(PC_M), .clk(clk), .clr(reset));
  Register #(.width(32)) register_3 (.D(PC4_E), .en(en), .Q(PC4_M), .clk(clk), .clr(reset));
  Register #(.width(32)) register_4 (.D(PC8_E), .en(en), .Q(PC8_M), .clk(clk), .clr(reset));
  Register #(.width(32)) register_5 (.D(ALU), .en(en), .Q(A0_M), .clk(clk), .clr(reset));
  Register #(.width(32)) register_6 (.D(RT_E), .en(en), .Q(RT_M), .clk(clk), .clr(reset));
endmodule

module WB_beforeW (
  input  [31:0] IR_M,
  input  [31:0] PC_M,
  input  [31:0] PC4_M,
  input  [31:0] PC8_M,
  input  [31:0] A0_M,
  input  [31:0] DM,
  input  clk,
  input  reset,
  input  en,
  output [31:0] IR_W,
  output [31:0] PC_W,
  output [31:0] PC4_W,
  output [31:0] PC8_W,
  output [31:0] A0_W,
  output [31:0] DR_W
);

  Register #(.width(32)) register_1 (.D(IR_M), .en(en), .Q(IR_W), .clk(clk), .clr(reset));
  Register #(.width(32)) register_2 (.D(PC_M), .en(en), .Q(PC_W), .clk(clk), .clr(reset));
  Register #(.width(32)) register_3 (.D(PC4_M), .en(en), .Q(PC4_W), .clk(clk), .clr(reset));
  Register #(.width(32)) register_4 (.D(PC8_M), .en(en), .Q(PC8_W), .clk(clk), .clr(reset));
  Register #(.width(32)) register_5 (.D(A0_M), .en(en), .Q(A0_W), .clk(clk), .clr(reset));
  Register #(.width(32)) register_6 (.D(DM), .en(en), .Q(DR_W), .clk(clk), .clr(reset));
endmodule

module main2 (
  input  rst
);

  wire ALU_B_01, ALU_immExt_02, clk, CMP_isequal, DM_WE, flushEX, GRF_WE_02, not_1_out, not_2_out,
       NPC_isBranch_03, NPC_isJal_02, NPC_isJr_01, or_1_out, stallID, stallPC;
  wire [1:0] Beq_RsChoose, Beq_RtChoose, GRF_A3_01, GRF_WD_03, JReg_RsChoose, store_RtChoose_E,
       store_RtChoose_M;
  wire [2:0] ALUOp_03, cal_r_ALURtChoose, cal_r_cal_i_load_store_ALURsChoose;
  wire [4:0] multiplexer_3_out, Rd_D, Rd_W, Rs_D, Rs_W, Rt_D, Rt_W;
  wire [15:0] imm_D, imm_E;
  wire [25:0] ins_index_D;
  wire [31:0] ALU_C, ALU_M, ALU_W, DM_M, DM_W, EXT_immhasexted, IR_D, IR_E, IR_F, IR_M, IR_W,
       multiplexer_1_out, multiplexer_2_out, multiplexer_4_out, multiplexer_5_out, multiplexer_6_out,
       multiplexer_7_out, multiplexer_8_out, multiplexer_10_out, NPC, PC4_D, PC4_E, PC4_M, PC4_W, PC8_D,
       PC8_E, PC8_M, PC8_W, PC_D, PC_E, PC_F, PC_M, PC_W, RD1_D, RD1_E, RD2_D, RD2_E, Rt_E, Rt_M;

  Clock clock_1 (.out(clk));
  // Probe on PC_F
  PC_02 PC (.NPC(NPC), .clk(clk), .rst(rst), .en(not_1_out), .PC(PC_F));
  not not_1 (not_1_out, stallPC);
  IM_01 IM (.PC(PC_F), .Ins(IR_F));
  // Probe on PC_D
  // Probe on IR_D
  // Probe on NPC
  // Probe on stallPC
  // Probe on stallID
  // Probe on flushEX
  // Probe on JReg_RsChoose
  // Probe on Beq_RsChoose
  // Probe on Beq_RtChoose
  // Probe on cal_r_cal_i_load_store_ALURsChoose
  // Probe on cal_r_ALURtChoose
  // Probe on store_RtChoose_M
  // Probe on store_RtChoose_E
  // Probe on PC_E
  // Probe on IR_E
  ID_beforeD ID (
    .IR_F(IR_F), .PC_F(PC_F), .IR_D(IR_D), .PC_D(PC_D), .PC4_D(PC4_D), .PC8_D(PC8_D), .clk(clk), .reset(rst),
    .en(not_2_out));
  not not_2 (not_2_out, stallID);
  // Probe on PC_M
  // Probe on IR_M
  Controller_08 Controller (
    .ins(IR_D), .NPC_isJr_01(NPC_isJr_01), .NPC_isJal_02(NPC_isJal_02), .NPC_isBranch_03(NPC_isBranch_03),
    .Rs(Rs_D), .Rt(Rt_D), .Rd(Rd_D), .imm(imm_D), .ins_index(ins_index_D));  // open: GRF_A3_01, GRF_WE_02, GRF_WD_03, ALU_B_01, ALU_immExt_02, ALU_Op_03, DM_WE_01
  // Probe on PC_W
  // Probe on IR_W
  Hazard_10 Hazard (.IR_D(IR_D), .IR_E(IR_E), .IR_M(IR_M), .stallPC(stallPC), .stallID(stallID), .flushEX(flushEX));
  Multiplexer #(.select(2), .width(32), .enable("false")) multiplexer_1 (
    .in0(RD1_D), .in1(PC8_M), .in2(ALU_M), .out(multiplexer_1_out), .sel(Beq_RsChoose));  // open: in3
  Multiplexer #(.select(2), .width(32), .enable("false")) multiplexer_2 (
    .in0(RD2_D), .in1(PC8_M), .in2(ALU_M), .out(multiplexer_2_out), .sel(Beq_RtChoose));  // open: in3
  Multiplexer #(.select(2), .width(5), .enable("false")) multiplexer_3 (
    .in0(Rd_W), .in1(Rt_W), .in2({5{1'b1}}), .out(multiplexer_3_out), .sel(GRF_A3_01));  // open: in3
  Multiplexer #(.select(2), .width(32), .enable("false")) multiplexer_4 (
    .in0(ALU_W), .in1(DM_W), .in2(PC8_W), .out(multiplexer_4_out), .sel(GRF_WD_03));  // open: in3
  Multiplexer #(.select(2), .width(32), .enable("false")) multiplexer_5 (
    .in0(RD1_D), .in1(PC8_M), .in2(ALU_M), .out(multiplexer_5_out), .sel(JReg_RsChoose));  // open: in3
  CMP_09 CMP (.Rs(multiplexer_1_out), .Rt(multiplexer_2_out), .isEqual(CMP_isequal));
  Forward_11 Forward (
    .IR_D(IR_D), .IR_E(IR_E), .IR_M(IR_M), .IR_W(IR_W), .JReg_NPCRsChoose(JReg_RsChoose),
    .Beq_CMPRsChoose(Beq_RsChoose), .Beq_CMPRtChoose(Beq_RtChoose),
    .cal_r_cal_i_LoadStore_ALURsChoose(cal_r_cal_i_load_store_ALURsChoose),
    .cal_r_ALURtChoose(cal_r_ALURtChoose), .store_RtChoose_M(store_RtChoose_M),
    .store_RtChoose_E(store_RtChoose_E));
  NPC_03 u_NPC (
    .PC_F(PC_F), .Rs(multiplexer_5_out), .imm(imm_D), .ins_index(ins_index_D), .isJr(NPC_isJr_01),
    .isJal(NPC_isJal_02), .isBranch(NPC_isBranch_03), .isBranchSuccess(CMP_isequal), .NPC(NPC), .PC_D(PC_D));
  GRF_04 GRF (
    .A1(Rs_D), .A2(Rt_D), .A3(multiplexer_3_out), .WD(multiplexer_4_out), .RD1(RD1_D), .RD2(RD2_D),
    .clk(clk), .rst(rst), .WE(GRF_WE_02));
  or or_1 (or_1_out, rst, flushEX);
  EX_beforeE EX (
    .IR_D(IR_D), .PC_D(PC_D), .PC4_D(PC4_D), .PC8_D(PC8_D), .RF_RD1(RD1_D), .RF_RD2(RD2_D), .IR_E(IR_E),
    .PC_E(PC_E), .PC4_E(PC4_E), .PC8_E(PC8_E), .RS_E(RD1_E), .RT_E(RD2_E), .clk(clk), .reset(or_1_out),
    .en(1'b1));  // open: EXT, EXT_E
  Controller_08 Controller_2 (
    .ins(IR_E), .ALU_B_01(ALU_B_01), .ALU_immExt_02(ALU_immExt_02), .ALU_Op_03(ALUOp_03), .imm(imm_E));  // open: GRF_A3_01, GRF_WE_02, GRF_WD_03, DM_WE_01, NPC_isJr_01, NPC_isJal_02, NPC_isBranch_03, Rs, Rt, Rd, ins_index
  Multiplexer #(.select(3), .width(32), .enable("false")) multiplexer_6 (
    .in0(RD2_E), .in1(PC8_W), .in2(DM_W), .in3(ALU_W), .in4(PC8_M), .in5(ALU_M), .out(multiplexer_6_out),
    .sel(cal_r_ALURtChoose));  // open: in6, in7
  EXT_07 EXT (.imm(imm_E), .zeroOrSigned(ALU_immExt_02), .immHasExted(EXT_immhasexted));
  Multiplexer #(.select(3), .width(32), .enable("false")) multiplexer_7 (
    .in0(RD1_E), .in1(PC8_W), .in2(DM_W), .in3(ALU_W), .in4(PC8_M), .in5(ALU_M), .out(multiplexer_7_out),
    .sel(cal_r_cal_i_load_store_ALURsChoose));  // open: in6, in7
  Multiplexer #(.width(32), .enable("false")) multiplexer_8 (
    .in0(multiplexer_6_out), .in1(EXT_immhasexted), .out(multiplexer_8_out), .sel(ALU_B_01));
  ALU_05 ALU (.A(multiplexer_7_out), .B(multiplexer_8_out), .ALUOp(ALUOp_03), .C(ALU_C));
  Multiplexer #(.select(2), .width(32), .enable("false")) multiplexer_9 (
    .in0(RD2_E), .in1(PC8_W), .in2(DM_W), .in3(ALU_W), .out(Rt_E), .sel(store_RtChoose_E));
  MEM_beforeM MEM (
    .IR_E(IR_E), .PC_E(PC_E), .PC4_E(PC4_E), .PC8_E(PC8_E), .ALU(ALU_C), .RT_E(Rt_E), .IR_M(IR_M),
    .PC_M(PC_M), .PC4_M(PC4_M), .PC8_M(PC8_M), .A0_M(ALU_M), .RT_M(Rt_M), .clk(clk), .reset(rst), .en(1'b1));
  Controller_08 Controller_3 (
    .ins(IR_M), .DM_WE_01(DM_WE));  // open: GRF_A3_01, GRF_WE_02, GRF_WD_03, ALU_B_01, ALU_immExt_02, ALU_Op_03, NPC_isJr_01, NPC_isJal_02, NPC_isBranch_03, Rs, Rt, Rd, imm, ins_index
  Multiplexer #(.select(2), .width(32), .enable("false")) multiplexer_10 (
    .in0(Rt_M), .in1(PC8_W), .in2(DM_W), .in3(ALU_W), .out(multiplexer_10_out), .sel(store_RtChoose_M));
  DM_06 DM (.A(ALU_M), .WD(multiplexer_10_out), .RD(DM_M), .WE(DM_WE), .clk(clk), .reset(rst));
  WB_beforeW WB (
    .IR_M(IR_M), .PC_M(PC_M), .PC4_M(PC4_M), .PC8_M(PC8_M), .A0_M(ALU_M), .DM(DM_M), .IR_W(IR_W),
    .PC_W(PC_W), .PC4_W(PC4_W), .PC8_W(PC8_W), .A0_W(ALU_W), .DR_W(DM_W), .clk(clk), .reset(rst), .en(1'b1));
  Controller_08 Controller_4 (
    .ins(IR_W), .GRF_A3_01(GRF_A3_01), .GRF_WE_02(GRF_WE_02), .GRF_WD_03(GRF_WD_03), .Rs(Rs_W), .Rt(Rt_W),
    .Rd(Rd_W));  // open: ALU_B_01, ALU_immExt_02, ALU_Op_03, DM_WE_01, NPC_isJr_01, NPC_isJal_02, NPC_isBranch_03, imm, ins_index

  // Notes on the sheet:
  //   F
  //   D
  //   E
  //   M
  //   W:1.Controller用于GRF 2.从Ins中解读Rs Rt Rd
  //   W
endmodule

module CMP_09 (
  input  [31:0] Rs,
  input  [31:0] Rt,
  output isEqual
);

  Comparator #(.width(32)) comparator_1 (.a(Rs), .b(Rt), .eq(isEqual));  // open: gt, lt
endmodule

module Hazard_10 (
  input  [31:0] IR_D,
  input  [31:0] IR_E,
  input  [31:0] IR_M,
  output stallPC,
  output stallID,
  output flushEX
);

  wire and_1_out, and_2_out, and_3_out, and_4_out, and_5_out, and_6_out, and_7_out, and_8_out, and_9_out,
       and_13_out, BeqStall_12, comparator_1_eq, comparator_2_eq, comparator_3_eq, comparator_4_eq,
       comparator_5_eq, comparator_6_eq, comparator_7_eq, comparator_8_eq, comparator_9_eq, comparator_10_eq,
       comparator_11_eq, comparator_12_eq, comparator_13_eq, comparator_14_eq, comparator_15_eq,
       comparator_16_eq, isBeq_D, isBeq_E, isBeq_M, isCal_i_D, isCal_i_E, isCal_i_M, isCal_r_D, isCal_r_E,
       isCal_r_M, isJal_D, isJal_E, isJal_M, isJReg_D, isJReg_E, isJReg_M, isLoad_D, isLoad_E, isLoad_M,
       isRead_D, isRead_E, isRead_M, isStore_D, isStore_E, isStore_M, isWrite_D, isWrite_E, isWrite_M,
       JRegBeqLoadStall_13, JRegStall_12, not_1_out, not_2_out, not_3_out, not_4_out, not_5_out, not_6_out,
       not_7_out, not_8_out, not_9_out, not_10_out, or_1_out, or_2_out, or_3_out, or_4_out, ReadLoadStall_12;
  wire [4:0] Rd_D, Rd_E, Rd_M, Rs_D, Rs_E, Rs_M, Rt_D, Rt_E, Rt_M, WriteDes_D, WriteDes_E, WriteDes_M;

  IRJudge_12 irjudge_12_1 (
    .ins(IR_D), .isCal_r(isCal_r_D), .isJReg(isJReg_D), .isCal_i(isCal_i_D), .isBeq(isBeq_D),
    .isLoad(isLoad_D), .isStore(isStore_D), .isJal(isJal_D), .Rs(Rs_D), .Rt(Rt_D), .Rd(Rd_D),
    .WriteDes(WriteDes_D), .isWrite(isWrite_D), .isRead(isRead_D));  // open: isNeedALURs
  IRJudge_12 irjudge_12_2 (
    .ins(IR_E), .isCal_r(isCal_r_E), .isJReg(isJReg_E), .isCal_i(isCal_i_E), .isBeq(isBeq_E),
    .isLoad(isLoad_E), .isStore(isStore_E), .isJal(isJal_E), .Rs(Rs_E), .Rt(Rt_E), .Rd(Rd_E),
    .WriteDes(WriteDes_E), .isWrite(isWrite_E), .isRead(isRead_E));  // open: isNeedALURs
  IRJudge_12 irjudge_12_3 (
    .ins(IR_M), .isCal_r(isCal_r_M), .isJReg(isJReg_M), .isCal_i(isCal_i_M), .isBeq(isBeq_M),
    .isLoad(isLoad_M), .isStore(isStore_M), .isJal(isJal_M), .Rs(Rs_M), .Rt(Rt_M), .Rd(Rd_M),
    .WriteDes(WriteDes_M), .isWrite(isWrite_M), .isRead(isRead_M));  // open: isNeedALURs
  Comparator #(.width(5)) comparator_1 (.a(Rs_D), .b(WriteDes_M), .eq(comparator_1_eq));  // open: gt, lt
  not not_1 (not_1_out, comparator_2_eq);
  Comparator #(.width(5)) comparator_2 (.a(Rs_D), .b({5{1'b0}}), .eq(comparator_2_eq));  // open: gt, lt
  Comparator #(.width(5)) comparator_3 (.a(Rs_D), .b(WriteDes_M), .eq(comparator_3_eq));  // open: gt, lt
  Comparator #(.width(5)) comparator_4 (.a(Rs_D), .b({5{1'b0}}), .eq(comparator_4_eq));  // open: gt, lt
  Comparator #(.width(5)) comparator_5 (.a(Rt_D), .b(WriteDes_M), .eq(comparator_5_eq));  // open: gt, lt
  Comparator #(.width(5)) comparator_6 (.a(Rt_D), .b({5{1'b0}}), .eq(comparator_6_eq));  // open: gt, lt
  not not_2 (not_2_out, isJal_E);
  Comparator #(.width(5)) comparator_7 (.a(Rs_D), .b(WriteDes_E), .eq(comparator_7_eq));  // open: gt, lt
  Comparator #(.width(5)) comparator_8 (.a(Rs_D), .b({5{1'b0}}), .eq(comparator_8_eq));  // open: gt, lt
  not not_3 (not_3_out, comparator_8_eq);
  not not_4 (not_4_out, isJal_E);
  Comparator #(.width(5)) comparator_9 (.a(Rs_D), .b(WriteDes_E), .eq(comparator_9_eq));  // open: gt, lt
  not not_5 (not_5_out, comparator_10_eq);
  Comparator #(.width(5)) comparator_10 (.a(Rs_D), .b({5{1'b0}}), .eq(comparator_10_eq));  // open: gt, lt
  Comparator #(.width(5)) comparator_11 (.a(Rt_D), .b(WriteDes_E), .eq(comparator_11_eq));  // open: gt, lt
  not not_6 (not_6_out, comparator_12_eq);
  Comparator #(.width(5)) comparator_12 (.a(Rt_D), .b({5{1'b0}}), .eq(comparator_12_eq));  // open: gt, lt
  Comparator #(.width(5)) comparator_13 (.a(Rs_D), .b(WriteDes_E), .eq(comparator_13_eq));  // open: gt, lt
  Comparator #(.width(5)) comparator_14 (.a(Rs_D), .b({5{1'b0}}), .eq(comparator_14_eq));  // open: gt, lt
  not not_7 (not_7_out, comparator_14_eq);
  Comparator #(.width(5)) comparator_15 (.a(Rt_D), .b(WriteDes_E), .eq(comparator_15_eq));  // open: gt, lt
  not not_8 (not_8_out, comparator_16_eq);
  Comparator #(.width(5)) comparator_16 (.a(Rt_D), .b({5{1'b0}}), .eq(comparator_16_eq));  // open: gt, lt
  and and_1 (and_1_out, comparator_1_eq, not_1_out);
  and and_2 (and_2_out, comparator_3_eq, not_9_out);
  not not_9 (not_9_out, comparator_4_eq);
  and and_3 (and_3_out, comparator_5_eq, not_10_out);
  not not_10 (not_10_out, comparator_6_eq);
  and and_4 (and_4_out, comparator_7_eq, not_3_out);
  and and_5 (and_5_out, comparator_9_eq, not_5_out);
  or or_1 (or_1_out, and_5_out, and_6_out);
  and and_6 (and_6_out, comparator_11_eq, not_6_out);
  and and_7 (and_7_out, comparator_13_eq, not_7_out);
  or or_2 (or_2_out, and_7_out, and_8_out);
  and and_8 (and_8_out, isCal_r_D, comparator_15_eq, not_8_out);
  and and_9 (and_9_out, isJReg_D, and_1_out);
  or or_3 (or_3_out, and_2_out, and_3_out);
  and and_10 (JRegStall_12, isJReg_D, isWrite_E, not_2_out, and_4_out);
  and and_11 (BeqStall_12, isBeq_D, isWrite_E, not_4_out, or_1_out);
  and and_12 (ReadLoadStall_12, isRead_D, isLoad_E, or_2_out);
  and and_13 (and_13_out, isBeq_D, or_3_out);
  and and_14 (JRegBeqLoadStall_13, isLoad_M, or_4_out);
  or or_4 (or_4_out, and_9_out, and_13_out);
  or or_5 (flushEX, JRegStall_12, BeqStall_12, ReadLoadStall_12, JRegBeqLoadStall_13);

  assign stallID = flushEX;
  assign stallPC = flushEX;

  // Notes on the sheet:
  //   D:JReg的暂停情况
  //   D:Beq的暂停情况
  //   D:D要ReadE为Load的暂停情况
  //   D:D为JReg或Beq M为load的暂停情况
endmodule

module Forward_11 (
  input  [31:0] IR_D,
  input  [31:0] IR_E,
  input  [31:0] IR_M,
  input  [31:0] IR_W,
  output [1:0] JReg_NPCRsChoose,
  output [1:0] Beq_CMPRsChoose,
  output [1:0] Beq_CMPRtChoose,
  output [2:0] cal_r_cal_i_LoadStore_ALURsChoose,
  output [2:0] cal_r_ALURtChoose,
  output [1:0] store_RtChoose_M,
  output [1:0] store_RtChoose_E
);

  wire ALURs_001_PC8_W, ALURs_010_DM_W, ALURs_011_ALU_W, ALURs_100_PC8_M, ALURs_101_ALU_M, ALURt_001_PC8_W,
       ALURt_010_DM_W, ALURt_011_ALU_W, ALURt_100_PC8_M, ALURt_101_ALU_M, and_20_out, and_21_out, and_22_out,
       and_23_out, and_24_out, and_25_out, CMPRs_NeedForward, CMPRt_NeedForward, comparator_1_eq,
       comparator_2_eq, comparator_3_eq, comparator_4_eq, comparator_5_eq, comparator_6_eq, comparator_7_eq,
       comparator_8_eq, comparator_9_eq, comparator_10_eq, comparator_11_eq, comparator_12_eq,
       comparator_13_eq, comparator_14_eq, comparator_15_eq, comparator_16_eq, comparator_17_eq,
       comparator_18_eq, comparator_19_eq, comparator_20_eq, comparator_21_eq, comparator_22_eq,
       comparator_23_eq, comparator_24_eq, comparator_25_eq, comparator_26_eq, comparator_27_eq,
       comparator_28_eq, comparator_29_eq, comparator_30_eq, comparator_31_eq, comparator_32_eq,
       DMRt_001_PC8_W, DMRt_010_DM_W, DMRt_011_ALU_W, isBeq_D, isBeq_E, isBeq_M, isBeq_W, isCal_i_D,
       isCal_i_E, isCal_i_M, isCal_i_W, isCal_r_D, isCal_r_E, isCal_r_M, isCal_r_W, isJal_D, isJal_E,
       isJal_M, isJal_W, isJReg_D, isJReg_E, isJReg_M, isJReg_W, isLoad_D, isLoad_E, isLoad_M, isLoad_W,
       isNeedALURs_D, isNeedALURs_E, isNeedALURs_M, isNeedALURs_W, isRead_D, isRead_E, isRead_M, isRead_W,
       isStore_D, isStore_E, isStore_M, isStore_W, isWrite_D, isWrite_E, isWrite_M, isWrite_W, not_1_out,
       not_2_out, not_3_out, not_4_out, not_5_out, not_6_out, not_7_out, not_8_out, not_9_out, not_10_out,
       not_11_out, not_12_out, not_13_out, not_14_out, not_15_out, not_16_out, NPCRs_NeedForward, or_1_out,
       or_2_out, or_3_out, or_4_out, or_5_out, or_6_out, or_7_out, or_8_out, or_9_out, RtE_001_PC8_W,
       RtE_010_DM_W, RtE_011_ALU_W;
  wire [1:0] multiplexer_3_out, multiplexer_4_out, multiplexer_7_out, multiplexer_8_out, multiplexer_9_out,
       multiplexer_10_out, multiplexer_11_out;
  wire [2:0] multiplexer_1_out, multiplexer_2_out, multiplexer_5_out, multiplexer_6_out, multiplexer_12_out,
       multiplexer_13_out, multiplexer_19_out, multiplexer_21_out;
  wire [4:0] Rd_D, Rd_E, Rd_M, Rd_W, Rs_D, Rs_E, Rs_M, Rs_W, Rt_D, Rt_E, Rt_M, Rt_W, WriteDes_D, WriteDes_E,
       WriteDes_M, WriteDes_W;

  IRJudge_12 irjudge_12_1 (
    .ins(IR_D), .isCal_r(isCal_r_D), .isJReg(isJReg_D), .isCal_i(isCal_i_D), .isBeq(isBeq_D),
    .isLoad(isLoad_D), .isStore(isStore_D), .isJal(isJal_D), .Rs(Rs_D), .Rt(Rt_D), .Rd(Rd_D),
    .WriteDes(WriteDes_D), .isWrite(isWrite_D), .isRead(isRead_D), .isNeedALURs(isNeedALURs_D));
  IRJudge_12 irjudge_12_2 (
    .ins(IR_E), .isCal_r(isCal_r_E), .isJReg(isJReg_E), .isCal_i(isCal_i_E), .isBeq(isBeq_E),
    .isLoad(isLoad_E), .isStore(isStore_E), .isJal(isJal_E), .Rs(Rs_E), .Rt(Rt_E), .Rd(Rd_E),
    .WriteDes(WriteDes_E), .isWrite(isWrite_E), .isRead(isRead_E), .isNeedALURs(isNeedALURs_E));
  IRJudge_12 irjudge_12_3 (
    .ins(IR_M), .isCal_r(isCal_r_M), .isJReg(isJReg_M), .isCal_i(isCal_i_M), .isBeq(isBeq_M),
    .isLoad(isLoad_M), .isStore(isStore_M), .isJal(isJal_M), .Rs(Rs_M), .Rt(Rt_M), .Rd(Rd_M),
    .WriteDes(WriteDes_M), .isWrite(isWrite_M), .isRead(isRead_M), .isNeedALURs(isNeedALURs_M));
  IRJudge_12 irjudge_12_4 (
    .ins(IR_W), .isCal_r(isCal_r_W), .isJReg(isJReg_W), .isCal_i(isCal_i_W), .isBeq(isBeq_W),
    .isLoad(isLoad_W), .isStore(isStore_W), .isJal(isJal_W), .Rs(Rs_W), .Rt(Rt_W), .Rd(Rd_W),
    .WriteDes(WriteDes_W), .isWrite(isWrite_W), .isRead(isRead_W), .isNeedALURs(isNeedALURs_W));
  or or_1 (or_1_out, isCal_r_M, isCal_i_M);
  or or_2 (or_2_out, isCal_r_W, isCal_i_W);
  or or_3 (or_3_out, isCal_r_M, isCal_i_M);
  or or_4 (or_4_out, isCal_r_W, isCal_i_W);
  or or_5 (or_5_out, isCal_r_W, isCal_i_W);
  Comparator #(.width(5)) comparator_1 (.a(Rt_M), .b(WriteDes_W), .eq(comparator_1_eq));  // open: gt, lt
  Comparator #(.width(5)) comparator_2 (.a(Rt_M), .b({5{1'b0}}), .eq(comparator_2_eq));  // open: gt, lt
  Comparator #(.width(5)) comparator_3 (.a(Rt_M), .b(WriteDes_W), .eq(comparator_3_eq));  // open: gt, lt
  Comparator #(.width(5)) comparator_4 (.a(Rt_M), .b({5{1'b0}}), .eq(comparator_4_eq));  // open: gt, lt
  Comparator #(.width(5)) comparator_5 (.a(Rt_M), .b(WriteDes_W), .eq(comparator_5_eq));  // open: gt, lt
  or or_6 (or_6_out, isCal_r_W, isCal_i_W);
  Comparator #(.width(5)) comparator_6 (.a(Rt_E), .b(WriteDes_W), .eq(comparator_6_eq));  // open: gt, lt
  Comparator #(.width(5)) comparator_7 (.a(Rt_E), .b({5{1'b0}}), .eq(comparator_7_eq));  // open: gt, lt
  Comparator #(.width(5)) comparator_8 (.a(Rt_E), .b(WriteDes_W), .eq(comparator_8_eq));  // open: gt, lt
  Comparator #(.width(5)) comparator_9 (.a(Rt_E), .b({5{1'b0}}), .eq(comparator_9_eq));  // open: gt, lt
  Comparator #(.width(5)) comparator_10 (.a(Rt_E), .b(WriteDes_W), .eq(comparator_10_eq));  // open: gt, lt
  not not_1 (not_1_out, isLoad_M);
  Comparator #(.width(5)) comparator_11 (.a(Rs_D), .b(WriteDes_M), .eq(comparator_11_eq));  // open: gt, lt
  not not_2 (not_2_out, comparator_12_eq);
  Comparator #(.width(5)) comparator_12 (.a(Rs_D), .b({5{1'b0}}), .eq(comparator_12_eq));  // open: gt, lt
  not not_3 (not_3_out, isLoad_M);
  Comparator #(.width(5)) comparator_13 (.a(Rs_D), .b(WriteDes_M), .eq(comparator_13_eq));  // open: gt, lt
  not not_4 (not_4_out, comparator_14_eq);
  Comparator #(.width(5)) comparator_14 (.a(Rs_D), .b({5{1'b0}}), .eq(comparator_14_eq));  // open: gt, lt
  not not_5 (not_5_out, isLoad_M);
  Comparator #(.width(5)) comparator_15 (.a(Rt_D), .b(WriteDes_M), .eq(comparator_15_eq));  // open: gt, lt
  Comparator #(.width(5)) comparator_16 (.a(Rt_D), .b({5{1'b0}}), .eq(comparator_16_eq));  // open: gt, lt
  not not_6 (not_6_out, comparator_16_eq);
  Comparator #(.width(5)) comparator_17 (.a(Rs_E), .b(WriteDes_M), .eq(comparator_17_eq));  // open: gt, lt
  not not_7 (not_7_out, comparator_18_eq);
  Comparator #(.width(5)) comparator_18 (.a(Rs_E), .b({5{1'b0}}), .eq(comparator_18_eq));  // open: gt, lt
  Comparator #(.width(5)) comparator_19 (.a(Rs_E), .b(WriteDes_M), .eq(comparator_19_eq));  // open: gt, lt
  Comparator #(.width(5)) comparator_20 (.a(Rs_E), .b(WriteDes_W), .eq(comparator_20_eq));  // open: gt, lt
  not not_8 (not_8_out, comparator_21_eq);
  Comparator #(.width(5)) comparator_21 (.a(Rs_E), .b({5{1'b0}}), .eq(comparator_21_eq));  // open: gt, lt
  Comparator #(.width(5)) comparator_22 (.a(Rs_E), .b(WriteDes_W), .eq(comparator_22_eq));  // open: gt, lt
  Comparator #(.width(5)) comparator_23 (.a(Rs_E), .b({5{1'b0}}), .eq(comparator_23_eq));  // open: gt, lt
  not not_9 (not_9_out, comparator_23_eq);
  Comparator #(.width(5)) comparator_24 (.a(Rs_E), .b(WriteDes_W), .eq(comparator_24_eq));  // open: gt, lt
  Comparator #(.width(5)) comparator_25 (.a(Rt_E), .b(WriteDes_M), .eq(comparator_25_eq));  // open: gt, lt
  not not_10 (not_10_out, comparator_26_eq);
  Comparator #(.width(5)) comparator_26 (.a(Rt_E), .b({5{1'b0}}), .eq(comparator_26_eq));  // open: gt, lt
  Comparator #(.width(5)) comparator_27 (.a(Rt_E), .b(WriteDes_M), .eq(comparator_27_eq));  // open: gt, lt
  Comparator #(.width(5)) comparator_28 (.a(Rt_E), .b(WriteDes_W), .eq(comparator_28_eq));  // open: gt, lt
  not not_11 (not_11_out, comparator_29_eq);
  Comparator #(.width(5)) comparator_29 (.a(Rt_E), .b({5{1'b0}}), .eq(comparator_29_eq));  // open: gt, lt
  Comparator #(.width(5)) comparator_30 (.a(Rt_E), .b(WriteDes_W), .eq(comparator_30_eq));  // open: gt, lt
  not not_12 (not_12_out, comparator_31_eq);
  Comparator #(.width(5)) comparator_31 (.a(Rt_E), .b({5{1'b0}}), .eq(comparator_31_eq));  // open: gt, lt
  Comparator #(.width(5)) comparator_32 (.a(Rt_E), .b(WriteDes_W), .eq(comparator_32_eq));  // open: gt, lt
  not not_13 (not_13_out, comparator_2_eq);
  not not_14 (not_14_out, comparator_4_eq);
  not not_15 (not_15_out, comparator_7_eq);
  not not_16 (not_16_out, comparator_9_eq);
  and and_1 (RtE_011_ALU_W, isStore_E, or_6_out, comparator_6_eq, not_15_out);
  and and_2 (RtE_010_DM_W, isStore_E, isLoad_W, comparator_8_eq, not_16_out);
  and and_3 (RtE_001_PC8_W, isStore_E, isJal_W, comparator_10_eq);
  and and_4 (NPCRs_NeedForward, isJReg_D, isWrite_M, not_1_out, comparator_11_eq, not_2_out);
  and and_5 (CMPRs_NeedForward, isBeq_D, isWrite_M, not_3_out, comparator_13_eq, not_4_out);
  and and_6 (CMPRt_NeedForward, isBeq_D, isWrite_M, not_5_out, comparator_15_eq, not_6_out);
  and and_7 (ALURs_101_ALU_M, isNeedALURs_E, or_1_out, comparator_17_eq, not_7_out);
  and and_8 (ALURs_100_PC8_M, isNeedALURs_E, isJal_M, comparator_19_eq);
  and and_9 (ALURs_011_ALU_W, isNeedALURs_E, or_2_out, comparator_20_eq, not_8_out);
  and and_10 (ALURs_010_DM_W, isNeedALURs_E, isLoad_W, comparator_22_eq, not_9_out);
  and and_11 (ALURs_001_PC8_W, isNeedALURs_E, isJal_W, comparator_24_eq);
  and and_12 (ALURt_101_ALU_M, isCal_r_E, or_3_out, comparator_25_eq, not_10_out);
  and and_13 (ALURt_100_PC8_M, isCal_r_E, isJal_M, comparator_27_eq);
  and and_14 (ALURt_011_ALU_W, isCal_r_E, or_4_out, comparator_28_eq, not_11_out);
  and and_15 (ALURt_010_DM_W, isCal_r_E, isLoad_W, comparator_30_eq, not_12_out);
  and and_16 (ALURt_001_PC8_W, isCal_r_E, isJal_W, comparator_32_eq);
  and and_17 (DMRt_011_ALU_W, isStore_M, or_5_out, comparator_1_eq, not_13_out);
  and and_18 (DMRt_010_DM_W, isStore_M, isLoad_W, comparator_3_eq, not_14_out);
  and and_19 (DMRt_001_PC8_W, isStore_M, isJal_W, comparator_5_eq);
  Multiplexer #(.width(3), .enable("false")) multiplexer_1 (
    .in0(3'b000), .in1(3'b001), .out(multiplexer_1_out), .sel(ALURs_001_PC8_W));
  Multiplexer #(.width(3), .enable("false")) multiplexer_2 (
    .in0(3'b000), .in1(3'b001), .out(multiplexer_2_out), .sel(ALURt_001_PC8_W));
  Multiplexer #(.width(2), .enable("false")) multiplexer_3 (
    .in0(2'b00), .in1(2'b01), .out(multiplexer_3_out), .sel(DMRt_001_PC8_W));
  Multiplexer #(.width(2), .enable("false")) multiplexer_4 (
    .in0(2'b00), .in1(2'b01), .out(multiplexer_4_out), .sel(RtE_001_PC8_W));
  and and_20 (and_20_out, isJal_M, NPCRs_NeedForward);
  and and_21 (and_21_out, isJal_M, CMPRt_NeedForward);
  Multiplexer #(.width(3), .enable("false")) multiplexer_5 (
    .in0(multiplexer_1_out), .in1(3'b010), .out(multiplexer_5_out), .sel(ALURs_010_DM_W));
  Multiplexer #(.width(3), .enable("false")) multiplexer_6 (
    .in0(multiplexer_2_out), .in1(3'b010), .out(multiplexer_6_out), .sel(ALURt_010_DM_W));
  Multiplexer #(.width(2), .enable("false")) multiplexer_7 (
    .in0(multiplexer_3_out), .in1(2'b10), .out(multiplexer_7_out), .sel(DMRt_010_DM_W));
  Multiplexer #(.width(2), .enable("false")) multiplexer_8 (
    .in0(multiplexer_4_out), .in1(2'b10), .out(multiplexer_8_out), .sel(RtE_010_DM_W));
  Multiplexer #(.width(2), .enable("false")) multiplexer_9 (
    .in0(2'b00), .in1(2'b01), .out(multiplexer_9_out), .sel(and_20_out));
  and and_22 (and_22_out, or_7_out, NPCRs_NeedForward);
  or or_7 (or_7_out, isCal_r_M, isCal_i_M);
  Multiplexer #(.width(2), .enable("false")) multiplexer_10 (
    .in0(2'b00), .in1(2'b01), .out(multiplexer_10_out), .sel(and_23_out));
  and and_23 (and_23_out, isJal_M, CMPRs_NeedForward);
  or or_8 (or_8_out, isCal_r_M, isCal_i_M);
  Multiplexer #(.width(2), .enable("false")) multiplexer_11 (
    .in0(2'b00), .in1(2'b01), .out(multiplexer_11_out), .sel(and_21_out));
  and and_24 (and_24_out, or_9_out, CMPRt_NeedForward);
  or or_9 (or_9_out, isCal_r_M, isCal_i_M);
  Multiplexer #(.width(3), .enable("false")) multiplexer_12 (
    .in0(multiplexer_5_out), .in1(3'b011), .out(multiplexer_12_out), .sel(ALURs_011_ALU_W));
  Multiplexer #(.width(3), .enable("false")) multiplexer_13 (
    .in0(multiplexer_6_out), .in1(3'b011), .out(multiplexer_13_out), .sel(ALURt_011_ALU_W));
  Multiplexer #(.width(2), .enable("false")) multiplexer_14 (
    .in0(multiplexer_7_out), .in1(2'b11), .out(store_RtChoose_M), .sel(DMRt_011_ALU_W));
  Multiplexer #(.width(2), .enable("false")) multiplexer_15 (
    .in0(multiplexer_8_out), .in1(2'b11), .out(store_RtChoose_E), .sel(RtE_011_ALU_W));
  Multiplexer #(.width(2), .enable("false")) multiplexer_16 (
    .in0(multiplexer_9_out), .in1(2'b10), .out(JReg_NPCRsChoose), .sel(and_22_out));
  Multiplexer #(.width(2), .enable("false")) multiplexer_17 (
    .in0(multiplexer_10_out), .in1(2'b10), .out(Beq_CMPRsChoose), .sel(and_25_out));
  and and_25 (and_25_out, or_8_out, CMPRs_NeedForward);
  Multiplexer #(.width(2), .enable("false")) multiplexer_18 (
    .in0(multiplexer_11_out), .in1(2'b10), .out(Beq_CMPRtChoose), .sel(and_24_out));
  Multiplexer #(.width(3), .enable("false")) multiplexer_19 (
    .in0(multiplexer_12_out), .in1(3'b100), .out(multiplexer_19_out), .sel(ALURs_100_PC8_M));
  Multiplexer #(.width(3), .enable("false")) multiplexer_20 (
    .in0(multiplexer_19_out), .in1(3'b101), .out(cal_r_cal_i_LoadStore_ALURsChoose), .sel(ALURs_101_ALU_M));
  Multiplexer #(.width(3), .enable("false")) multiplexer_21 (
    .in0(multiplexer_13_out), .in1(3'b100), .out(multiplexer_21_out), .sel(ALURt_100_PC8_M));
  Multiplexer #(.width(3), .enable("false")) multiplexer_22 (
    .in0(multiplexer_21_out), .in1(3'b101), .out(cal_r_ALURtChoose), .sel(ALURt_101_ALU_M));

  // Notes on the sheet:
  //   D:JReg的转发，选NPC的Rs
  //   D:Beq的转发，选CMP的Rs
  //   E:cal_r的转发，选ALU的Rt
  //   M:store的Rt转发，选DM的Rt
  //   E:cal_r cal_i load store的转发，选ALU的Rs
  //   M:store的Rt转发，E阶段时Store的Rt，进入Rt_M作为00
endmodule

// IRJudge
module IRJudge_12 (
  input  [31:0] ins,
  output isCal_r,
  output isJReg,
  output isCal_i,
  output isBeq,
  output isLoad,
  output isStore,
  output isJal,
  output [4:0] Rs,
  output [4:0] Rt,
  output [4:0] Rd,
  output isRead,
  output isWrite,
  output [4:0] WriteDes,
  output isNeedALURs
);

  wire addu, isR, lui, not_1_out, not_2_out, not_3_out, not_4_out, not_5_out, not_6_out, not_7_out,
       not_8_out, not_9_out, not_10_out, not_11_out, not_12_out, or_3_out, ori, subu;
  wire [4:0] multiplexer_1_out, multiplexer_2_out;

  not not_1 (not_1_out, ins[31]);
  not not_2 (not_2_out, ins[28]);
  not not_3 (not_3_out, ins[29]);
  not not_4 (not_4_out, ins[30]);
  not not_5 (not_5_out, ins[27]);
  not not_6 (not_6_out, ins[26]);
  not not_7 (not_7_out, ins[5]);
  not not_8 (not_8_out, ins[4]);
  not not_9 (not_9_out, ins[3]);
  not not_10 (not_10_out, ins[2]);
  not not_11 (not_11_out, ins[0]);
  not not_12 (not_12_out, ins[1]);
  and and_1 (isR, not_1_out, not_4_out, not_3_out, not_2_out, not_5_out, not_6_out);
  and and_2 (addu, isR, ins[5], not_8_out, not_9_out, not_10_out, not_12_out, not_11_out);
  and and_3 (subu, isR, ins[5], not_8_out, not_9_out, not_10_out, ins[1], not_11_out);
  and and_4 (isJReg, isR, not_7_out, not_8_out, ins[3], not_10_out, not_12_out, not_11_out);
  and and_5 (ori, not_1_out, not_4_out, ins[29], ins[28], not_5_out, ins[26]);
  and and_6 (isLoad, ins[31], not_4_out, not_3_out, not_2_out, ins[27], ins[26]);
  and and_7 (isStore, ins[31], not_4_out, ins[29], not_2_out, ins[27], ins[26]);
  and and_8 (isBeq, not_1_out, not_4_out, not_3_out, ins[28], not_5_out, not_6_out);
  and and_9 (lui, not_1_out, not_4_out, ins[29], ins[28], ins[27], ins[26]);
  and and_10 (isJal, not_1_out, not_4_out, not_3_out, not_2_out, ins[27], ins[26]);
  Multiplexer #(.width(5), .enable("false")) multiplexer_1 (
    .in0({5{1'b0}}), .in1({5{1'b1}}), .out(multiplexer_1_out), .sel(isJal));
  or or_1 (isCal_r, addu, subu);
  or or_2 (isCal_i, ori, lui);
  Multiplexer #(.width(5), .enable("false")) multiplexer_2 (
    .in0(multiplexer_1_out), .in1(ins[20:16]), .out(multiplexer_2_out), .sel(or_3_out));
  or or_3 (or_3_out, isCal_i, isLoad);
  or or_4 (isRead, isCal_r, isJReg, isCal_i, isBeq, isLoad, isStore);
  or or_5 (isWrite, isCal_r, isCal_i, isLoad, isJal);
  Multiplexer #(.width(5), .enable("false")) multiplexer_3 (
    .in0(multiplexer_2_out), .in1(ins[15:11]), .out(WriteDes), .sel(isCal_r));
  or or_6 (isNeedALURs, isCal_r, isCal_i, isLoad, isStore);

  assign Rd = ins[15:11];
  assign Rs = ins[25:21];
  assign Rt = ins[20:16];

  // Other names for the same wires on the sheet: beq = isBeq; op[5:0] = ins[31:26]; func[5:0] = ins[5:0];
  //   imm[15:0] = ins[15:0]; ins_index[25:0] = ins[25:0]; shamt[4:0] = ins[10:6]; jal = isJal; jr = isJReg;
  //   lw = isLoad; sw = isStore

  // Notes on the sheet:
  //   R: addu 下一跳是PC+4
  //   R: subu 下一跳是PC+4
  //   R: jr 下一跳是Rs的内容
  //   I: ori 下一跳是PC+4
  //   I: lw 下一跳是PC+4
  //   I: sw 下一跳是PC+4
  //   I: lui 下一条是PC+4
  //   R
  //   I: beq 下一跳是PC+4+imm(符扩)|00
  //   J: jal 下一条是PC[31:28]|26|00
  //   I
  //   J
  //   cal_r cal_i load store需要ALU的Rs
  //   R
endmodule
