// Logisim project 同步复位流水线-deluxe.circ as structural Verilog
module IM_01 (
  input  [31:0] PC,
  output [31:0] Ins
);

  wire [31:0] subtractor_1_out;

  Subtractor #(.width(32)) subtractor_1 (.a(PC), .b(32'h3000), .out(subtractor_1_out));  // open: bin, bout
  ROM #(.addrWidth(12), .dataWidth(32)) rom_1 (.addr(subtractor_1_out[13:2]), .data(Ins));  // open: sel

  // Notes on the sheet:
  //   输入：PC，用于选择需要ROM中的哪个指令
  //   contents of rom_1 (hex, n*v repeats v):
  //   3c1dd817 1b92822 340751b5 37411553 2d50820 2e77822 3c15217e 1c47822 36ef307b 34b4020 3bee822 25dc822
  //   1de1820 35a2022 23b9822 1da5822 8ee820 d2c820 3c13d499 3c13f0d4 373b464e 253020 3daf022 fc2822
  //   3c172513 39ce020 1fc3820 2fa8820 35836a55 1f5f022 24022 36c20ade 3c0c68c7 3440022 2b18020 3c1c8e3e
  //   345469a4 22ff020 3c0df0f7 3a15022 36ba22fb 602820 3c1363ed 2bfb020 1926022 3c028cb5 3c07ec3e 323b822
  //   1749822 31d0022 4de822 2187020 348d20a5 35ed2515 18d022 3969020 366e4b7b 185c822 3c163b71 3c1513c3
  //   3c0efd05 3c0ff6fd 353d557f 2e1d820 3f62022 30a7822 35be5ae4 30b8822 3c1b9d97 3c0e4ba3 27cb020
  //   378f2195 3c1f528e 34091d7d 3cea022 2d01022 3c0c2e7a 3fb5820 3c17aff4 3c1dfb29 37fc5a84 3c1a1db0
  //   3fce022 3c16ca98 3c142aaa 3c1ae551 3c0481a8 3418671f 1833820 3c0c5dac 3918822 a48022 3c100944 ac3820
  //   3dd1022 afc022 3cb8822 346d1b11 2179020 3c088638 34040100 34850123 3c0601c8 3c07ffff 34e7ffff 868020
  //   878820 e7a020 869022 879822 ac040000 ac050004 ac060008 ac07000c ac100010 ac110014 ac120018 ac13002c
  //   ac140030 8c040000 8c05000c ac04001c ac050020 34040001 34050002 34060001 10850000 34010001 34a50004
  //   36b50005
  //   输出：instr，ROM中指令被取出
endmodule

module PC_02 (
  input  [31:0] NPC,
  input  clk,
  input  rst,
  input  en,
  output [31:0] PC
);

  wire comparator_1_eq;
  wire [31:0] PC_q;

  Register #(.width(32)) u_PC (.D(NPC), .en(en), .Q(PC_q), .clk(clk), .clr(rst));
  Multiplexer #(.width(32), .enable("false")) multiplexer_1 (
    .in0(PC_q), .in1(32'h3000), .out(PC), .sel(comparator_1_eq));
  Comparator #(.width(32), .mode("unsigned")) comparator_1 (
    .a(PC_q), .b({32{1'b0}}), .eq(comparator_1_eq));  // open: gt, lt

  // Notes on the sheet:
  //   输入：时钟；异步复位
  //   输入：NPC，下一条指令地址
  //   输出：PC，当前指令地址
endmodule

module NPC_03 (
  input  [31:0] PC_F,
  input  [31:0] PC_D,
  input  [31:0] Rs,
  input  [15:0] imm,
  input  [25:0] ins_index,
  input  isJr,
  input  isJal,
  input  isBranchSuccess,
  output [31:0] NPC
);

  wire [31:0] bit_extender_1_out, \desBranch_b指令 , multiplexer_1_out, multiplexer_2_out, PC4_D, PC4_F;

  assign bit_extender_1_out = {{14{imm[15]}}, {imm, 2'b00}};  // Bit_Extender bit_extender_1
  Adder #(.width(32)) adder_1 (.a(bit_extender_1_out), .b(PC4_D), .out(\desBranch_b指令 ));  // open: cin, cout
  Adder #(.width(32)) adder_2 (.a(PC_F), .b(32'h4), .out(PC4_F));  // open: cin, cout
  Adder #(.width(32)) adder_3 (.a(PC_D), .b(32'h4), .out(PC4_D));  // open: cin, cout
  Multiplexer #(.width(32), .enable("false")) multiplexer_1 (
    .in0(PC4_F), .in1(Rs), .out(multiplexer_1_out), .sel(isJr));
  Multiplexer #(.width(32), .enable("false")) multiplexer_2 (
    .in0(multiplexer_1_out), .in1(\desBranch_b指令 ), .out(multiplexer_2_out), .sel(isBranchSuccess));
  Multiplexer #(.width(32), .enable("false")) multiplexer_3 (
    .in0(multiplexer_2_out), .in1({PC_D[31:28], ins_index, 2'b00}), .out(NPC), .sel(isJal));

  // Other names for the same wires on the sheet: desJal_jal[31:2] = {PC_D[31:28], ins_index}; desRs_jr[31:0] = Rs

  // Notes on the sheet:
  //   指令有：
  //   输入：PC，当前PC值
  //   R: addu 下一跳是PC+4
  //   R: subu 下一跳是PC+4
  //   R: jr 下一跳是Rs的内容
  //   I: ori 下一跳是PC+4
  //   I: lw 下一跳是PC+4
  //   I: sw 下一跳是PC+4
  //   I: lui 下一条是PC+4
  //   J: jal 下一条是PC[31:28]|26|00
  //   I: beq 下一跳是PC+4+imm(符扩)|00
  //   输入：Rs内容,是不是j,是不是jr
  //   输入：imm,是不是branch,有没有成功beq
  //   输入：ins_index，是不是j，是不是jal
  //   输出：PC+4，jal要用，要存进$ra
  //   输出：NPC，根据输入层层选择后得到
endmodule

module GRF_04 (
  input  clk,
  input  rst,
  input  WE,
  input  [4:0] A1,
  input  [4:0] A2,
  input  [4:0] A3,
  input  [31:0] WD,
  output [31:0] RD1,
  output [31:0] RD2
);

  wire and_1_out, and_2_out, comparator_1_eq, comparator_2_eq, comparator_3_eq, comparator_4_eq, not_1_out,
       not_2_out;
  wire [31:0] in01, in02, in03, in04, in05, in06, in07, in08, in09, in10, in11, in12, in13, in14, in15, in16,
       in17, in18, in19, in20, in21, in22, in23, in24, in25, in26, in27, in28, in29, in30, in31,
       multiplexer_1_out, multiplexer_2_out, out00, out01, out02, out03, out04, out05, out06, out07, out08,
       out09, out10, out11, out12, out13, out14, out15, out16, out17, out18, out19, out20, out21, out22,
       out23, out24, out25, out26, out27, out28, out29, out30, out31;

  Register #(.width(32)) register_1 (.D({32{1'b0}}), .en(WE), .Q(out00), .clk(clk), .clr(rst));
  Register #(.width(32)) register_2 (.D(in01), .en(WE), .Q(out01), .clk(clk), .clr(rst));
  Register #(.width(32)) register_3 (.D(in02), .en(WE), .Q(out02), .clk(clk), .clr(rst));
  Register #(.width(32)) register_4 (.D(in03), .en(WE), .Q(out03), .clk(clk), .clr(rst));
  // Probe on out00
  // Probe on out01
  // Probe on out02
  // Probe on out03
  // Probe on out04
  // Probe on out05
  // Probe on out06
  // Probe on out07
  // Probe on out08
  // Probe on out09
  // Probe on out10
  // Probe on out11
  // Probe on out12
  // Probe on out13
  // Probe on out14
  // Probe on out15
  // Probe on out16
  // Probe on out17
  // Probe on out18
  // Probe on out19
  // Probe on out20
  // Probe on out21
  // Probe on out22
  // Probe on out23
  // Probe on out24
  // Probe on out25
  // Probe on out26
  // Probe on out27
  // Probe on out28
  // Probe on out29
  // Probe on out30
  // Probe on out31
  Register #(.width(32)) register_5 (.D(in04), .en(WE), .Q(out04), .clk(clk), .clr(rst));
  Register #(.width(32)) register_6 (.D(in05), .en(WE), .Q(out05), .clk(clk), .clr(rst));
  Register #(.width(32)) register_7 (.D(in06), .en(WE), .Q(out06), .clk(clk), .clr(rst));
  Register #(.width(32)) register_8 (.D(in07), .en(WE), .Q(out07), .clk(clk), .clr(rst));
  Multiplexer #(.select(5), .width(32), .enable("false")) multiplexer_1 (
    .in0(out00), .in1(out01), .in2(out02), .in3(out03), .in4(out04), .in5(out05), .in6(out06), .in7(out07),
    .in8(out08), .in9(out09), .in10(out10), .in11(out11), .in12(out12), .in13(out13), .in14(out14),
    .in15(out15), .in16(out16), .in17(out17), .in18(out18), .in19(out19), .in20(out20), .in21(out21),
    .in22(out22), .in23(out23), .in24(out24), .in25(out25), .in26(out26), .in27(out27), .in28(out28),
    .in29(out29), .in30(out30), .in31(out31), .out(multiplexer_1_out), .sel(A1));
  Register #(.width(32)) register_9 (.D(in08), .en(WE), .Q(out08), .clk(clk), .clr(rst));
  Register #(.width(32)) register_10 (.D(in09), .en(WE), .Q(out09), .clk(clk), .clr(rst));
  Register #(.width(32)) register_11 (.D(in10), .en(WE), .Q(out10), .clk(clk), .clr(rst));
  Register #(.width(32)) register_12 (.D(in11), .en(WE), .Q(out11), .clk(clk), .clr(rst));
  Multiplexer #(.select(5), .width(32), .enable("false")) multiplexer_2 (
    .in0(out00), .in1(out01), .in2(out02), .in3(out03), .in4(out04), .in5(out05), .in6(out06), .in7(out07),
    .in8(out08), .in9(out09), .in10(out10), .in11(out11), .in12(out12), .in13(out13), .in14(out14),
    .in15(out15), .in16(out16), .in17(out17), .in18(out18), .in19(out19), .in20(out20), .in21(out21),
    .in22(out22), .in23(out23), .in24(out24), .in25(out25), .in26(out26), .in27(out27), .in28(out28),
    .in29(out29), .in30(out30), .in31(out31), .out(multiplexer_2_out), .sel(A2));
  Register #(.width(32)) register_13 (.D(in12), .en(WE), .Q(out12), .clk(clk), .clr(rst));
  Register #(.width(32)) register_14 (.D(in13), .en(WE), .Q(out13), .clk(clk), .clr(rst));
  Register #(.width(32)) register_15 (.D(in14), .en(WE), .Q(out14), .clk(clk), .clr(rst));
  Register #(.width(32)) register_16 (.D(in15), .en(WE), .Q(out15), .clk(clk), .clr(rst));
  Demultiplexer #(.select(5), .width(32), .tristate("true"), .enable("false")) demultiplexer_1 (
    .out1(in01), .out2(in02), .out3(in03), .out4(in04), .out5(in05), .out6(in06), .out7(in07), .out8(in08),
    .out9(in09), .out10(in10), .out11(in11), .out12(in12), .out13(in13), .out14(in14), .out15(in15),
    .out16(in16), .out17(in17), .out18(in18), .out19(in19), .out20(in20), .out21(in21), .out22(in22),
    .out23(in23), .out24(in24), .out25(in25), .out26(in26), .out27(in27), .out28(in28), .out29(in29),
    .out30(in30), .out31(in31), .in(WD), .sel(A3));  // open: out0
  Register #(.width(32)) register_17 (.D(in16), .en(WE), .Q(out16), .clk(clk), .clr(rst));
  Register #(.width(32)) register_18 (.D(in17), .en(WE), .Q(out17), .clk(clk), .clr(rst));
  Register #(.width(32)) register_19 (.D(in18), .en(WE), .Q(out18), .clk(clk), .clr(rst));
  Register #(.width(32)) register_20 (.D(in19), .en(WE), .Q(out19), .clk(clk), .clr(rst));
  Register #(.width(32)) register_21 (.D(in20), .en(WE), .Q(out20), .clk(clk), .clr(rst));
  Register #(.width(32)) register_22 (.D(in21), .en(WE), .Q(out21), .clk(clk), .clr(rst));
  Register #(.width(32)) register_23 (.D(in22), .en(WE), .Q(out22), .clk(clk), .clr(rst));
  Register #(.width(32)) register_24 (.D(in23), .en(WE), .Q(out23), .clk(clk), .clr(rst));
  Comparator #(.width(5), .mode("unsigned")) comparator_1 (.a(A1), .b(A3), .eq(comparator_1_eq));  // open: gt, lt
  Comparator #(.width(5), .mode("unsigned")) comparator_2 (
    .a(A1), .b({5{1'b0}}), .eq(comparator_2_eq));  // open: gt, lt
  not not_1 (not_1_out, comparator_2_eq);
  Comparator #(.width(5), .mode("unsigned")) comparator_3 (.a(A2), .b(A3), .eq(comparator_3_eq));  // open: gt, lt
  not not_2 (not_2_out, comparator_4_eq);
  Comparator #(.width(5), .mode("unsigned")) comparator_4 (
    .a(A2), .b({5{1'b0}}), .eq(comparator_4_eq));  // open: gt, lt
  Multiplexer #(.width(32), .enable("false")) multiplexer_3 (
    .in0(multiplexer_1_out), .in1(WD), .out(RD1), .sel(and_1_out));
  and and_1 (and_1_out, comparator_1_eq, WE, not_1_out);
  Multiplexer #(.width(32), .enable("false")) multiplexer_4 (
    .in0(multiplexer_2_out), .in1(WD), .out(RD2), .sel(and_2_out));
  and and_2 (and_2_out, comparator_3_eq, WE, not_2_out);
  Register #(.width(32)) register_25 (.D(in24), .en(WE), .Q(out24), .clk(clk), .clr(rst));
  Register #(.width(32)) register_26 (.D(in25), .en(WE), .Q(out25), .clk(clk), .clr(rst));
  Register #(.width(32)) register_27 (.D(in26), .en(WE), .Q(out26), .clk(clk), .clr(rst));
  Register #(.width(32)) register_28 (.D(in27), .en(WE), .Q(out27), .clk(clk), .clr(rst));
  Register #(.width(32)) register_29 (.D(in28), .en(WE), .Q(out28), .clk(clk), .clr(rst));
  Register #(.width(32)) register_30 (.D(in29), .en(WE), .Q(out29), .clk(clk), .clr(rst));
  Register #(.width(32)) register_31 (.D(in30), .en(WE), .Q(out30), .clk(clk), .clr(rst));
  Register #(.width(32)) register_32 (.D(in31), .en(WE), .Q(out31), .clk(clk), .clr(rst));

  // Notes on the sheet:
  //   输入：A1，A2，A3选址
  //   输入：时钟；异步复位；写入使能
  //   输出：RD1，RD2读出
  //   输出：RD1，RD2读出
endmodule

module ALU_05 (
  input  [31:0] A,
  input  [31:0] B,
  input  [2:0] ALUOp,
  output [31:0] C
);

  wire [31:0] adder_1_out, and_1_out, or_1_out, shifter_1_out, subtractor_1_out;

  Adder #(.width(32)) adder_1 (.a(A), .b(B), .out(adder_1_out));  // open: cin, cout
  Subtractor #(.width(32)) subtractor_1 (.a(A), .b(B), .out(subtractor_1_out));  // open: bin, bout
  assign and_1_out = A & B;  // AND_Gate and_1, 32 bits wide
  assign or_1_out = A | B;  // OR_Gate or_1, 32 bits wide
  Shifter #(.width(32)) shifter_1 (.in(B), .\dist (5'b10000), .out(shifter_1_out));
  Multiplexer #(.select(3), .width(32), .enable("false")) multiplexer_1 (
    .in0(adder_1_out), .in1(subtractor_1_out), .in2(and_1_out), .in3(or_1_out), .in4(shifter_1_out), .out(C),
    .sel(ALUOp));  // open: in5, in6, in7

  // Notes on the sheet:
  //   输入：计算方式选择
  //   R: jr 无
  //   I: ori 011
  //   I: lw 无
  //   I: sw 无
  //   I: beq 无
  //   J: jal 无
  //   输入：A，B两个等待计算的数字
  //   R: addu 000
  //   R: subu 001
  //   I: andi 010-实验中不涉及这条指令，但还是预留一个坑位
  //   I: lui 100 lui对于imm，0扩成32位后传入输入A，之后的处理在ALU中完成
  //   输出：C计算结果
  //   输出：A是否等于B
  //   输出：A是否等于B
endmodule

module DM_06 (
  input  [31:0] A,
  input  [31:0] WD,
  input  WE,
  input  clk,
  input  reset,
  output [31:0] RD
);

  RAM #(.addrWidth(12), .dataWidth(32), .bus("separate")) ram_1 (
    .addr(A[13:2]), .din(WD), .data(RD), .str(WE), .clk(clk), .clr(reset));  // open: sel, ld

  // Notes on the sheet:
  //   输入:clk，reset
  //   输入:写使能，写内容
  //   输入:选址信号[31:0]，取[13:2]用来选址
  //   输出：读内容
endmodule

module EXT_07 (
  input  [15:0] imm,
  input  zeroOrSigned,
  output [31:0] immHasExted
);

  wire [31:0] bit_extender_1_out, bit_extender_2_out;

  assign bit_extender_1_out = {{16{1'b0}}, imm};  // Bit_Extender bit_extender_1
  assign bit_extender_2_out = {{16{imm[15]}}, imm};  // Bit_Extender bit_extender_2
  Multiplexer #(.width(32), .enable("false")) multiplexer_1 (
    .in0(bit_extender_1_out), .in1(bit_extender_2_out), .out(immHasExted), .sel(zeroOrSigned));

  // Notes on the sheet:
  //   输入:0扩展还是符号扩展
  //   I: ori 0扩展
  //   I: lw 符号扩展
  //   I: sw 符号扩展
  //   I: beq NPC中处理
  //   I: lui ALU中处理
  //   输入:imm[15:0]，不经过任何处理输入
  //   输出：扩展成32位
endmodule

module Controller_08 (
  input  [31:0] ins,
  input  [2:0] stage,
  output [1:0] GRF_A3_01,
  output GRF_WE_02,
  output ALU_B_01,
  output ALU_immExt_02,
  output [2:0] ALU_Op_03,
  output DM_WE_01,
  output NPC_isJr_01,
  output NPC_isJ_02,
  output NPC_isBeq_03,
  output [1:0] Forward_outChoose,
  output [4:0] Rs,
  output [4:0] Rt,
  output [4:0] Rd,
  output [15:0] imm,
  output [25:0] ins_index,
  output [1:0] Tuse_Rs,
  output [1:0] Tuse_Rt,
  output [1:0] Tnew,
  output isRead_Rs,
  output isRead_Rt,
  output isWrite,
  output [4:0] WriteDes
);

  wire addu, comparator_1_eq, comparator_2_eq, comparator_3_eq, comparator_4_eq, comparator_5_eq,
       comparator_6_eq, comparator_7_eq, comparator_8_eq, isCal_i, isCal_r, isLoad, isR, lui, not_1_out,
       not_2_out, not_3_out, not_4_out, not_5_out, not_6_out, not_7_out, not_8_out, not_9_out, not_10_out,
       not_11_out, not_12_out, or_1_out, or_2_out, or_3_out, or_6_out, or_7_out, or_11_out, or_12_out, ori,
       subu;
  wire [1:0] multiplexer_1_out, multiplexer_2_out, multiplexer_3_out, multiplexer_4_out, multiplexer_6_out,
       multiplexer_9_out, multiplexer_11_out, multiplexer_20_out, Tnew_E, Tnew_Etemp, Tnew_M, Tnew_Mtemp,
       Tnew_W, Tuse_D_Rs, Tuse_D_Rt, Tuse_E_Rs, Tuse_E_Rstemp, Tuse_E_Rt, Tuse_E_Rttemp, Tuse_M_Rs,
       Tuse_M_Rstemp, Tuse_M_Rt, Tuse_M_Rttemp, Tuse_W_Rs, Tuse_W_Rstemp, Tuse_W_Rt, Tuse_W_Rttemp;
  wire [4:0] multiplexer_21_out;

  not not_1 (not_1_out, ins[31]);
  not not_2 (not_2_out, ins[29]);
  not not_3 (not_3_out, ins[30]);
  not not_4 (not_4_out, ins[28]);
  not not_5 (not_5_out, ins[27]);
  not not_6 (not_6_out, ins[26]);
  not not_7 (not_7_out, ins[5]);
  not not_8 (not_8_out, ins[3]);
  not not_9 (not_9_out, ins[4]);
  not not_10 (not_10_out, ins[2]);
  not not_11 (not_11_out, ins[1]);
  not not_12 (not_12_out, ins[0]);
  Multiplexer #(.width(2), .enable("false")) multiplexer_1 (
    .in0(2'b11), .in1(2'b10), .out(multiplexer_1_out), .sel(1'b1));
  Multiplexer #(.width(2), .enable("false")) multiplexer_2 (
    .in0(multiplexer_1_out), .in1(2'b01), .out(multiplexer_2_out), .sel(or_1_out));
  or or_1 (or_1_out, isCal_r, isCal_i, isLoad, DM_WE_01);
  Multiplexer #(.width(2), .enable("false")) multiplexer_3 (
    .in0(2'b11), .in1(2'b10), .out(multiplexer_3_out), .sel(DM_WE_01));
  and and_1 (isR, not_1_out, not_3_out, not_2_out, not_4_out, not_5_out, not_6_out);
  and and_2 (addu, isR, ins[5], not_9_out, not_8_out, not_10_out, not_11_out, not_12_out);
  and and_3 (subu, isR, ins[5], not_9_out, not_8_out, not_10_out, ins[1], not_12_out);
  and and_4 (NPC_isJr_01, isR, not_7_out, not_9_out, ins[3], not_10_out, not_11_out, not_12_out);
  and and_5 (ori, not_1_out, not_3_out, ins[29], ins[28], not_5_out, ins[26]);
  and and_6 (isLoad, ins[31], not_3_out, not_2_out, not_4_out, ins[27], ins[26]);
  and and_7 (DM_WE_01, ins[31], not_3_out, ins[29], not_4_out, ins[27], ins[26]);
  and and_8 (NPC_isBeq_03, not_1_out, not_3_out, not_2_out, ins[28], not_5_out, not_6_out);
  and and_9 (lui, not_1_out, not_3_out, ins[29], ins[28], ins[27], ins[26]);
  and and_10 (NPC_isJ_02, not_1_out, not_3_out, not_2_out, not_4_out, ins[27], ins[26]);
  or or_2 (or_2_out, NPC_isJr_01, NPC_isBeq_03);
  Multiplexer #(.width(2), .enable("false")) multiplexer_4 (
    .in0(multiplexer_3_out), .in1(2'b01), .out(multiplexer_4_out), .sel(isCal_r));
  Multiplexer #(.width(2), .enable("false")) multiplexer_5 (
    .in0(multiplexer_4_out), .in1(2'b00), .out(Tuse_D_Rt), .sel(NPC_isBeq_03));
  Multiplexer #(.width(2), .enable("false")) multiplexer_6 (
    .in0(2'b00), .in1(2'b01), .out(multiplexer_6_out), .sel(or_3_out));
  or or_3 (or_3_out, isCal_r, isCal_i);
  Multiplexer #(.width(2), .enable("false")) multiplexer_7 (
    .in0(multiplexer_2_out), .in1(2'b00), .out(Tuse_D_Rs), .sel(or_2_out));
  Multiplexer #(.width(2), .enable("false")) multiplexer_8 (
    .in0(multiplexer_6_out), .in1(2'b10), .out(Tnew_E), .sel(isLoad));
  or or_4 (isCal_r, addu, subu);
  or or_5 (isCal_i, ori, lui);
  Subtractor #(.width(2)) subtractor_1 (.a(Tuse_D_Rs), .b(2'b01), .out(Tuse_E_Rstemp));  // open: bin, bout
  Subtractor #(.width(2)) subtractor_2 (.a(Tuse_E_Rs), .b(2'b01), .out(Tuse_M_Rstemp));  // open: bin, bout
  Subtractor #(.width(2)) subtractor_3 (.a(Tuse_M_Rs), .b(2'b01), .out(Tuse_W_Rstemp));  // open: bin, bout
  Subtractor #(.width(2)) subtractor_4 (.a(Tuse_D_Rt), .b(2'b01), .out(Tuse_E_Rttemp));  // open: bin, bout
  Subtractor #(.width(2)) subtractor_5 (.a(Tuse_E_Rt), .b(2'b01), .out(Tuse_M_Rttemp));  // open: bin, bout
  Subtractor #(.width(2)) subtractor_6 (.a(Tuse_M_Rt), .b(2'b01), .out(Tuse_W_Rttemp));  // open: bin, bout
  Subtractor #(.width(2)) subtractor_7 (.a(Tnew_E), .b(2'b01), .out(Tnew_Etemp));  // open: bin, bout
  Subtractor #(.width(2)) subtractor_8 (.a(Tnew_M), .b(2'b01), .out(Tnew_Mtemp));  // open: bin, bout
  or or_6 (or_6_out, isCal_i, isLoad);
  Comparator #(.width(2)) comparator_1 (.a(Tuse_E_Rstemp), .b(2'b11), .eq(comparator_1_eq));  // open: gt, lt
  Comparator #(.width(2)) comparator_2 (.a(Tuse_M_Rstemp), .b(2'b11), .eq(comparator_2_eq));  // open: gt, lt
  Comparator #(.width(2)) comparator_3 (.a(Tuse_W_Rstemp), .b(2'b11), .eq(comparator_3_eq));  // open: gt, lt
  Comparator #(.width(2)) comparator_4 (.a(Tuse_E_Rttemp), .b(2'b11), .eq(comparator_4_eq));  // open: gt, lt
  Comparator #(.width(2)) comparator_5 (.a(Tuse_M_Rttemp), .b(2'b11), .eq(comparator_5_eq));  // open: gt, lt
  Comparator #(.width(2)) comparator_6 (.a(Tuse_W_Rttemp), .b(2'b11), .eq(comparator_6_eq));  // open: gt, lt
  Comparator #(.width(2)) comparator_7 (.a(Tnew_Etemp), .b(2'b11), .eq(comparator_7_eq));  // open: gt, lt
  Comparator #(.width(2)) comparator_8 (.a(Tnew_Mtemp), .b(2'b11), .eq(comparator_8_eq));  // open: gt, lt
  Multiplexer #(.width(2), .enable("false")) multiplexer_9 (
    .in0(2'b00), .in1(2'b01), .out(multiplexer_9_out), .sel(or_6_out));
  Multiplexer #(.width(2), .enable("false")) multiplexer_10 (
    .in0(multiplexer_9_out), .in1(2'b10), .out(GRF_A3_01), .sel(NPC_isJ_02));
  Multiplexer #(.width(2), .enable("false")) multiplexer_11 (
    .in0(2'b00), .in1(2'b01), .out(multiplexer_11_out), .sel(or_7_out));
  or or_7 (or_7_out, isCal_r, isCal_i);
  Multiplexer #(.width(2), .enable("false")) multiplexer_12 (
    .in0(Tuse_E_Rstemp), .in1(2'b00), .out(Tuse_E_Rs), .sel(comparator_1_eq));
  Multiplexer #(.width(2), .enable("false")) multiplexer_13 (
    .in0(Tuse_M_Rstemp), .in1(2'b00), .out(Tuse_M_Rs), .sel(comparator_2_eq));
  Multiplexer #(.width(2), .enable("false")) multiplexer_14 (
    .in0(Tuse_W_Rstemp), .in1(2'b00), .out(Tuse_W_Rs), .sel(comparator_3_eq));
  Multiplexer #(.width(2), .enable("false")) multiplexer_15 (
    .in0(Tuse_E_Rttemp), .in1(2'b00), .out(Tuse_E_Rt), .sel(comparator_4_eq));
  Multiplexer #(.width(2), .enable("false")) multiplexer_16 (
    .in0(Tuse_M_Rttemp), .in1(2'b00), .out(Tuse_M_Rt), .sel(comparator_5_eq));
  Multiplexer #(.width(2), .enable("false")) multiplexer_17 (
    .in0(Tuse_W_Rttemp), .in1(2'b00), .out(Tuse_W_Rt), .sel(comparator_6_eq));
  Multiplexer #(.width(2), .enable("false")) multiplexer_18 (
    .in0(Tnew_Etemp), .in1(2'b00), .out(Tnew_M), .sel(comparator_7_eq));
  Multiplexer #(.width(2), .enable("false")) multiplexer_19 (
    .in0(Tnew_Mtemp), .in1(2'b00), .out(Tnew_W), .sel(comparator_8_eq));
  or or_8 (GRF_WE_02, isCal_r, isCal_i, isLoad, NPC_isJ_02);
  or or_9 (ALU_B_01, isCal_i, isLoad, DM_WE_01);
  or or_10 (ALU_immExt_02, isLoad, DM_WE_01);
  or or_11 (or_11_out, addu, isLoad, DM_WE_01);
  Multiplexer #(.width(2), .enable("false")) multiplexer_20 (
    .in0(multiplexer_11_out), .in1(2'b10), .out(multiplexer_20_out), .sel(isLoad));
  // Probe on Tuse_D_Rs
  // Probe on Tuse_E_Rs
  // Probe on Tuse_M_Rs
  // Probe on Tuse_W_Rs
  // Probe on Tuse_D_Rt
  // Probe on Tuse_E_Rt
  // Probe on Tuse_M_Rt
  // Probe on Tuse_W_Rt
  Multiplexer #(.width(5), .enable("false")) multiplexer_21 (
    .in0(5'b11110), .in1(ins[20:16]), .out(multiplexer_21_out), .sel(or_12_out));
  or or_12 (or_12_out, isCal_i, isLoad);
  ALUOp_5to3zip aluop_5to3zip_1 (
    .addu(or_11_out), .subu(subu), .andi(1'b0), .ori(ori), .lui(lui), .o2(ALU_Op_03[2]), .o1(ALU_Op_03[1]),
    .o0(ALU_Op_03[0]));
  Multiplexer #(.width(2), .enable("false")) multiplexer_22 (
    .in0(multiplexer_20_out), .in1(2'b11), .out(Forward_outChoose), .sel(1'b0));
  or or_13 (isRead_Rt, isCal_r, NPC_isBeq_03, DM_WE_01);
  or or_14 (isWrite, isCal_r, isCal_i, isLoad, NPC_isJ_02);
  Multiplexer #(.width(5), .enable("false")) multiplexer_23 (
    .in0(multiplexer_21_out), .in1(ins[15:11]), .out(WriteDes), .sel(isCal_r));
  Multiplexer #(.select(3), .width(2), .enable("false")) multiplexer_24 (
    .in2(Tnew_E), .in3(Tnew_M), .in4(Tnew_W), .out(Tnew), .sel(stage));  // open: in0, in1, in5, in6, in7
  or or_15 (isRead_Rs, isCal_r, NPC_isJr_01, isCal_i, NPC_isBeq_03, isLoad, DM_WE_01);
  Multiplexer #(.select(3), .width(2), .enable("false")) multiplexer_25 (
    .in1(Tuse_D_Rs), .in2(Tuse_E_Rs), .in3(Tuse_M_Rs), .in4(Tuse_W_Rs), .out(Tuse_Rs), .sel(stage));  // open: in0, in5, in6, in7
  Multiplexer #(.select(3), .width(2), .enable("false")) multiplexer_26 (
    .in1(Tuse_D_Rt), .in2(Tuse_E_Rt), .in3(Tuse_M_Rt), .in4(Tuse_W_Rt), .out(Tuse_Rt), .sel(stage));  // open: in0, in5, in6, in7

  assign imm = ins[15:0];
  assign ins_index = ins[25:0];
  assign Rd = ins[15:11];
  assign Rs = ins[25:21];
  assign Rt = ins[20:16];

  // Other names for the same wires on the sheet: op[5:0] = ins[31:26]; func[5:0] = ins[5:0]; shamt[4:0] = ins[10:6];
  //   beq = NPC_isBeq_03; isBeq = NPC_isBeq_03; isJ = NPC_isJ_02; isLink = NPC_isJ_02; jal = NPC_isJ_02;
  //   isJReg = NPC_isJr_01; jr = NPC_isJr_01; lw = isLoad; isStore = DM_WE_01; sw = DM_WE_01

  // Notes on the sheet:
  //   R: addu 下一跳是PC+4
  //   R: subu 下一跳是PC+4
  //   R: jr 下一跳是Rs的内容
  //   I: ori 下一跳是PC+4
  //   I: lw 下一跳是PC+4
  //   I: sw 下一跳是PC+4
  //   I: lui 下一条是PC+4
  //   R
  //   I: beq 下一跳是PC+4+imm(符扩)|00
  //   J: jal 下一条是PC[31:28]|26|00
  //   I
  //   J
  //   读：Tuse_Rs
  //   读：Tuse_Rt
  //   写：Tnew
  //   转发送出
  //   00为Rd，01为Rt，10为$ra
  //   0为RD2,1为imm
  //   beq lui不用管
  //   读：Tuse_Rs
  //   读：Tuse_Rt
  //   写：Tnew
  //   0为0扩展，1为Signed扩展
  //   ori 0扩展；lw sw符扩
  //   R: addu 000
  //   R: subu 001
  //   I: ori 011
  //   00为PC8,01为ALU，10为DM
  //   I: andi 010-实验中不涉及这条指令，但还是预留一个坑位，目前放置了常数0
  //   I: lui 100 lui对于imm，0扩成32位后传入输入A，之后的处理在ALU中完成
  //   R
endmodule

module ALUOp_5to3zip (
  input  addu,
  input  subu,
  input  andi,
  input  ori,
  input  lui,
  output o2,
  output o1,
  output o0
);

  wire not_1_out, not_2_out, not_3_out, not_4_out, not_5_out, not_6_out;

  not not_1 (not_1_out, addu);
  not not_2 (not_2_out, subu);
  not not_3 (not_3_out, lui);
  not not_4 (not_4_out, addu);
  not not_5 (not_5_out, andi);
  not not_6 (not_6_out, lui);
  and and_1 (o1, not_1_out, not_2_out, not_3_out);
  and and_2 (o0, not_4_out, not_5_out, not_6_out);

  assign o2 = lui;
endmodule

module main2 (
  input  rst
);

  wire ALU_B_01, ALU_immExt_02, and_1_out, clk, CMP_isequal, DM_WE, flushEX, GRF_WE_02, isNeedForwrd_DE_Rs,
       isNeedForwrd_DE_Rt, isNeedForwrd_DEM_Rs, isNeedForwrd_DEM_Rt, isNeedForwrd_EM_Rs, isNeedForwrd_EM_Rt,
       isNeedForwrd_EMW_Rs, isNeedForwrd_EMW_Rt, isNeedForwrd_MW_Rs, isNeedForwrd_MW_Rt, isRead_Rs_D,
       isRead_Rs_E, isRead_Rs_M, isRead_Rs_W, isRead_Rt_D, isRead_Rt_E, isRead_Rt_M, isRead_Rt_W, isWrite_D,
       isWrite_E, isWrite_M, isWrite_W, not_1_out, not_2_out, NPC_isBeq_03, NPC_isJ_02, NPC_isJr_01,
       or_1_out, stallID, stallPC;
  wire [1:0] Forward_outChoose_E, Forward_outChoose_M, Forward_outChoose_W, GRF_A3_01, Tnew_D, Tnew_E,
       Tnew_M, Tnew_W, Tuse_Rs_D, Tuse_Rs_E, Tuse_Rs_M, Tuse_Rs_W, Tuse_Rt_D, Tuse_Rt_E, Tuse_Rt_M, Tuse_Rt_W;
  wire [2:0] ALUOp_03;
  wire [4:0] multiplexer_5_out, Rd_D, Rd_E, Rd_M, Rd_W, Rs_D, Rs_E, Rs_M, Rs_W, Rt_D, Rt_E, Rt_M, Rt_W,
       WriteDes_D, WriteDes_E, WriteDes_M, WriteDes_W;
  wire [15:0] imm_D, imm_E, imm_M, imm_W;
  wire [25:0] ins_index_D, ins_index_E, ins_index_M, ins_index_W;
  wire [31:0] adder_1_out, adder_2_out, ALU_E, ALU_M, ALU_W, Data_E, Data_M, Data_W, DM_M, DM_W,
       EXT_immhasexted, IR_D, IR_E, IR_F, IR_M, IR_W, multiplexer_1_out, multiplexer_2_out,
       multiplexer_6_out, multiplexer_7_out, multiplexer_11_out, NPC, PC4_D, PC4_E, PC4_M, PC4_W, PC8_D,
       PC8_E, PC8_M, PC8_W, PC_D, PC_E, PC_F, PC_M, PC_W, RD1_D, RD1_D_final, RD1_E, RD1_E_final, RD1_M,
       RD1_M_final, RD1_W, RD2_D, RD2_D_final, RD2_E, RD2_E_final, RD2_M, RD2_M_final, RD2_W;

  // Probe on PC_F
  // Probe on IR_F
  Clock clock_1 (.out(clk));
  PC_02 PC (.NPC(NPC), .clk(clk), .rst(rst), .en(not_1_out), .PC(PC_F));
  not not_1 (not_1_out, stallPC);
  Hazard_11 hazard_11_1 (
    .isRead_Rs_D(isRead_Rs_D), .Rs_D(Rs_D), .Tuse_Rs_D(Tuse_Rs_D), .isRead_Rt_D(isRead_Rt_D), .Rt_D(Rt_D),
    .Tuse_Rt_D(Tuse_Rt_D), .isWrite_E(isWrite_E), .WriteDes_E(WriteDes_E), .Tnew_E(Tnew_E),
    .isWrite_M(isWrite_M), .WriteDes_M(WriteDes_M), .Tnew_M(Tnew_M), .stallPC(stallPC), .stallID(stallID),
    .flushEX(flushEX));
  // Probe on PC_D
  // Probe on IR_D
  // Probe on NPC
  // Probe on isNeedForwrd_DE_Rs
  // Probe on isNeedForwrd_DEM_Rs
  // Probe on isNeedForwrd_DE_Rt
  // Probe on isNeedForwrd_DEM_Rt
  // Probe on stallPC
  // Probe on RD1_D_final
  // Probe on RD2_D_final
  IM_01 IM (.PC(PC_F), .Ins(IR_F));
  ForwardUnit_13 D_E__Rs (
    .isRead(isRead_Rs_D), .ReadDes(Rs_D), .Tuse(Tuse_Rs_D), .isWrite(isWrite_E), .WriteDes(WriteDes_E),
    .Tnew(Tnew_E), .NeedForward(isNeedForwrd_DE_Rs));
  ForwardUnit_13 E_M__Rs (
    .isRead(isRead_Rs_E), .ReadDes(Rs_E), .Tuse(Tuse_Rs_E), .isWrite(isWrite_M), .WriteDes(WriteDes_M),
    .Tnew(Tnew_M), .NeedForward(isNeedForwrd_EM_Rs));
  ForwardUnit_13 M_W__Rs (
    .isRead(isRead_Rs_M), .ReadDes(Rs_M), .Tuse(Tuse_Rs_M), .isWrite(isWrite_W), .WriteDes(WriteDes_W),
    .Tnew(Tnew_W), .NeedForward(isNeedForwrd_MW_Rs));
  // Probe on isNeedForwrd_EM_Rs
  // Probe on isNeedForwrd_EMW_Rs
  // Probe on isNeedForwrd_EM_Rt
  // Probe on isNeedForwrd_EMW_Rt
  // Probe on PC_E
  // Probe on IR_E
  // Probe on RD1_E_final
  // Probe on RD2_E_final
  // Probe on PC_M
  // Probe on IR_M
  // Probe on isNeedForwrd_MW_Rs
  // Probe on isNeedForwrd_MW_Rt
  // Probe on RD1_M_final
  // Probe on RD2_M_final
  ForwardUnit_13 D_E_M__Rs (
    .isRead(isRead_Rs_D), .ReadDes(Rs_D), .Tuse(Tuse_Rs_D), .isWrite(isWrite_M), .WriteDes(WriteDes_M),
    .Tnew(Tnew_M), .NeedForward(isNeedForwrd_DEM_Rs));
  ForwardUnit_13 E_M_W__Rs (
    .isRead(isRead_Rs_E), .ReadDes(Rs_E), .Tuse(Tuse_Rs_E), .isWrite(isWrite_W), .WriteDes(WriteDes_W),
    .Tnew(Tnew_W), .NeedForward(isNeedForwrd_EMW_Rs));
  Adder #(.width(32)) adder_1 (.a(PC_F), .b(32'h4), .out(adder_1_out));  // open: cin, cout
  Adder #(.width(32)) adder_2 (.a(PC_F), .b(32'h8), .out(adder_2_out));  // open: cin, cout
  // Probe on PC_W
  // Probe on IR_W
  DEMW ID (
    .PC(PC_F), .PC_2(PC_D), .PC4(adder_1_out), .PC4_2(PC4_D), .PC8(adder_2_out), .PC8_2(PC8_D), .clk(clk),
    .reset(rst), .en(not_2_out), .IR(IR_F), .IR_2(IR_D));  // open: RD1, RD1_2, RD2, RD2_2, ALU, ALU_2, DM, DM_2, standBy, standBy_2, isStandbySuc, isStandbySuc_2
  not not_2 (not_2_out, stallID);
  Controller_08 controller_08_1 (
    .ins(IR_D), .NPC_isJr_01(NPC_isJr_01), .NPC_isJ_02(NPC_isJ_02), .NPC_isBeq_03(NPC_isBeq_03), .Rs(Rs_D),
    .Rt(Rt_D), .Rd(Rd_D), .imm(imm_D), .ins_index(ins_index_D), .stage(3'b001), .Tuse_Rs(Tuse_Rs_D),
    .Tnew(Tnew_D), .Tuse_Rt(Tuse_Rt_D), .isRead_Rs(isRead_Rs_D), .isRead_Rt(isRead_Rt_D),
    .isWrite(isWrite_D), .WriteDes(WriteDes_D));  // open: GRF_A3_01, GRF_WE_02, ALU_B_01, ALU_immExt_02, ALU_Op_03, DM_WE_01, Forward_outChoose
  Multiplexer #(.width(32), .enable("false")) multiplexer_1 (
    .in0(RD1_D), .in1(Data_M), .out(multiplexer_1_out), .sel(isNeedForwrd_DEM_Rs));
  Multiplexer #(.width(32), .enable("false")) multiplexer_2 (
    .in0(RD2_D), .in1(Data_M), .out(multiplexer_2_out), .sel(isNeedForwrd_DEM_Rt));
  Multiplexer #(.width(32), .enable("false")) multiplexer_3 (
    .in0(multiplexer_1_out), .in1(Data_E), .out(RD1_D_final), .sel(isNeedForwrd_DE_Rs));
  Multiplexer #(.width(32), .enable("false")) multiplexer_4 (
    .in0(multiplexer_2_out), .in1(Data_E), .out(RD2_D_final), .sel(isNeedForwrd_DE_Rt));
  Multiplexer #(.select(2), .width(5), .enable("false")) multiplexer_5 (
    .in0(Rd_W), .in1(Rt_W), .in2({5{1'b1}}), .out(multiplexer_5_out), .sel(GRF_A3_01));  // open: in3
  CMP_09 CMP (.Rs(RD1_D_final), .Rt(RD2_D_final), .isEqual(CMP_isequal));
  ForwardUnit_13 E_M__Rt (
    .isRead(isRead_Rt_E), .ReadDes(Rt_E), .Tuse(Tuse_Rt_E), .isWrite(isWrite_M), .WriteDes(WriteDes_M),
    .Tnew(Tnew_M), .NeedForward(isNeedForwrd_EM_Rt));
  ForwardUnit_13 M_W__Rt (
    .isRead(isRead_Rt_M), .ReadDes(Rt_M), .Tuse(Tuse_Rt_M), .isWrite(isWrite_W), .WriteDes(WriteDes_W),
    .Tnew(Tnew_W), .NeedForward(isNeedForwrd_MW_Rt));
  and and_1 (and_1_out, NPC_isBeq_03, CMP_isequal);
  ForwardUnit_13 D_E__Rt (
    .isRead(isRead_Rt_D), .ReadDes(Rt_D), .Tuse(Tuse_Rt_D), .isWrite(isWrite_E), .WriteDes(WriteDes_E),
    .Tnew(Tnew_E), .NeedForward(isNeedForwrd_DE_Rt));
  NPC_03 u_NPC (
    .PC_F(PC_F), .Rs(RD1_D_final), .imm(imm_D), .ins_index(ins_index_D), .isJr(NPC_isJr_01),
    .isJal(NPC_isJ_02), .isBranchSuccess(and_1_out), .NPC(NPC), .PC_D(PC_D));
  GRF_04 GRF (
    .A1(Rs_D), .A2(Rt_D), .A3(multiplexer_5_out), .WD(Data_W), .RD1(RD1_D), .RD2(RD2_D), .clk(clk),
    .rst(rst), .WE(GRF_WE_02));
  ForwardUnit_13 E_M_W__Rt (
    .isRead(isRead_Rt_E), .ReadDes(Rt_E), .Tuse(Tuse_Rt_E), .isWrite(isWrite_W), .WriteDes(WriteDes_W),
    .Tnew(Tnew_W), .NeedForward(isNeedForwrd_EMW_Rt));
  ForwardUnit_13 D_E_M__Rt (
    .isRead(isRead_Rt_D), .ReadDes(Rt_D), .Tuse(Tuse_Rt_D), .isWrite(isWrite_M), .WriteDes(WriteDes_M),
    .Tnew(Tnew_M), .NeedForward(isNeedForwrd_DEM_Rt));
  DEMW EX (
    .PC(PC_D), .PC_2(PC_E), .PC4(PC4_D), .PC4_2(PC4_E), .RD1(RD1_D_final), .RD1_2(RD1_E), .RD2(RD2_D_final),
    .RD2_2(RD2_E), .PC8(PC8_D), .PC8_2(PC8_E), .clk(clk), .reset(or_1_out), .en(1'b1), .IR(IR_D), .IR_2(IR_E));  // open: ALU, ALU_2, DM, DM_2, standBy, standBy_2, isStandbySuc, isStandbySuc_2
  or or_1 (or_1_out, rst, flushEX);
  Multiplexer #(.width(32), .enable("false")) multiplexer_6 (
    .in0(RD1_E), .in1(Data_W), .out(multiplexer_6_out), .sel(isNeedForwrd_EMW_Rs));
  Multiplexer #(.width(32), .enable("false")) multiplexer_7 (
    .in0(RD2_E), .in1(Data_W), .out(multiplexer_7_out), .sel(isNeedForwrd_EMW_Rt));
  Controller_08 controller_08_2 (
    .ins(IR_E), .ALU_B_01(ALU_B_01), .ALU_immExt_02(ALU_immExt_02), .ALU_Op_03(ALUOp_03), .Rs(Rs_E),
    .Rt(Rt_E), .Rd(Rd_E), .imm(imm_E), .ins_index(ins_index_E), .Forward_outChoose(Forward_outChoose_E),
    .stage(3'b010), .Tuse_Rs(Tuse_Rs_E), .Tnew(Tnew_E), .Tuse_Rt(Tuse_Rt_E), .isRead_Rs(isRead_Rs_E),
    .isRead_Rt(isRead_Rt_E), .isWrite(isWrite_E), .WriteDes(WriteDes_E));  // open: GRF_A3_01, GRF_WE_02, DM_WE_01, NPC_isJr_01, NPC_isJ_02, NPC_isBeq_03
  Multiplexer #(.width(32), .enable("false")) multiplexer_8 (
    .in0(multiplexer_6_out), .in1(Data_M), .out(RD1_E_final), .sel(isNeedForwrd_EM_Rs));
  Multiplexer #(.width(32), .enable("false")) multiplexer_9 (
    .in0(multiplexer_7_out), .in1(Data_M), .out(RD2_E_final), .sel(isNeedForwrd_EM_Rt));
  EXT_07 EXT (.imm(imm_E), .zeroOrSigned(ALU_immExt_02), .immHasExted(EXT_immhasexted));
  Multiplexer #(.select(2), .width(32), .enable("false")) multiplexer_10 (
    .in0(PC8_E), .out(Data_E), .sel(Forward_outChoose_E));  // open: in1, in2, in3
  Multiplexer #(.width(32), .enable("false")) multiplexer_11 (
    .in0(RD2_E_final), .in1(EXT_immhasexted), .out(multiplexer_11_out), .sel(ALU_B_01));
  ALU_05 ALU (.A(RD1_E_final), .B(multiplexer_11_out), .ALUOp(ALUOp_03), .C(ALU_E));
  DEMW MEM (
    .PC(PC_E), .PC_2(PC_M), .PC4(PC4_E), .PC4_2(PC4_M), .RD1(RD1_E_final), .RD1_2(RD1_M), .RD2(RD2_E_final),
    .RD2_2(RD2_M), .PC8(PC8_E), .PC8_2(PC8_M), .ALU(ALU_E), .ALU_2(ALU_M), .clk(clk), .reset(rst), .en(1'b1),
    .IR(IR_E), .IR_2(IR_M));  // open: DM, DM_2, standBy, standBy_2, isStandbySuc, isStandbySuc_2
  Multiplexer #(.select(2), .width(32), .enable("false")) multiplexer_12 (
    .in0(PC8_M), .in1(ALU_M), .out(Data_M), .sel(Forward_outChoose_M));  // open: in2, in3
  Multiplexer #(.width(32), .enable("false")) multiplexer_13 (
    .in0(RD1_M), .in1(Data_W), .out(RD1_M_final), .sel(isNeedForwrd_MW_Rs));
  Multiplexer #(.width(32), .enable("false")) multiplexer_14 (
    .in0(RD2_M), .in1(Data_W), .out(RD2_M_final), .sel(isNeedForwrd_MW_Rt));
  Controller_08 controller_08_3 (
    .ins(IR_M), .DM_WE_01(DM_WE), .Rs(Rs_M), .Rt(Rt_M), .Rd(Rd_M), .imm(imm_M), .ins_index(ins_index_M),
    .Forward_outChoose(Forward_outChoose_M), .stage(3'b011), .Tuse_Rs(Tuse_Rs_M), .Tnew(Tnew_M),
    .Tuse_Rt(Tuse_Rt_M), .isRead_Rs(isRead_Rs_M), .isRead_Rt(isRead_Rt_M), .isWrite(isWrite_M),
    .WriteDes(WriteDes_M));  // open: GRF_A3_01, GRF_WE_02, ALU_B_01, ALU_immExt_02, ALU_Op_03, NPC_isJr_01, NPC_isJ_02, NPC_isBeq_03
  DM_06 DM (.A(ALU_M), .WD(RD2_M_final), .RD(DM_M), .WE(DM_WE), .clk(clk), .reset(rst));
  DEMW WB (
    .PC(PC_M), .PC_2(PC_W), .PC4(PC4_M), .PC4_2(PC4_W), .RD1(RD1_M_final), .RD1_2(RD1_W), .RD2(RD2_M_final),
    .RD2_2(RD2_W), .PC8(PC8_M), .PC8_2(PC8_W), .ALU(ALU_M), .ALU_2(ALU_W), .DM(DM_M), .DM_2(DM_W), .clk(clk),
    .reset(rst), .en(1'b1), .IR(IR_M), .IR_2(IR_W));  // open: standBy, standBy_2, isStandbySuc, isStandbySuc_2
  Controller_08 controller_08_4 (
    .ins(IR_W), .GRF_A3_01(GRF_A3_01), .GRF_WE_02(GRF_WE_02), .Rs(Rs_W), .Rt(Rt_W), .Rd(Rd_W), .imm(imm_W),
    .ins_index(ins_index_W), .Forward_outChoose(Forward_outChoose_W), .stage(3'b100), .Tuse_Rs(Tuse_Rs_W),
    .Tnew(Tnew_W), .Tuse_Rt(Tuse_Rt_W), .isRead_Rs(isRead_Rs_W), .isRead_Rt(isRead_Rt_W),
    .isWrite(isWrite_W), .WriteDes(WriteDes_W));  // open: ALU_B_01, ALU_immExt_02, ALU_Op_03, DM_WE_01, NPC_isJr_01, NPC_isJ_02, NPC_isBeq_03
  Multiplexer #(.select(2), .width(32), .enable("false")) multiplexer_15 (
    .in0(PC8_W), .in1(ALU_W), .in2(DM_W), .out(Data_W), .sel(Forward_outChoose_W));  // open: in3

  // Notes on the sheet:
  //   向D转发
  //   向E转发
  //   向M转发
  //   F
  //   D
  //   E
  //   M
  //   W:1.Controller用于GRF 2.从Ins中解读Rs Rt Rd
  //   W
endmodule

module CMP_09 (
  input  [31:0] Rs,
  input  [31:0] Rt,
  output isEqual
);

  Comparator #(.width(32)) comparator_1 (.a(Rs), .b(Rt), .eq(isEqual));  // open: gt, lt
endmodule

module DEMW (
  input  [31:0] IR,
  input  [31:0] PC,
  input  [31:0] PC4,
  input  [31:0] RD1,
  input  [31:0] RD2,
  input  isStandbySuc,
  input  [31:0] PC8,
  input  [31:0] ALU,
  input  [31:0] DM,
  input  [31:0] standBy,
  input  clk,
  input  reset,
  input  en,
  output [31:0] IR_2,
  output [31:0] PC_2,
  output [31:0] PC4_2,
  output [31:0] RD1_2,
  output [31:0] RD2_2,
  output isStandbySuc_2,
  output [31:0] PC8_2,
  output [31:0] ALU_2,
  output [31:0] DM_2,
  output [31:0] standBy_2
);

  wire multiplexer_6_out;
  wire [31:0] multiplexer_1_out, multiplexer_2_out, multiplexer_3_out, multiplexer_4_out, multiplexer_5_out,
       multiplexer_7_out, multiplexer_8_out, multiplexer_9_out, multiplexer_10_out;

  Multiplexer #(.width(32), .enable("false")) multiplexer_1 (
    .in0(IR), .in1({32{1'b0}}), .out(multiplexer_1_out), .sel(reset));
  Multiplexer #(.width(32), .enable("false")) multiplexer_2 (
    .in0(PC), .in1({32{1'b0}}), .out(multiplexer_2_out), .sel(reset));
  Multiplexer #(.width(32), .enable("false")) multiplexer_3 (
    .in0(PC4), .in1({32{1'b0}}), .out(multiplexer_3_out), .sel(reset));
  Multiplexer #(.width(32), .enable("false")) multiplexer_4 (
    .in0(RD1), .in1({32{1'b0}}), .out(multiplexer_4_out), .sel(reset));
  Multiplexer #(.width(32), .enable("false")) multiplexer_5 (
    .in0(RD2), .in1({32{1'b0}}), .out(multiplexer_5_out), .sel(reset));
  Multiplexer #(.enable("false")) multiplexer_6 (.in0(isStandbySuc), .in1(1'b0), .out(multiplexer_6_out), .sel(reset));
  Multiplexer #(.width(32), .enable("false")) multiplexer_7 (
    .in0(PC8), .in1({32{1'b0}}), .out(multiplexer_7_out), .sel(reset));
  Multiplexer #(.width(32), .enable("false")) multiplexer_8 (
    .in0(ALU), .in1({32{1'b0}}), .out(multiplexer_8_out), .sel(reset));
  Multiplexer #(.width(32), .enable("false")) multiplexer_9 (
    .in0(DM), .in1({32{1'b0}}), .out(multiplexer_9_out), .sel(reset));
  Multiplexer #(.width(32), .enable("false")) multiplexer_10 (
    .in0(standBy), .in1({32{1'b0}}), .out(multiplexer_10_out), .sel(reset));
  Register #(.width(32)) register_1 (.D(multiplexer_1_out), .en(en), .Q(IR_2), .clk(clk));  // open: clr
  Register #(.width(32)) register_2 (.D(multiplexer_2_out), .en(en), .Q(PC_2), .clk(clk));  // open: clr
  Register #(.width(32)) register_3 (.D(multiplexer_3_out), .en(en), .Q(PC4_2), .clk(clk));  // open: clr
  Register #(.width(32)) register_4 (.D(multiplexer_4_out), .en(en), .Q(RD1_2), .clk(clk));  // open: clr
  Register #(.width(32)) register_5 (.D(multiplexer_5_out), .en(en), .Q(RD2_2), .clk(clk));  // open: clr
  Register #(.width(1)) register_6 (.D(multiplexer_6_out), .en(en), .Q(isStandbySuc_2), .clk(clk));  // open: clr
  Register #(.width(32)) register_7 (.D(multiplexer_7_out), .en(en), .Q(PC8_2), .clk(clk));  // open: clr
  Register #(.width(32)) register_8 (.D(multiplexer_8_out), .en(en), .Q(ALU_2), .clk(clk));  // open: clr
  Register #(.width(32)) register_9 (.D(multiplexer_9_out), .en(en), .Q(DM_2), .clk(clk));  // open: clr
  Register #(.width(32)) register_10 (.D(multiplexer_10_out), .en(en), .Q(standBy_2), .clk(clk));  // open: clr
endmodule

module Hazard_11 (
  input  isRead_Rs_D,
  input  [4:0] Rs_D,
  input  [1:0] Tuse_Rs_D,
  input  isRead_Rt_D,
  input  [4:0] Rt_D,
  input  [1:0] Tuse_Rt_D,
  input  isWrite_E,
  input  [4:0] WriteDes_E,
  input  [1:0] Tnew_E,
  input  isWrite_M,
  input  [4:0] WriteDes_M,
  input  [1:0] Tnew_M,
  output stallPC,
  output stallID,
  output flushEX
);

  wire and_1_out, and_2_out, and_3_out, and_4_out, comparator_1_eq, comparator_2_lt, comparator_3_lt,
       comparator_4_eq, comparator_5_lt, comparator_6_lt, comparator_7_eq, comparator_8_lt, comparator_9_lt,
       comparator_10_eq, comparator_11_lt, comparator_12_lt, not_1_out, not_2_out, not_3_out, not_4_out;

  Comparator #(.width(5), .mode("unsigned")) comparator_1 (
    .a(Rs_D), .b(WriteDes_E), .eq(comparator_1_eq));  // open: gt, lt
  Comparator #(.width(5), .mode("unsigned")) comparator_2 (
    .a(Rs_D), .b({5{1'b0}}), .lt(comparator_2_lt));  // open: gt, eq
  Comparator #(.width(2), .mode("unsigned")) comparator_3 (
    .a(Tuse_Rs_D), .b(Tnew_E), .lt(comparator_3_lt));  // open: gt, eq
  Comparator #(.width(5), .mode("unsigned")) comparator_4 (
    .a(Rt_D), .b(WriteDes_E), .eq(comparator_4_eq));  // open: gt, lt
  Comparator #(.width(5), .mode("unsigned")) comparator_5 (
    .a(Rt_D), .b({5{1'b0}}), .lt(comparator_5_lt));  // open: gt, eq
  Comparator #(.width(2), .mode("unsigned")) comparator_6 (
    .a(Tuse_Rt_D), .b(Tnew_E), .lt(comparator_6_lt));  // open: gt, eq
  Comparator #(.width(5), .mode("unsigned")) comparator_7 (
    .a(Rs_D), .b(WriteDes_M), .eq(comparator_7_eq));  // open: gt, lt
  Comparator #(.width(5), .mode("unsigned")) comparator_8 (
    .a(Rs_D), .b({5{1'b0}}), .lt(comparator_8_lt));  // open: gt, eq
  Comparator #(.width(2), .mode("unsigned")) comparator_9 (
    .a(Tuse_Rs_D), .b(Tnew_M), .lt(comparator_9_lt));  // open: gt, eq
  Comparator #(.width(5), .mode("unsigned")) comparator_10 (
    .a(Rt_D), .b(WriteDes_M), .eq(comparator_10_eq));  // open: gt, lt
  Comparator #(.width(5), .mode("unsigned")) comparator_11 (
    .a(Rt_D), .b({5{1'b0}}), .lt(comparator_11_lt));  // open: gt, eq
  Comparator #(.width(2), .mode("unsigned")) comparator_12 (
    .a(Tuse_Rt_D), .b(Tnew_M), .lt(comparator_12_lt));  // open: gt, eq
  not not_1 (not_1_out, comparator_2_lt);
  not not_2 (not_2_out, comparator_5_lt);
  not not_3 (not_3_out, comparator_8_lt);
  not not_4 (not_4_out, comparator_11_lt);
  and and_1 (and_1_out, isRead_Rs_D, isWrite_E, comparator_1_eq, not_1_out, comparator_3_lt);
  and and_2 (and_2_out, isRead_Rt_D, isWrite_E, comparator_4_eq, not_2_out, comparator_6_lt);
  and and_3 (and_3_out, isRead_Rs_D, isWrite_M, comparator_7_eq, not_3_out, comparator_9_lt);
  and and_4 (and_4_out, isRead_Rt_D, isWrite_M, comparator_10_eq, not_4_out, comparator_12_lt);
  or or_1 (flushEX, and_1_out, and_2_out, and_3_out, and_4_out);

  assign stallID = flushEX;
  assign stallPC = flushEX;

  // Notes on the sheet:
  //   D读E写 Rs
  //   D读E写 Rt
  //   D读M写 Rs
  //   D读M写 Rt
endmodule

module ForwardUnit_13 (
  input  isRead,
  input  [4:0] ReadDes,
  input  [1:0] Tuse,
  input  isWrite,
  input  [4:0] WriteDes,
  input  [1:0] Tnew,
  output NeedForward
);

  wire comparator_1_eq, comparator_2_eq, comparator_3_eq, comparator_4_eq, not_1_out;

  Comparator #(.width(5), .mode("unsigned")) comparator_1 (
    .a(ReadDes), .b(WriteDes), .eq(comparator_1_eq));  // open: gt, lt
  Comparator #(.width(5), .mode("unsigned")) comparator_2 (
    .a(ReadDes), .b({5{1'b0}}), .eq(comparator_2_eq));  // open: gt, lt
  Comparator #(.width(2), .mode("unsigned")) comparator_3 (.a(Tuse), .b(2'b00), .eq(comparator_3_eq));  // open: gt, lt
  Comparator #(.width(2), .mode("unsigned")) comparator_4 (.a(Tnew), .b(2'b00), .eq(comparator_4_eq));  // open: gt, lt
  not not_1 (not_1_out, comparator_2_eq);
  and and_1 (NeedForward, isRead, isWrite, comparator_1_eq, not_1_out, comparator_3_eq, comparator_4_eq);
endmodule
