// Logisim project 同步复位流水线-改进-A3-ing.circ as structural Verilog: 17 circuits, main circuit IM_01
module IM_01 (
  input  [31:0] PC,
  output [31:0] Ins
);

  wire [31:0] subtractor_1_out;

  Subtractor #(.width(32)) subtractor_1 (.a(PC), .b(32'h3000), .out(subtractor_1_out));  // open: bin, bout
  ROM #(.addrWidth(12), .dataWidth(32)) rom_1 (.addr(subtractor_1_out[13:2]), .data(Ins));  // open: sel

  // Notes on the sheet:
  //   输入：PC，用于选择需要ROM中的哪个指令
  //   contents of rom_1 (hex, n*v repeats v):
  //   34010006 34020009 34030005 34040009 34050007 34060004 3407000a 34080008 3409000a 340a0004 340b0009
  //   340c000c 340d0006 340e000a 340f0004 34100005 34110005 3412000c 34130008 34140008 34150005 34160008
  //   34170007 34180003 34190008 341a000a 341b0005 341c000c 341d0008 341e000c 0 c000c24 0 0 c000c4d 0 0
  //   3c020010 340f0008 adfb0050 35490088 17d5822 0 3dcb820 0 0 13c7820 3f9820 34180014 8f050044 258f022
  //   2592022 34050004 acbd0078 0 3405000c acb50000 0 3c1d0186 3404000c ac96005c 341e0004 8fcf008c 0
  //   340d0018 ada30034 377001a1 11a9020 367d003c 0 34150004 aebd0024 37f50012 340d0004 adb20004 12afffd5
  //   0 c000c53 0 340f0014 adf50034 c000c7b 0 2936022 1fcf022 0 0 35b500e3 340a0018 8d5d0044 34100008
  //   ae070020 3414000c 8e940048 3c120032 2c3822 1816820 37bd020 341c0018 8f9b0044 0 4ff822 3c050112
  //   34170018 8eeb0028 2bb2820 34120010 ae41000c 3708020 3cf5822 34c8007a 1eda020 37980167 34130004
  //   ae700010 3c04004c 3f0b820 34070004 8cf60000 0 0 1024ffd5 0 c000c80 0 0 c000ca8 0 34150008 8eb8008c
  //   342901c2 34040004 8c930074 0 0 34080008 8d0a001c 37df822 1d3822 362f00be 3dbd820 362800bd 3706004c
  //   1f89820 185b020 27b8820 0 34120004 ae400068 0 1941822 1088820 340e000c 8dc7000c 19b8022 37ea019f
  //   2197022 0 35b820 34130018 8e780050 340c0010 8d900048 34190008 8f240090 3c1700a6 12d9ffd6 0 13a50001
  //   0 20d0822 34d60182 0 34180014 8f040018 340a0008 8d440008 34170018 8eeb0060 0 341d0018 8faa0044
  //   340d0018 8da10028 3c0900a8 27ad022 e21820 3c030046 3c0b0180 0 3c1b01be 278f022 1958022 0 34060008
  //   accf003c 34950051 340a0010 ad5b0014 340e000c addc003c 34070008 8cf4002c 292c020 34100010 8e1c0060
  //   3c100089 35e20153 131f0028 0 341d0018 8fb10098 10ff822 340f0014 adef0068 1453822 2283822 3b9822
  //   34160004 aed20004 0 340f0004 8df50098 804822 0 3c160120 165a820 34110008 ae21004c 34090010 ad370054
  //   3c1d01c6 3f14820 2897820 0 3c5820 0 36da0121 2084820 341c0014 8f870030 341c0018 8f87001c 3419020
  //   340c0004 8d830088 0 11260001 0 3c18004f b69020 340b0014 ad630054 0 0 4a7022 0 e01022 36630122
  //   3c150007 0 0 3c0c0036 34080010 8d09001c 0 8c190030 341b0014 8f79004c 7bf822 0 340a0018 8d4d00a0 0
  //   34140004 ae9d0038 340c000c 8d91009c 345c00e2 0 37b00012 3c030159 3413000c 8e640070 37740143 3c140020
  //   10390001 0 3c1a0199 34110014 8e2d0094 3c1d0060 0 310c020 314d020 3411820 3408000c 8d1d002c 0 233c820
  //   36d40108 34260049 34180004 8f030008 0 34060014 accc008c 366a00cd b3c020 3c130037 c56022 f1c022 0 0
  //   340f0004 ade70048 34040010 ac800040 357e013e 367f0001 37b4822 36bc00ac 376500bc 10630001 0 0
  //   34140008 8e930068 34080010 ad15004c 378801c4 34050018 acbb0094 0 199c022 37a3020 34100008 ae130098
  //   34090010 ad3f009c 3c020110 340a0014 8d5d00a0 34100014 ae0d0020 0 0 8c1c007c 0 875822 36ea0050 439822
  //   e79820 34190010 8f3b0074 3596012a 343000e5 0 2523822 34010014 ac36009c 3c150151 2b04822 34140014
  //   ae8b0054 11c50001 0 34d901b3 3c170078 340e0014 adcf0098 3c1500e6 3c010155 254822 34cf0049 379000c5
  //   341b0014 8f780040 3c1f00ed 374e009e 0 341a0004 af410044 36a7013b 0 34040008 ac8e0020 366c018c
  //   1698020 36d30165 ac040064 3c1b019f 3c170101 34050008 8ca400a0 24f3020 0 3c1000c2 3c0d006e 582020 0
  //   3c180120 10930001 0 22fb822 340e000c add60070 583022 0 99c820 340b0018 8d71003c 19a3822 3416000c
  //   8ec5004c 3c160085 0 3c1800ae 3c18006c 353b01be 3c0100a6 3c0b00e0 586822 8c130080 341d0004 8fba004c 0
  //   35570031 312d020 14fd822 34090008 ad230004 2dc822 340c0014 8d82005c f37820 3c1f00ab 0 352c000a
  //   35e101bb 12a20001 0 340a0008 ad44007c 3c10011b 3411000c ae260004 0 34030010 ac770094 8c050090
  //   34170010 8ef3004c 370c0159 0 34110018 8e250064 3c0701c5 34130008 8e6d0090 bb2820 234a820 34090014
  //   ad260048 254d020 34050018 8ca10030 33a5020 340e000c adde0054 373b022 3c010139 2d99020 34080018
  //   ad090098 3c110098 3413000c 8e7b0074 3c020036 0 34150018 aeaa0004 602820 13590001 0 2515822 3c1d01a6
  //   71022 34160014 8ec70024 0 36eb019d 3c1501c5 347f010c 0 3c0401be 36f50083 f59822 359600cd 0 34050010
  //   acb40060 3c01004b 14a3822 340f0010 adf70000 340a0008 8d550064 2f0a822 e81022 13b822 34090014
  //   ad350094 0 2ef9820 0 0 3c0601a7 38f7022 13ec022 13b30001 0 3402000c ac490024 0 d83822 340d000c ad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
  //   输出：instr，ROM中指令被取出
endmodule

module PC_02 (
  input  [31:0] NPC,
  input  clk,
  input  rst,
  input  en,
  output [31:0] PC
);

  wire comparator_1_eq;
  wire [31:0] PC_q;

  Register #(.width(32)) u_PC (.D(NPC), .en(en), .Q(PC_q), .clk(clk), .clr(rst));
  Multiplexer #(.width(32), .enable("false")) multiplexer_1 (
    .in0(PC_q), .in1(32'h3000), .out(PC), .sel(comparator_1_eq));
  Comparator #(.width(32), .mode("unsigned")) comparator_1 (
    .a(PC_q), .b({32{1'b0}}), .eq(comparator_1_eq));  // open: gt, lt

  // Notes on the sheet:
  //   输入：时钟；异步复位
  //   输入：NPC，下一条指令地址
  //   输出：PC，当前指令地址
endmodule

module NPC_03 (
  input  [31:0] PC_F,
  input  [31:0] PC_D,
  input  [31:0] Rs,
  input  [15:0] imm,
  input  [25:0] ins_index,
  input  isJr,
  input  isJ,
  input  isBranchSuccess,
  output [31:0] NPC
);

  wire [31:0] bit_extender_1_out, \desBranch_b指令 , multiplexer_1_out, multiplexer_2_out, PC4_D, PC4_F;

  assign bit_extender_1_out = {{14{imm[15]}}, {imm, 2'b00}};  // Bit_Extender bit_extender_1
  Adder #(.width(32)) adder_1 (.a(bit_extender_1_out), .b(PC4_D), .out(\desBranch_b指令 ));  // open: cin, cout
  Adder #(.width(32)) adder_2 (.a(PC_F), .b(32'h4), .out(PC4_F));  // open: cin, cout
  Adder #(.width(32)) adder_3 (.a(PC_D), .b(32'h4), .out(PC4_D));  // open: cin, cout
  Multiplexer #(.width(32), .enable("false")) multiplexer_1 (
    .in0(PC4_F), .in1(Rs), .out(multiplexer_1_out), .sel(isJr));
  Multiplexer #(.width(32), .enable("false")) multiplexer_2 (
    .in0(multiplexer_1_out), .in1(\desBranch_b指令 ), .out(multiplexer_2_out), .sel(isBranchSuccess));
  Multiplexer #(.width(32), .enable("false")) multiplexer_3 (
    .in0(multiplexer_2_out), .in1({PC_D[31:28], ins_index, 2'b00}), .out(NPC), .sel(isJ));

  // Other names for the same wires on the sheet: desJal_jal[31:2] = {PC_D[31:28], ins_index}; desRs_jr[31:0] = Rs

  // Notes on the sheet:
  //   指令有：
  //   输入：PC，当前PC值
  //   R: addu 下一跳是PC+4
  //   R: subu 下一跳是PC+4
  //   R: jr 下一跳是Rs的内容
  //   I: ori 下一跳是PC+4
  //   I: lw 下一跳是PC+4
  //   I: sw 下一跳是PC+4
  //   I: lui 下一条是PC+4
  //   J: jal 下一条是PC[31:28]|26|00
  //   I: beq 下一跳是PC+4+imm(符扩)|00
  //   输入：Rs内容,是不是j,是不是jr
  //   输入：imm,是不是branch,有没有成功beq
  //   输入：ins_index，是不是j，是不是jal
  //   输出：PC+4，jal要用，要存进$ra
  //   输出：NPC，根据输入层层选择后得到
endmodule

module GRF_04 (
  input  clk,
  input  rst,
  input  [4:0] A1,
  input  [4:0] A2,
  input  [4:0] A3,
  input  [31:0] WD,
  output [31:0] RD1,
  output [31:0] RD2
);

  wire and_1_out, and_2_out, comparator_1_eq, comparator_2_eq, comparator_3_eq, comparator_4_eq, not_1_out,
       not_2_out;
  wire [31:0] in01, in02, in03, in04, in05, in06, in07, in08, in09, in10, in11, in12, in13, in14, in15, in16,
       in17, in18, in19, in20, in21, in22, in23, in24, in25, in26, in27, in28, in29, in30, in31,
       multiplexer_1_out, multiplexer_2_out, out00, out01, out02, out03, out04, out05, out06, out07, out08,
       out09, out10, out11, out12, out13, out14, out15, out16, out17, out18, out19, out20, out21, out22,
       out23, out24, out25, out26, out27, out28, out29, out30, out31;

  Register #(.width(32)) register_1 (.D({32{1'b0}}), .en(1'b1), .Q(out00), .clk(clk), .clr(rst));
  Register #(.width(32)) register_2 (.D(in01), .en(1'b1), .Q(out01), .clk(clk), .clr(rst));
  Register #(.width(32)) register_3 (.D(in02), .en(1'b1), .Q(out02), .clk(clk), .clr(rst));
  Register #(.width(32)) register_4 (.D(in03), .en(1'b1), .Q(out03), .clk(clk), .clr(rst));
  // Probe on out00
  // Probe on out01
  // Probe on out02
  // Probe on out03
  // Probe on out04
  // Probe on out05
  // Probe on out06
  // Probe on out07
  // Probe on out08
  // Probe on out09
  // Probe on out10
  // Probe on out11
  // Probe on out12
  // Probe on out13
  // Probe on out14
  // Probe on out15
  // Probe on out16
  // Probe on out17
  // Probe on out18
  // Probe on out19
  // Probe on out20
  // Probe on out21
  // Probe on out22
  // Probe on out23
  // Probe on out24
  // Probe on out25
  // Probe on out26
  // Probe on out27
  // Probe on out28
  // Probe on out29
  // Probe on out30
  // Probe on out31
  Register #(.width(32)) register_5 (.D(in04), .en(1'b1), .Q(out04), .clk(clk), .clr(rst));
  Register #(.width(32)) register_6 (.D(in05), .en(1'b1), .Q(out05), .clk(clk), .clr(rst));
  Register #(.width(32)) register_7 (.D(in06), .en(1'b1), .Q(out06), .clk(clk), .clr(rst));
  Register #(.width(32)) register_8 (.D(in07), .en(1'b1), .Q(out07), .clk(clk), .clr(rst));
  Multiplexer #(.select(5), .width(32), .enable("false")) multiplexer_1 (
    .in0(out00), .in1(out01), .in2(out02), .in3(out03), .in4(out04), .in5(out05), .in6(out06), .in7(out07),
    .in8(out08), .in9(out09), .in10(out10), .in11(out11), .in12(out12), .in13(out13), .in14(out14),
    .in15(out15), .in16(out16), .in17(out17), .in18(out18), .in19(out19), .in20(out20), .in21(out21),
    .in22(out22), .in23(out23), .in24(out24), .in25(out25), .in26(out26), .in27(out27), .in28(out28),
    .in29(out29), .in30(out30), .in31(out31), .out(multiplexer_1_out), .sel(A1));
  Register #(.width(32)) register_9 (.D(in08), .en(1'b1), .Q(out08), .clk(clk), .clr(rst));
  Register #(.width(32)) register_10 (.D(in09), .en(1'b1), .Q(out09), .clk(clk), .clr(rst));
  Register #(.width(32)) register_11 (.D(in10), .en(1'b1), .Q(out10), .clk(clk), .clr(rst));
  Register #(.width(32)) register_12 (.D(in11), .en(1'b1), .Q(out11), .clk(clk), .clr(rst));
  Multiplexer #(.select(5), .width(32), .enable("false")) multiplexer_2 (
    .in0(out00), .in1(out01), .in2(out02), .in3(out03), .in4(out04), .in5(out05), .in6(out06), .in7(out07),
    .in8(out08), .in9(out09), .in10(out10), .in11(out11), .in12(out12), .in13(out13), .in14(out14),
    .in15(out15), .in16(out16), .in17(out17), .in18(out18), .in19(out19), .in20(out20), .in21(out21),
    .in22(out22), .in23(out23), .in24(out24), .in25(out25), .in26(out26), .in27(out27), .in28(out28),
    .in29(out29), .in30(out30), .in31(out31), .out(multiplexer_2_out), .sel(A2));
  Register #(.width(32)) register_13 (.D(in12), .en(1'b1), .Q(out12), .clk(clk), .clr(rst));
  Register #(.width(32)) register_14 (.D(in13), .en(1'b1), .Q(out13), .clk(clk), .clr(rst));
  Register #(.width(32)) register_15 (.D(in14), .en(1'b1), .Q(out14), .clk(clk), .clr(rst));
  Register #(.width(32)) register_16 (.D(in15), .en(1'b1), .Q(out15), .clk(clk), .clr(rst));
  Demultiplexer #(.select(5), .width(32), .tristate("true"), .enable("false")) demultiplexer_1 (
    .out1(in01), .out2(in02), .out3(in03), .out4(in04), .out5(in05), .out6(in06), .out7(in07), .out8(in08),
    .out9(in09), .out10(in10), .out11(in11), .out12(in12), .out13(in13), .out14(in14), .out15(in15),
    .out16(in16), .out17(in17), .out18(in18), .out19(in19), .out20(in20), .out21(in21), .out22(in22),
    .out23(in23), .out24(in24), .out25(in25), .out26(in26), .out27(in27), .out28(in28), .out29(in29),
    .out30(in30), .out31(in31), .in(WD), .sel(A3));  // open: out0
  Register #(.width(32)) register_17 (.D(in16), .en(1'b1), .Q(out16), .clk(clk), .clr(rst));
  Register #(.width(32)) register_18 (.D(in17), .en(1'b1), .Q(out17), .clk(clk), .clr(rst));
  Register #(.width(32)) register_19 (.D(in18), .en(1'b1), .Q(out18), .clk(clk), .clr(rst));
  Register #(.width(32)) register_20 (.D(in19), .en(1'b1), .Q(out19), .clk(clk), .clr(rst));
  Register #(.width(32)) register_21 (.D(in20), .en(1'b1), .Q(out20), .clk(clk), .clr(rst));
  Register #(.width(32)) register_22 (.D(in21), .en(1'b1), .Q(out21), .clk(clk), .clr(rst));
  Register #(.width(32)) register_23 (.D(in22), .en(1'b1), .Q(out22), .clk(clk), .clr(rst));
  Register #(.width(32)) register_24 (.D(in23), .en(1'b1), .Q(out23), .clk(clk), .clr(rst));
  Comparator #(.width(5), .mode("unsigned")) comparator_1 (.a(A1), .b(A3), .eq(comparator_1_eq));  // open: gt, lt
  Comparator #(.width(5), .mode("unsigned")) comparator_2 (
    .a(A1), .b({5{1'b0}}), .eq(comparator_2_eq));  // open: gt, lt
  not not_1 (not_1_out, comparator_2_eq);
  Comparator #(.width(5), .mode("unsigned")) comparator_3 (.a(A2), .b(A3), .eq(comparator_3_eq));  // open: gt, lt
  not not_2 (not_2_out, comparator_4_eq);
  Comparator #(.width(5), .mode("unsigned")) comparator_4 (
    .a(A2), .b({5{1'b0}}), .eq(comparator_4_eq));  // open: gt, lt
  Multiplexer #(.width(32), .enable("false")) multiplexer_3 (
    .in0(multiplexer_1_out), .in1(WD), .out(RD1), .sel(and_1_out));
  and and_1 (and_1_out, comparator_1_eq, 1'b1, not_1_out);
  Multiplexer #(.width(32), .enable("false")) multiplexer_4 (
    .in0(multiplexer_2_out), .in1(WD), .out(RD2), .sel(and_2_out));
  and and_2 (and_2_out, comparator_3_eq, 1'b1, not_2_out);
  Register #(.width(32)) register_25 (.D(in24), .en(1'b1), .Q(out24), .clk(clk), .clr(rst));
  Register #(.width(32)) register_26 (.D(in25), .en(1'b1), .Q(out25), .clk(clk), .clr(rst));
  Register #(.width(32)) register_27 (.D(in26), .en(1'b1), .Q(out26), .clk(clk), .clr(rst));
  Register #(.width(32)) register_28 (.D(in27), .en(1'b1), .Q(out27), .clk(clk), .clr(rst));
  Register #(.width(32)) register_29 (.D(in28), .en(1'b1), .Q(out28), .clk(clk), .clr(rst));
  Register #(.width(32)) register_30 (.D(in29), .en(1'b1), .Q(out29), .clk(clk), .clr(rst));
  Register #(.width(32)) register_31 (.D(in30), .en(1'b1), .Q(out30), .clk(clk), .clr(rst));
  Register #(.width(32)) register_32 (.D(in31), .en(1'b1), .Q(out31), .clk(clk), .clr(rst));

  // Notes on the sheet:
  //   输入：A1，A2，A3选址
  //   输入：时钟；异步复位；写入使能
  //   输出：RD1，RD2读出
  //   输出：RD1，RD2读出
endmodule

module ALU_05 (
  input  [31:0] A,
  input  [31:0] B,
  input  [2:0] ALUOp,
  output [31:0] C
);

  wire [31:0] adder_1_out, and_1_out, or_1_out, shifter_1_out, subtractor_1_out;

  Adder #(.width(32)) adder_1 (.a(A), .b(B), .out(adder_1_out));  // open: cin, cout
  Subtractor #(.width(32)) subtractor_1 (.a(A), .b(B), .out(subtractor_1_out));  // open: bin, bout
  assign and_1_out = A & B;  // AND_Gate and_1, 32 bits wide
  assign or_1_out = A | B;  // OR_Gate or_1, 32 bits wide
  Shifter #(.width(32)) shifter_1 (.in(B), .\dist (5'b10000), .out(shifter_1_out));
  Multiplexer #(.select(3), .width(32), .enable("false")) multiplexer_1 (
    .in0(adder_1_out), .in1(subtractor_1_out), .in2(and_1_out), .in3(or_1_out), .in4(shifter_1_out), .out(C),
    .sel(ALUOp));  // open: in5, in6, in7

  // Notes on the sheet:
  //   输入：计算方式选择
  //   R: jr 无
  //   I: ori 011
  //   I: lw 无
  //   I: sw 无
  //   I: beq 无
  //   J: jal 无
  //   输入：A，B两个等待计算的数字
  //   R: addu 000
  //   R: subu 001
  //   I: andi 010-实验中不涉及这条指令，但还是预留一个坑位
  //   I: lui 100 lui对于imm，0扩成32位后传入输入A，之后的处理在ALU中完成
  //   输出：C计算结果
  //   输出：A是否等于B
  //   输出：A是否等于B
endmodule

module DM_06 (
  input  [31:0] A,
  input  [31:0] WD,
  input  WE,
  input  clk,
  input  reset,
  output [31:0] RD
);

  RAM #(.addrWidth(12), .dataWidth(32), .bus("separate")) ram_1 (
    .addr(A[13:2]), .din(WD), .data(RD), .str(WE), .clk(clk), .clr(reset));  // open: sel, ld

  // Notes on the sheet:
  //   输入:clk，reset
  //   输入:写使能，写内容
  //   输入:选址信号[31:0]，取[13:2]用来选址
  //   输出：读内容
endmodule

module EXT_07 (
  input  [15:0] imm,
  input  zeroOrSigned,
  output [31:0] immHasExted
);

  wire [31:0] bit_extender_1_out, bit_extender_2_out;

  assign bit_extender_1_out = {{16{1'b0}}, imm};  // Bit_Extender bit_extender_1
  assign bit_extender_2_out = {{16{imm[15]}}, imm};  // Bit_Extender bit_extender_2
  Multiplexer #(.width(32), .enable("false")) multiplexer_1 (
    .in0(bit_extender_1_out), .in1(bit_extender_2_out), .out(immHasExted), .sel(zeroOrSigned));

  // Notes on the sheet:
  //   输入:0扩展还是符号扩展
  //   I: ori 0扩展
  //   I: lw 符号扩展
  //   I: sw 符号扩展
  //   I: beq NPC中处理
  //   I: lui ALU中处理
  //   输入:imm[15:0]，不经过任何处理输入
  //   输出：扩展成32位
endmodule

module ALUOp_5to3zip (
  input  addu,
  input  subu,
  input  andi,
  input  ori,
  input  lui,
  output o2,
  output o1,
  output o0
);

  wire not_1_out, not_2_out, not_3_out, not_4_out, not_5_out, not_6_out;

  not not_1 (not_1_out, addu);
  not not_2 (not_2_out, subu);
  not not_3 (not_3_out, lui);
  not not_4 (not_4_out, addu);
  not not_5 (not_5_out, andi);
  not not_6 (not_6_out, lui);
  and and_1 (o1, not_1_out, not_2_out, not_3_out);
  and and_2 (o0, not_4_out, not_5_out, not_6_out);

  assign o2 = lui;
endmodule

module main2 (
  input  rst
);

  wire ALU_B_01, ALU_immExt_02, and_1_out, clk, CMP_isequal, DM_WE, flushEX, isRead_A1_D, isRead_A1_E,
       isRead_A1_M, isRead_A1_W, isRead_A2_D, isRead_A2_E, isRead_A2_M, isRead_A2_W, isRead_A3_D,
       isRead_A3_E, isRead_A3_M, isRead_A3_W, isRead_Rs_D, isRead_Rs_E, isRead_Rs_M, isRead_Rt_D,
       isRead_Rt_E, isRead_Rt_M, not_1_out, not_2_out, NPC_isBeq_03, NPC_isJ_02, NPC_isJr_01, or_1_out,
       OutSelect_D, OutSelect_E, OutSelect_M, stallID, stallPC;
  wire [1:0] Tnew_D, Tnew_E, Tnew_M, Tnew_W, Tuse_A1_D, Tuse_A1_E, Tuse_A1_M, Tuse_A1_W, Tuse_A2_D,
       Tuse_A2_E, Tuse_A2_M, Tuse_A2_W, Tuse_A3_D, Tuse_A3_E, Tuse_A3_M, Tuse_A3_W;
  wire [2:0] ALUOp_03;
  wire [4:0] A1_D, A1_E, A1_M, A1_W, A2_D, A2_E, A2_M, A2_W, A3_D, A3_E, A3_M, A3_W, Rs_D, Rs_E, Rs_M, Rt_D,
       Rt_E, Rt_M;
  wire [10:0] imm_D, imm_E, imm_M, imm_W;
  wire [31:0] adder_1_out, ALU_C, Data_D_final, Data_E, Data_E_final, Data_M, Data_M_final, Data_W, DM_A,
       DM_RD, EXT_immhasexted, IR_F, multiplexer_3_out, NPC, PC_D, PC_E, PC_F, PC_M, PC_W, RD1_D,
       RD1_D_final, RD1_E, RD1_E_final, RD1_M, RD1_M_final, RD1_W, RD2_D, RD2_D_final, RD2_E, RD2_E_final,
       RD2_M, RD2_M_final, RD2_W;
  wire [31:26] IR_D, IR_E, IR_M, IR_W;

  // Probe on PC_F
  // Probe on IR_F
  Clock clock_1 (.out(clk));
  PC_02 PC (.NPC(NPC), .clk(clk), .rst(rst), .en(not_1_out), .PC(PC_F));
  not not_1 (not_1_out, stallPC);
  // Probe on PC_D
  // Probe on {IR_D, A1_D, A2_D, A3_D, imm_D}
  // Probe on NPC
  Hazard_n_11 Hazard (
    .isRead_A1_D(isRead_A1_D), .Tuse_A1_D(Tuse_A1_D), .A1_D(A1_D), .A3_E(A3_E), .Tnew_E(Tnew_E), .A3_M(A3_M),
    .Tnew_M(Tnew_M), .stallPC(stallPC), .stallID(stallID), .flushEX(flushEX), .isRead_A2_D(isRead_A2_D),
    .Tuse_A2_D(Tuse_A2_D), .A2_D(A2_D), .isRead_A3_D(isRead_A3_D), .Tuse_A3_D(Tuse_A3_D), .A3_D(A3_D));
  // Probe on RD1_D_final
  // Probe on RD2_D_final
  IM_01 IM (.PC(PC_F), .Ins(IR_F));
  // Probe on PC_E
  // Probe on {IR_E, A1_E, A2_E, A3_E, imm_E}
  // Probe on RD1_E
  // Probe on RD2_E
  // Probe on RD1_E_final
  // Probe on RD2_E_final
  // Probe on Data_E
  // Probe on {A3_E, imm_E}
  // Probe on ALU_C
  Forward_13 Forward (
    .D_A1(Rs_D), .D_A2(Rt_D), .D_Use_1(isRead_Rs_D), .D_Use_2(isRead_Rt_D), .D_RD1(RD1_D), .D_RD2(RD2_D),
    .D_A3(A3_D), .E_A1(Rs_E), .E_A2(Rt_E), .E_Use_1(isRead_Rs_E), .E_Use_2(isRead_Rt_E), .E_RD1(RD1_E),
    .E_RD2(RD2_E), .E_A3(A3_E), .M_A1(Rs_M), .M_A2(Rt_M), .M_Use_1(isRead_Rs_M), .M_Use_2(isRead_Rt_M),
    .M_RD1(RD1_M), .M_RD2(RD2_M), .M_A3(A3_M), .W_A3(A3_W), .Data_E(Data_E), .Data_M(Data_M),
    .Data_W(Data_W), .RD1_D_final(RD1_D_final), .RD2_D_final(RD2_D_final), .RD1_E_final(RD1_E_final),
    .RD2_E_final(RD2_E_final), .RD1_M_final(RD1_M_final), .RD2_M_final(RD2_M_final));
  // Probe on PC_M
  // Probe on {IR_M, A1_M, A2_M, A3_M, imm_M}
  // Probe on RD1_M_final
  // Probe on RD2_M_final
  // Probe on Data_M
  // Probe on PC_W
  // Probe on {IR_W, A1_W, A2_W, A3_W, imm_W}
  // Probe on Data_W
  DEMW_n_10 ID (
    .IR(IR_F), .PC(PC_F), .IR_2({IR_D, A1_D, A2_D, A3_D, imm_D}), .PC_2(PC_D), .clk(clk), .reset(rst),
    .en(not_2_out));  // open: A3, Tuse_A1, Tuse_A2, Tnew, RD1, RD2, Data, A3_2, Tuse_A1_2, Tuse_A2_2, Tnew_2, RD1_2, RD2_2, Data_2, ALU, ALU_2, Tuse_A3, Tuse_A3_2
  not not_2 (not_2_out, stallID);
  Controller_n_08 ID_Controller (
    .ins({IR_D, A1_D, A2_D, A3_D, imm_D}), .NPC_isJr_01(NPC_isJr_01), .NPC_isJ_02(NPC_isJ_02),
    .NPC_isBeq_03(NPC_isBeq_03), .OutSelect_D(OutSelect_D), .A3_D(A3_D), .Tuse_A1_D(Tuse_A1_D),
    .Tuse_A2_D(Tuse_A2_D), .Tnew_D(Tnew_D), .isRead_A1(isRead_A1_D), .isRead_A2(isRead_A2_D),
    .Tuse_A3_D(Tuse_A3_D), .isRead_A3(isRead_A3_D));  // open: ALU_B_01, ALU_immExt_02, ALU_Op_03, OutSelect_E, DM_WE_01, OutSelect_M
  Adder #(.width(32)) adder_1 (.a(PC_D), .b(32'h8), .out(adder_1_out));  // open: cin, cout
  CMP_09 CMP (.Rs(RD1_D_final), .Rt(RD2_D_final), .isEqual(CMP_isequal));
  Multiplexer #(.width(32), .enable("false")) multiplexer_1 (
    .in1(adder_1_out), .out(Data_D_final), .sel(OutSelect_D));  // open: in0
  and and_1 (and_1_out, NPC_isBeq_03, CMP_isequal);
  GRF_04 GRF (.A1(Rs_D), .A2(Rt_D), .A3(A3_W), .WD(Data_W), .RD1(RD1_D), .RD2(RD2_D), .clk(clk), .rst(rst));
  NPC_03 u_NPC (
    .PC_F(PC_F), .Rs(RD1_D_final), .imm({A3_D, imm_D}), .ins_index({A1_D, A2_D, A3_D, imm_D}),
    .isJr(NPC_isJr_01), .isJ(NPC_isJ_02), .isBranchSuccess(and_1_out), .NPC(NPC), .PC_D(PC_D));
  DEMW_n_10 EX (
    .IR({IR_D, A1_D, A2_D, A3_D, imm_D}), .PC(PC_D), .A3(A3_D), .Tuse_A1(Tuse_A1_D), .Tuse_A2(Tuse_A2_D),
    .Tnew(Tnew_D), .RD1(RD1_D_final), .RD2(RD2_D_final), .Data(Data_D_final),
    .IR_2({IR_E, A1_E, A2_E, A3_E, imm_E}), .PC_2(PC_E), .A3_2(A3_E), .Tuse_A1_2(Tuse_A1_E),
    .Tuse_A2_2(Tuse_A2_E), .Tnew_2(Tnew_E), .RD1_2(RD1_E), .RD2_2(RD2_E), .Data_2(Data_E), .clk(clk),
    .reset(or_1_out), .en(1'b1), .Tuse_A3(Tuse_A3_D), .Tuse_A3_2(Tuse_A3_E));  // open: ALU, ALU_2
  or or_1 (or_1_out, rst, flushEX);
  Controller_n_08 EX_Controller (
    .ins({IR_E, A1_E, A2_E, A3_E, imm_E}), .ALU_B_01(ALU_B_01), .ALU_immExt_02(ALU_immExt_02),
    .ALU_Op_03(ALUOp_03), .OutSelect_E(OutSelect_E), .isRead_A1(isRead_A1_E), .isRead_A2(isRead_A2_E),
    .isRead_A3(isRead_A3_E));  // open: NPC_isJr_01, NPC_isJ_02, NPC_isBeq_03, OutSelect_D, A3_D, Tuse_A1_D, Tuse_A2_D, Tnew_D, DM_WE_01, OutSelect_M, Tuse_A3_D
  EXT_07 EXT (.imm({A3_E, imm_E}), .zeroOrSigned(ALU_immExt_02), .immHasExted(EXT_immhasexted));
  Multiplexer #(.width(32), .enable("false")) multiplexer_2 (
    .in0(Data_E), .in1(ALU_C), .out(Data_E_final), .sel(OutSelect_E));
  Multiplexer #(.width(32), .enable("false")) multiplexer_3 (
    .in0(RD2_E_final), .in1(EXT_immhasexted), .out(multiplexer_3_out), .sel(ALU_B_01));
  ALU_05 ALU (.A(RD1_E_final), .B(multiplexer_3_out), .ALUOp(ALUOp_03), .C(ALU_C));
  Controller_n_08 MEM_Controller (
    .ins({IR_M, A1_M, A2_M, A3_M, imm_M}), .DM_WE_01(DM_WE), .OutSelect_M(OutSelect_M),
    .isRead_A1(isRead_A1_M), .isRead_A2(isRead_A2_M), .isRead_A3(isRead_A3_M));  // open: NPC_isJr_01, NPC_isJ_02, NPC_isBeq_03, OutSelect_D, A3_D, Tuse_A1_D, Tuse_A2_D, Tnew_D, ALU_B_01, ALU_immExt_02, ALU_Op_03, OutSelect_E, Tuse_A3_D
  DEMW_n_10 MEM (
    .IR({IR_E, A1_E, A2_E, A3_E, imm_E}), .PC(PC_E), .A3(A3_E), .Tuse_A1(Tuse_A1_E), .Tuse_A2(Tuse_A2_E),
    .Tnew(Tnew_E), .RD1(RD1_E_final), .RD2(RD2_E_final), .Data(Data_E_final),
    .IR_2({IR_M, A1_M, A2_M, A3_M, imm_M}), .PC_2(PC_M), .A3_2(A3_M), .Tuse_A1_2(Tuse_A1_M),
    .Tuse_A2_2(Tuse_A2_M), .Tnew_2(Tnew_M), .RD1_2(RD1_M), .RD2_2(RD2_M), .Data_2(Data_M), .clk(clk),
    .reset(rst), .en(1'b1), .ALU(ALU_C), .ALU_2(DM_A), .Tuse_A3(Tuse_A3_E), .Tuse_A3_2(Tuse_A3_M));
  Multiplexer #(.width(32), .enable("false")) multiplexer_4 (
    .in0(Data_M), .in1(DM_RD), .out(Data_M_final), .sel(OutSelect_M));
  DM_06 DM (.A(DM_A), .WD(RD2_M_final), .RD(DM_RD), .WE(DM_WE), .clk(clk), .reset(rst));
  DEMW_n_10 WB (
    .IR({IR_M, A1_M, A2_M, A3_M, imm_M}), .PC(PC_M), .A3(A3_M), .Tuse_A1(Tuse_A1_M), .Tuse_A2(Tuse_A2_M),
    .Tnew(Tnew_M), .RD1(RD1_M_final), .RD2(RD2_M_final), .Data(Data_M_final),
    .IR_2({IR_W, A1_W, A2_W, A3_W, imm_W}), .PC_2(PC_W), .A3_2(A3_W), .Tuse_A1_2(Tuse_A1_W),
    .Tuse_A2_2(Tuse_A2_W), .Tnew_2(Tnew_W), .RD1_2(RD1_W), .RD2_2(RD2_W), .Data_2(Data_W), .clk(clk),
    .reset(rst), .en(1'b1), .Tuse_A3(Tuse_A3_M), .Tuse_A3_2(Tuse_A3_W));  // open: ALU, ALU_2
  Controller_n_08 WB_Controller (
    .ins({IR_W, A1_W, A2_W, A3_W, imm_W}), .isRead_A1(isRead_A1_W), .isRead_A2(isRead_A2_W),
    .isRead_A3(isRead_A3_W));  // open: NPC_isJr_01, NPC_isJ_02, NPC_isBeq_03, OutSelect_D, A3_D, Tuse_A1_D, Tuse_A2_D, Tnew_D, ALU_B_01, ALU_immExt_02, ALU_Op_03, OutSelect_E, DM_WE_01, OutSelect_M, Tuse_A3_D

  // Other names for the same wires on the sheet: ins_index_D[25:0] = {A1_D, A2_D, A3_D, imm_D};
  //   IR_D[25:0] = {A1_D, A2_D, A3_D, imm_D}; imm_D[15:11] = A3_D; ins_index_E[25:0] = {A1_E, A2_E, A3_E, imm_E};
  //   IR_E[25:0] = {A1_E, A2_E, A3_E, imm_E}; imm_E[15:11] = A3_E; ins_index_M[25:0] = {A1_M, A2_M, A3_M, imm_M};
  //   IR_M[25:0] = {A1_M, A2_M, A3_M, imm_M}; imm_M[15:11] = A3_M; ins_index_W[25:0] = {A1_W, A2_W, A3_W, imm_W};
  //   IR_W[25:0] = {A1_W, A2_W, A3_W, imm_W}; imm_W[15:11] = A3_W

  // Notes on the sheet:
  //   F
  //   D
  //   E
  //   F
  //   M
  //   W
  //   送入下一流水级
  //   D
  //   立即被送出
  //   送入下一流水级
  //   E
  //   立即被送出
  //   送入下一流水级
  //   M
  //   立即被送出
  //   W
  //   W
endmodule

module CMP_09 (
  input  [31:0] Rs,
  input  [31:0] Rt,
  output isEqual
);

  Comparator #(.width(32)) comparator_1 (.a(Rs), .b(Rt), .eq(isEqual));  // open: gt, lt
endmodule

module ForwardUnit_13 (
  input  isRead,
  input  [4:0] ReadDes,
  input  [1:0] Tuse,
  input  [4:0] WriteDes,
  input  [1:0] Tnew,
  output NeedForward
);

  wire comparator_1_eq, comparator_2_eq, comparator_3_eq, not_1_out;

  Comparator #(.width(5), .mode("unsigned")) comparator_1 (
    .a(ReadDes), .b(WriteDes), .eq(comparator_1_eq));  // open: gt, lt
  Comparator #(.width(5), .mode("unsigned")) comparator_2 (
    .a(WriteDes), .b({5{1'b0}}), .eq(comparator_2_eq));  // open: gt, lt
  Comparator #(.width(2), .mode("unsigned")) comparator_3 (.a(Tnew), .b(2'b00), .eq(comparator_3_eq));  // open: gt, lt
  not not_1 (not_1_out, comparator_2_eq);
  and and_1 (NeedForward, isRead, 1'b1, comparator_1_eq, not_1_out, comparator_3_eq);
endmodule

module Controller_n_08 (
  input  [31:0] ins,
  output NPC_isJr_01,
  output NPC_isJ_02,
  output NPC_isBeq_03,
  output OutSelect_D,
  output [4:0] A3_D,
  output [1:0] Tuse_A1_D,
  output [1:0] Tuse_A2_D,
  output [1:0] Tuse_A3_D,
  output [1:0] Tnew_D,
  output ALU_B_01,
  output ALU_immExt_02,
  output [2:0] ALU_Op_03,
  output OutSelect_E,
  output DM_WE_01,
  output OutSelect_M,
  output isRead_A1,
  output isRead_A2,
  output isRead_A3
);

  wire addu, isCal_i, isCal_r, isLoad, isR, lui, not_1_out, not_2_out, not_3_out, not_4_out, not_5_out,
       not_6_out, not_7_out, not_8_out, not_9_out, not_10_out, not_11_out, not_12_out, or_3_out, or_4_out,
       or_7_out, or_8_out, or_10_out, or_13_out, ori, subu;
  wire [1:0] multiplexer_6_out, multiplexer_7_out, multiplexer_8_out, multiplexer_12_out, multiplexer_15_out;
  wire [4:0] multiplexer_2_out, multiplexer_5_out, multiplexer_9_out;

  not not_1 (not_1_out, ins[30]);
  not not_2 (not_2_out, ins[29]);
  not not_3 (not_3_out, ins[31]);
  not not_4 (not_4_out, ins[26]);
  not not_5 (not_5_out, ins[27]);
  not not_6 (not_6_out, ins[28]);
  or or_1 (isCal_r, addu, subu);
  or or_2 (isCal_i, ori, lui);
  not not_7 (not_7_out, ins[5]);
  not not_8 (not_8_out, ins[4]);
  not not_9 (not_9_out, ins[1]);
  not not_10 (not_10_out, ins[2]);
  not not_11 (not_11_out, ins[3]);
  not not_12 (not_12_out, ins[0]);
  and and_1 (isR, not_3_out, not_1_out, not_2_out, not_6_out, not_5_out, not_4_out);
  and and_2 (addu, isR, ins[5], not_8_out, not_11_out, not_10_out, not_9_out, not_12_out);
  and and_3 (subu, isR, ins[5], not_8_out, not_11_out, not_10_out, ins[1], not_12_out);
  and and_4 (NPC_isJr_01, isR, not_7_out, not_8_out, ins[3], not_10_out, not_9_out, not_12_out);
  and and_5 (ori, not_3_out, not_1_out, ins[29], ins[28], not_5_out, ins[26]);
  and and_6 (isLoad, ins[31], not_1_out, not_2_out, not_6_out, ins[27], ins[26]);
  and and_7 (DM_WE_01, ins[31], not_1_out, ins[29], not_6_out, ins[27], ins[26]);
  and and_8 (NPC_isBeq_03, not_3_out, not_1_out, not_2_out, ins[28], not_5_out, not_4_out);
  and and_9 (lui, not_3_out, not_1_out, ins[29], ins[28], ins[27], ins[26]);
  and and_10 (NPC_isJ_02, not_3_out, not_1_out, not_2_out, not_6_out, ins[27], ins[26]);
  Multiplexer #(.enable("false")) multiplexer_1 (.in0(1'b0), .in1(1'b1), .out(OutSelect_D), .sel(NPC_isJ_02));
  Multiplexer #(.width(5), .enable("false")) multiplexer_2 (
    .in0({5{1'b0}}), .in1(5'b11110), .out(multiplexer_2_out), .sel(NPC_isJ_02));
  or or_3 (or_3_out, isCal_i, isLoad);
  Multiplexer #(.enable("false")) multiplexer_3 (.in0(1'b0), .in1(1'b1), .out(OutSelect_E), .sel(or_4_out));
  or or_4 (or_4_out, isCal_i, isCal_r);
  Multiplexer #(.enable("false")) multiplexer_4 (.in0(1'b0), .in1(1'b1), .out(OutSelect_M), .sel(isLoad));
  or or_5 (isRead_A2, isCal_r, NPC_isBeq_03, DM_WE_01);
  or or_6 (isRead_A3, isCal_r, NPC_isBeq_03, DM_WE_01);
  Multiplexer #(.width(5), .enable("false")) multiplexer_5 (
    .in0(multiplexer_2_out), .in1(ins[20:16]), .out(multiplexer_5_out), .sel(or_3_out));
  Multiplexer #(.width(2), .enable("false")) multiplexer_6 (
    .in0(2'b11), .in1(2'b01), .out(multiplexer_6_out), .sel(or_7_out));
  or or_7 (or_7_out, isCal_r, isCal_i, isLoad, DM_WE_01);
  Multiplexer #(.width(2), .enable("false")) multiplexer_7 (
    .in0(2'b11), .in1(2'b10), .out(multiplexer_7_out), .sel(DM_WE_01));
  Multiplexer #(.width(2), .enable("false")) multiplexer_8 (
    .in0(2'b00), .in1(2'b01), .out(multiplexer_8_out), .sel(NPC_isJ_02));
  or or_8 (or_8_out, isCal_r, isCal_i);
  or or_9 (isRead_A1, isCal_r, NPC_isJr_01, isCal_i, NPC_isBeq_03, isLoad, DM_WE_01);
  Multiplexer #(.width(5), .enable("false")) multiplexer_9 (
    .in0(multiplexer_5_out), .in1(ins[15:11]), .out(multiplexer_9_out), .sel(isCal_r));
  Multiplexer #(.width(5), .enable("false")) multiplexer_10 (
    .in0(multiplexer_9_out), .out(A3_D), .sel(1'b0));  // open: in1
  Multiplexer #(.width(2), .enable("false")) multiplexer_11 (
    .in0(multiplexer_6_out), .in1(2'b00), .out(Tuse_A1_D), .sel(or_10_out));
  or or_10 (or_10_out, NPC_isJr_01, NPC_isBeq_03);
  Multiplexer #(.width(2), .enable("false")) multiplexer_12 (
    .in0(multiplexer_7_out), .in1(2'b01), .out(multiplexer_12_out), .sel(isCal_r));
  Multiplexer #(.width(2), .enable("false")) multiplexer_13 (
    .in0(multiplexer_12_out), .in1(2'b00), .out(Tuse_A2_D), .sel(NPC_isBeq_03));
  Multiplexer #(.width(2), .enable("false")) multiplexer_14 (.in0(2'b11), .in1(2'b00), .out(Tuse_A3_D), .sel(1'b0));
  Multiplexer #(.width(2), .enable("false")) multiplexer_15 (
    .in0(multiplexer_8_out), .in1(2'b10), .out(multiplexer_15_out), .sel(or_8_out));
  Multiplexer #(.width(2), .enable("false")) multiplexer_16 (
    .in0(multiplexer_15_out), .in1(2'b11), .out(Tnew_D), .sel(isLoad));
  or or_11 (ALU_B_01, isCal_i, isLoad, DM_WE_01);
  or or_12 (ALU_immExt_02, isLoad, DM_WE_01);
  or or_13 (or_13_out, addu, isLoad, DM_WE_01);
  ALUOp_5to3zip aluop_5to3zip_1 (
    .addu(or_13_out), .subu(subu), .andi(1'b0), .ori(ori), .lui(lui), .o2(ALU_Op_03[2]), .o1(ALU_Op_03[1]),
    .o0(ALU_Op_03[0]));

  // Other names for the same wires on the sheet: op[5:0] = ins[31:26]; func[5:0] = ins[5:0]; imm[15:0] = ins[15:0];
  //   ins_index[25:0] = ins[25:0]; shamt[4:0] = ins[10:6]; Rd[4:0] = ins[15:11]; Rt[4:0] = ins[20:16];
  //   Rs[4:0] = ins[25:21]; beq = NPC_isBeq_03; isBeq = NPC_isBeq_03; isJ = NPC_isJ_02; isLink = NPC_isJ_02;
  //   jal = NPC_isJ_02; isJReg = NPC_isJr_01; jr = NPC_isJr_01; lw = isLoad; isStore = DM_WE_01; sw = DM_WE_01

  // Notes on the sheet:
  //   R
  //   I
  //   J
  //   Decode
  //   Execute
  //   Memory
  //   WB
  //   无
  //   HazardAndForward
  //   读：Tuse_A1
  //   读：Tuse_A2
  //   读：Tuse_A3
  //   0为RD2,1为imm
  //   beq lui不用管
  //   选择流向下一级的数据，1为PC8，0为高阻
  //   直接输出写入地址，不能确定就高阻，不写入就0
  //   0为0扩展，1为Signed扩展
  //   ori 0扩展；lw sw符扩
  //   R: addu 000
  //   R: subu 001
  //   I: ori 011
  //   这里是在D的Tnew，所以即使是Link Tnew也是1，Load则是3
  //   选择流向下一级的数据，1为ALU_M，0为上一级数据
  //   选择流向下一级的数据，为1选DM_W，0上一级数据
  //   I: andi 010-实验中不涉及这条指令，但还是预留一个坑位，目前放置了常数0
  //   I: lui 100 lui对于imm，0扩成32位后传入输入A，之后的处理在ALU中完成
  //   R
endmodule

module DEMW_n_10 (
  input  [31:0] IR,
  input  [31:0] PC,
  input  [4:0] A3,
  input  [1:0] Tuse_A1,
  input  [1:0] Tuse_A2,
  input  [1:0] Tuse_A3,
  input  [1:0] Tnew,
  input  [31:0] RD1,
  input  [31:0] RD2,
  input  [31:0] Data,
  input  [31:0] ALU,
  input  clk,
  input  reset,
  input  en,
  output [31:0] IR_2,
  output [31:0] PC_2,
  output [4:0] A3_2,
  output [1:0] Tuse_A1_2,
  output [1:0] Tuse_A2_2,
  output [1:0] Tuse_A3_2,
  output [1:0] Tnew_2,
  output [31:0] RD1_2,
  output [31:0] RD2_2,
  output [31:0] Data_2,
  output [31:0] ALU_2
);

  wire comparator_1_eq, comparator_2_eq, comparator_3_eq, comparator_4_eq;
  wire [1:0] multiplexer_4_out, multiplexer_5_out, multiplexer_6_out, multiplexer_7_out, subtractor_2_out,
       subtractor_3_out, subtractor_4_out, Tnew_final, Tuse_A1_final, Tuse_A2_final, Tuse_A3_final,
       Tuse_Rstemp;
  wire [4:0] multiplexer_3_out;
  wire [31:0] multiplexer_1_out, multiplexer_2_out, multiplexer_8_out, multiplexer_9_out, multiplexer_10_out,
       multiplexer_11_out;

  Multiplexer #(.width(32), .enable("false")) multiplexer_1 (
    .in0(IR), .in1({32{1'b0}}), .out(multiplexer_1_out), .sel(reset));
  Multiplexer #(.width(32), .enable("false")) multiplexer_2 (
    .in0(PC), .in1({32{1'b0}}), .out(multiplexer_2_out), .sel(reset));
  Multiplexer #(.width(5), .enable("false")) multiplexer_3 (
    .in0(A3), .in1({5{1'b0}}), .out(multiplexer_3_out), .sel(reset));
  Multiplexer #(.width(2), .enable("false")) multiplexer_4 (
    .in0(Tuse_A1_final), .in1(2'b00), .out(multiplexer_4_out), .sel(reset));
  Multiplexer #(.width(2), .enable("false")) multiplexer_5 (
    .in0(Tuse_A2_final), .in1(2'b00), .out(multiplexer_5_out), .sel(reset));
  Multiplexer #(.width(2), .enable("false")) multiplexer_6 (
    .in0(Tuse_A3_final), .in1(2'b00), .out(multiplexer_6_out), .sel(reset));
  Multiplexer #(.width(2), .enable("false")) multiplexer_7 (
    .in0(Tnew_final), .in1(2'b00), .out(multiplexer_7_out), .sel(reset));
  Multiplexer #(.width(32), .enable("false")) multiplexer_8 (
    .in0(RD1), .in1({32{1'b0}}), .out(multiplexer_8_out), .sel(reset));
  Multiplexer #(.width(32), .enable("false")) multiplexer_9 (
    .in0(RD2), .in1({32{1'b0}}), .out(multiplexer_9_out), .sel(reset));
  Multiplexer #(.width(32), .enable("false")) multiplexer_10 (
    .in0(Data), .in1({32{1'b0}}), .out(multiplexer_10_out), .sel(reset));
  Multiplexer #(.width(32), .enable("false")) multiplexer_11 (
    .in0(ALU), .in1({32{1'b0}}), .out(multiplexer_11_out), .sel(reset));
  Register #(.width(32)) register_1 (.D(multiplexer_1_out), .en(en), .Q(IR_2), .clk(clk));  // open: clr
  Register #(.width(32)) register_2 (.D(multiplexer_2_out), .en(en), .Q(PC_2), .clk(clk));  // open: clr
  Register #(.width(5)) register_3 (.D(multiplexer_3_out), .en(en), .Q(A3_2), .clk(clk));  // open: clr
  Register #(.width(2)) register_4 (.D(multiplexer_4_out), .en(en), .Q(Tuse_A1_2), .clk(clk));  // open: clr
  Register #(.width(2)) register_5 (.D(multiplexer_5_out), .en(en), .Q(Tuse_A2_2), .clk(clk));  // open: clr
  Register #(.width(2)) register_6 (.D(multiplexer_6_out), .en(en), .Q(Tuse_A3_2), .clk(clk));  // open: clr
  Register #(.width(2)) register_7 (.D(multiplexer_7_out), .en(en), .Q(Tnew_2), .clk(clk));  // open: clr
  Register #(.width(32)) register_8 (.D(multiplexer_8_out), .en(en), .Q(RD1_2), .clk(clk));  // open: clr
  Register #(.width(32)) register_9 (.D(multiplexer_9_out), .en(en), .Q(RD2_2), .clk(clk));  // open: clr
  Register #(.width(32)) register_10 (.D(multiplexer_10_out), .en(en), .Q(Data_2), .clk(clk));  // open: clr
  Register #(.width(32)) register_11 (.D(multiplexer_11_out), .en(en), .Q(ALU_2), .clk(clk));  // open: clr
  Subtractor #(.width(2)) subtractor_1 (.a(Tuse_A1), .b(2'b01), .out(Tuse_Rstemp));  // open: bin, bout
  Subtractor #(.width(2)) subtractor_2 (.a(Tuse_A2), .b(2'b01), .out(subtractor_2_out));  // open: bin, bout
  Subtractor #(.width(2)) subtractor_3 (.a(Tuse_A3), .b(2'b01), .out(subtractor_3_out));  // open: bin, bout
  Subtractor #(.width(2)) subtractor_4 (.a(Tnew), .b(2'b01), .out(subtractor_4_out));  // open: bin, bout
  Comparator #(.width(2)) comparator_1 (.a(Tuse_Rstemp), .b(2'b11), .eq(comparator_1_eq));  // open: gt, lt
  Comparator #(.width(2)) comparator_2 (.a(subtractor_2_out), .b(2'b11), .eq(comparator_2_eq));  // open: gt, lt
  Comparator #(.width(2)) comparator_3 (.a(subtractor_3_out), .b(2'b11), .eq(comparator_3_eq));  // open: gt, lt
  Comparator #(.width(2)) comparator_4 (.a(subtractor_4_out), .b(2'b11), .eq(comparator_4_eq));  // open: gt, lt
  Multiplexer #(.width(2), .enable("false")) multiplexer_12 (
    .in0(Tuse_Rstemp), .in1(2'b00), .out(Tuse_A1_final), .sel(comparator_1_eq));
  Multiplexer #(.width(2), .enable("false")) multiplexer_13 (
    .in0(subtractor_2_out), .in1(2'b00), .out(Tuse_A2_final), .sel(comparator_2_eq));
  Multiplexer #(.width(2), .enable("false")) multiplexer_14 (
    .in0(subtractor_3_out), .in1(2'b00), .out(Tuse_A3_final), .sel(comparator_3_eq));
  Multiplexer #(.width(2), .enable("false")) multiplexer_15 (
    .in0(subtractor_4_out), .in1(2'b00), .out(Tnew_final), .sel(comparator_4_eq));
endmodule

module Hazard_n_11 (
  input  isRead_A1_D,
  input  [1:0] Tuse_A1_D,
  input  [4:0] A1_D,
  input  isRead_A2_D,
  input  [1:0] Tuse_A2_D,
  input  [4:0] A2_D,
  input  isRead_A3_D,
  input  [1:0] Tuse_A3_D,
  input  [4:0] A3_D,
  input  [4:0] A3_E,
  input  [1:0] Tnew_E,
  input  [4:0] A3_M,
  input  [1:0] Tnew_M,
  output stallPC,
  output stallID,
  output flushEX
);

  wire and_1_out, and_2_out, and_3_out, and_4_out, and_5_out, and_6_out, comparator_1_eq, comparator_2_eq,
       comparator_3_lt, comparator_4_eq, comparator_5_eq, comparator_6_lt, comparator_7_eq, comparator_8_eq,
       comparator_9_lt, comparator_10_eq, comparator_11_eq, comparator_12_lt, comparator_13_eq,
       comparator_14_eq, comparator_15_lt, comparator_16_eq, comparator_17_eq, comparator_18_lt, not_1_out,
       not_2_out, not_3_out, not_4_out, not_5_out, not_6_out;

  Comparator #(.width(5), .mode("unsigned")) comparator_1 (.a(A1_D), .b(A3_E), .eq(comparator_1_eq));  // open: gt, lt
  not not_1 (not_1_out, comparator_2_eq);
  Comparator #(.width(5), .mode("unsigned")) comparator_2 (
    .a(A3_E), .b({5{1'b0}}), .eq(comparator_2_eq));  // open: gt, lt
  Comparator #(.width(2), .mode("unsigned")) comparator_3 (
    .a(Tuse_A1_D), .b(Tnew_E), .lt(comparator_3_lt));  // open: gt, eq
  Comparator #(.width(5), .mode("unsigned")) comparator_4 (.a(A2_D), .b(A3_E), .eq(comparator_4_eq));  // open: gt, lt
  Comparator #(.width(5), .mode("unsigned")) comparator_5 (
    .a(A3_E), .b({5{1'b0}}), .eq(comparator_5_eq));  // open: gt, lt
  not not_2 (not_2_out, comparator_5_eq);
  Comparator #(.width(2), .mode("unsigned")) comparator_6 (
    .a(Tuse_A2_D), .b(Tnew_E), .lt(comparator_6_lt));  // open: gt, eq
  Comparator #(.width(5), .mode("unsigned")) comparator_7 (.a(A3_D), .b(A3_E), .eq(comparator_7_eq));  // open: gt, lt
  Comparator #(.width(5), .mode("unsigned")) comparator_8 (
    .a(A3_E), .b({5{1'b0}}), .eq(comparator_8_eq));  // open: gt, lt
  not not_3 (not_3_out, comparator_8_eq);
  Comparator #(.width(2), .mode("unsigned")) comparator_9 (
    .a(Tuse_A3_D), .b(Tnew_E), .lt(comparator_9_lt));  // open: gt, eq
  Comparator #(.width(5), .mode("unsigned")) comparator_10 (.a(A1_D), .b(A3_M), .eq(comparator_10_eq));  // open: gt, lt
  Comparator #(.width(5), .mode("unsigned")) comparator_11 (
    .a(A3_M), .b({5{1'b0}}), .eq(comparator_11_eq));  // open: gt, lt
  not not_4 (not_4_out, comparator_11_eq);
  Comparator #(.width(2), .mode("unsigned")) comparator_12 (
    .a(Tuse_A1_D), .b(Tnew_M), .lt(comparator_12_lt));  // open: gt, eq
  Comparator #(.width(5), .mode("unsigned")) comparator_13 (.a(A2_D), .b(A3_M), .eq(comparator_13_eq));  // open: gt, lt
  not not_5 (not_5_out, comparator_14_eq);
  Comparator #(.width(5), .mode("unsigned")) comparator_14 (
    .a(A3_M), .b({5{1'b0}}), .eq(comparator_14_eq));  // open: gt, lt
  Comparator #(.width(2), .mode("unsigned")) comparator_15 (
    .a(Tuse_A2_D), .b(Tnew_M), .lt(comparator_15_lt));  // open: gt, eq
  Comparator #(.width(5), .mode("unsigned")) comparator_16 (.a(A3_D), .b(A3_M), .eq(comparator_16_eq));  // open: gt, lt
  Comparator #(.width(5), .mode("unsigned")) comparator_17 (
    .a(A3_M), .b({5{1'b0}}), .eq(comparator_17_eq));  // open: gt, lt
  not not_6 (not_6_out, comparator_17_eq);
  Comparator #(.width(2), .mode("unsigned")) comparator_18 (
    .a(Tuse_A3_D), .b(Tnew_M), .lt(comparator_18_lt));  // open: gt, eq
  and and_1 (and_1_out, isRead_A1_D, comparator_1_eq, not_1_out, comparator_3_lt);
  and and_2 (and_2_out, isRead_A2_D, comparator_4_eq, not_2_out, comparator_6_lt);
  and and_3 (and_3_out, isRead_A3_D, comparator_7_eq, not_3_out, comparator_9_lt);
  and and_4 (and_4_out, isRead_A1_D, comparator_10_eq, not_4_out, comparator_12_lt);
  and and_5 (and_5_out, isRead_A2_D, comparator_13_eq, not_5_out, comparator_15_lt);
  and and_6 (and_6_out, isRead_A3_D, comparator_16_eq, not_6_out, comparator_18_lt);
  or or_1 (flushEX, and_1_out, and_2_out, and_3_out, and_4_out, and_5_out, and_6_out);

  assign stallID = flushEX;
  assign stallPC = flushEX;

  // Notes on the sheet:
  //   D读E写 A1
  //   D读E写 A2
  //   D读E写 A3
  //   D读M写 A1
  //   D读M写 A2
  //   D读M写 A3
endmodule

module ForwardUnit_n_12 (
  input  [4:0] ReadDes,
  input  isRead,
  input  [4:0] A3,
  output NeedForward
);

  wire comparator_1_eq, comparator_2_eq, not_1_out;

  Comparator #(.width(5), .mode("unsigned")) comparator_1 (.a(ReadDes), .b(A3), .eq(comparator_1_eq));  // open: gt, lt
  Comparator #(.width(5), .mode("unsigned")) comparator_2 (
    .a(A3), .b({5{1'b0}}), .eq(comparator_2_eq));  // open: gt, lt
  not not_1 (not_1_out, comparator_2_eq);
  and and_1 (NeedForward, isRead, comparator_1_eq, not_1_out);
endmodule

module Forward_13 (
  input  [4:0] D_A1,
  input  [4:0] D_A2,
  input  D_Use_1,
  input  D_Use_2,
  input  [31:0] D_RD1,
  input  [31:0] D_RD2,
  input  [4:0] D_A3,
  input  [4:0] E_A1,
  input  [4:0] E_A2,
  input  E_Use_1,
  input  E_Use_2,
  input  [31:0] E_RD1,
  input  [31:0] E_RD2,
  input  [4:0] E_A3,
  input  [4:0] M_A1,
  input  [4:0] M_A2,
  input  M_Use_1,
  input  M_Use_2,
  input  [31:0] M_RD1,
  input  [31:0] M_RD2,
  input  [4:0] M_A3,
  input  [4:0] W_A3,
  input  [31:0] Data_E,
  input  [31:0] Data_M,
  input  [31:0] Data_W,
  output [31:0] RD1_D_final,
  output [31:0] RD2_D_final,
  output [31:0] RD1_E_final,
  output [31:0] RD2_E_final,
  output [31:0] RD1_M_final,
  output [31:0] RD2_M_final
);

  wire _1, _2, _3, _4, _5, _6, _7, _8, _9, _10;
  wire [31:0] multiplexer_1_out, multiplexer_2_out, multiplexer_3_out, multiplexer_4_out;

  ForwardUnit_n_12 forwardunit_n_12_1 (.isRead(D_Use_1), .ReadDes(D_A1), .A3(E_A3), .NeedForward(_1));
  ForwardUnit_n_12 forwardunit_n_12_2 (.isRead(D_Use_2), .ReadDes(D_A2), .A3(E_A3), .NeedForward(_3));
  ForwardUnit_n_12 forwardunit_n_12_3 (.isRead(E_Use_1), .ReadDes(E_A1), .A3(M_A3), .NeedForward(_5));
  ForwardUnit_n_12 forwardunit_n_12_4 (.isRead(E_Use_2), .ReadDes(E_A2), .A3(M_A3), .NeedForward(_7));
  ForwardUnit_n_12 forwardunit_n_12_5 (.isRead(M_Use_1), .ReadDes(M_A1), .A3(W_A3), .NeedForward(_9));
  ForwardUnit_n_12 forwardunit_n_12_6 (.isRead(M_Use_2), .ReadDes(M_A2), .A3(W_A3), .NeedForward(_10));
  ForwardUnit_n_12 forwardunit_n_12_7 (.isRead(D_Use_1), .ReadDes(D_A1), .A3(M_A3), .NeedForward(_2));
  ForwardUnit_n_12 forwardunit_n_12_8 (.isRead(D_Use_2), .ReadDes(D_A2), .A3(M_A3), .NeedForward(_4));
  ForwardUnit_n_12 forwardunit_n_12_9 (.isRead(E_Use_1), .ReadDes(E_A1), .A3(W_A3), .NeedForward(_6));
  ForwardUnit_n_12 forwardunit_n_12_10 (.isRead(E_Use_2), .ReadDes(E_A2), .A3(W_A3), .NeedForward(_8));
  Multiplexer #(.width(32), .enable("false")) multiplexer_1 (
    .in0(D_RD1), .in1(Data_M), .out(multiplexer_1_out), .sel(_2));
  Multiplexer #(.width(32), .enable("false")) multiplexer_2 (
    .in0(D_RD2), .in1(Data_M), .out(multiplexer_2_out), .sel(_4));
  Multiplexer #(.width(32), .enable("false")) multiplexer_3 (
    .in0(E_RD1), .in1(Data_W), .out(multiplexer_3_out), .sel(_6));
  Multiplexer #(.width(32), .enable("false")) multiplexer_4 (
    .in0(E_RD2), .in1(Data_W), .out(multiplexer_4_out), .sel(_8));
  Multiplexer #(.width(32), .enable("false")) multiplexer_5 (
    .in0(multiplexer_1_out), .in1(Data_E), .out(RD1_D_final), .sel(_1));
  Multiplexer #(.width(32), .enable("false")) multiplexer_6 (
    .in0(multiplexer_2_out), .in1(Data_E), .out(RD2_D_final), .sel(_3));
  Multiplexer #(.width(32), .enable("false")) multiplexer_7 (
    .in0(multiplexer_3_out), .in1(Data_M), .out(RD1_E_final), .sel(_5));
  Multiplexer #(.width(32), .enable("false")) multiplexer_8 (
    .in0(multiplexer_4_out), .in1(Data_M), .out(RD2_E_final), .sel(_7));
  Multiplexer #(.width(32), .enable("false")) multiplexer_9 (.in0(M_RD1), .in1(Data_W), .out(RD1_M_final), .sel(_9));
  Multiplexer #(.width(32), .enable("false")) multiplexer_10 (.in0(M_RD2), .in1(Data_W), .out(RD2_M_final), .sel(_10));

  // Notes on the sheet:
  //   D
  //   E
  //   M
  //   W
  //   相邻转发
  //   相邻转发
  //   相邻转发
  //   间隔转发
  //   间隔转发
endmodule

module Forward_n_13 (
  input  [4:0] D_A1,
  input  [4:0] D_A2,
  input  [4:0] D_A2_2,
  input  D_Use_1,
  input  D_Use_2,
  input  D_Use_2_2,
  input  [31:0] D_RD1,
  input  [31:0] D_RD2,
  input  [4:0] D_A3,
  input  [31:0] Data_E,
  input  [31:0] Data_M,
  input  [31:0] Data_W,
  output [31:0] RD1_D_final,
  output [31:0] RD2_D_final
);

  wire _1, _2, _3, _4;
  wire [4:0] E_A3, M_A3;
  wire [31:0] multiplexer_1_out, multiplexer_2_out;

  ForwardUnit_n_12 forwardunit_n_12_1 (.isRead(D_Use_1), .ReadDes(D_A1), .A3(E_A3), .NeedForward(_1));
  ForwardUnit_n_12 forwardunit_n_12_2 (.isRead(D_Use_2), .ReadDes(D_A2), .A3(E_A3), .NeedForward(_3));
  ForwardUnit_n_12 forwardunit_n_12_3 (.isRead(D_Use_1), .ReadDes(D_A1), .A3(M_A3), .NeedForward(_2));
  ForwardUnit_n_12 forwardunit_n_12_4 (.isRead(D_Use_2), .ReadDes(D_A2), .A3(M_A3), .NeedForward(_4));
  Multiplexer #(.width(32), .enable("false")) multiplexer_1 (
    .in0(D_RD1), .in1(Data_M), .out(multiplexer_1_out), .sel(_2));
  Multiplexer #(.width(32), .enable("false")) multiplexer_2 (
    .in0(D_RD2), .in1(Data_M), .out(multiplexer_2_out), .sel(_4));
  Multiplexer #(.width(32), .enable("false")) multiplexer_3 (
    .in0(multiplexer_1_out), .in1(Data_E), .out(RD1_D_final), .sel(_1));
  Multiplexer #(.width(32), .enable("false")) multiplexer_4 (
    .in0(multiplexer_2_out), .in1(Data_E), .out(RD2_D_final), .sel(_3));

  assign D_A2_2 = D_A2;
  assign D_Use_2_2 = D_Use_2;

  // Notes on the sheet:
  //   D
  //   相邻转发
  //   间隔转发
endmodule
