// Logisim project 二进制编码to格雷码.circ as structural Verilog: 1 circuit, main circuit main
module main (
  input  A2,
  input  A1,
  input  A0,
  output C2,
  output C1,
  output C0
);

  xor xor_1 (C1, A2, A1);
  xor xor_2 (C0, A1, A0);

  assign C2 = A2;
endmodule
