// Logisim project 五人投票表决器.circ as structural Verilog: 1 circuit, main circuit main
module main (
  input  A,
  input  B,
  input  C,
  input  D,
  input  E,
  output F
);

  wire and_1_out, and_2_out, and_3_out, and_4_out, and_5_out, and_6_out, and_7_out, and_8_out, and_9_out,
       and_10_out, not_1_out, not_2_out, not_3_out;

  not not_1 (not_1_out, A);
  not not_2 (not_2_out, B);
  not not_3 (not_3_out, D);
  and and_1 (and_1_out, A, B, E);
  and and_2 (and_2_out, A, C, E);
  and and_3 (and_3_out, A, B, D);
  and and_4 (and_4_out, A, C, D);
  and and_5 (and_5_out, not_1_out, C, D, E);
  and and_6 (and_6_out, not_1_out, B, D, E);
  and and_7 (and_7_out, not_1_out, B, C, E);
  and and_8 (and_8_out, not_1_out, B, C, D);
  and and_9 (and_9_out, A, B, C, not_3_out);
  and and_10 (and_10_out, A, not_2_out, D, E);
  or or_1 (F, and_1_out, and_2_out, and_3_out, and_4_out, and_5_out, and_6_out, and_7_out, and_8_out, and_9_out, and_10_out);
endmodule
